// Logisim project TTL_Version.circ as structural Verilog: 19 circuits, main circuit main
module main (
  input  in_1,
  output [7:0] out_2
);

  wire clkdelay_1_out_2, clkdelay_2_out_2, clock_1_out, cpu_1_iodread, cpu_1_iodsend, cpu_1_ramread,
       cpu_1_ramwrite, or_1_out, por_1_out;
  wire [7:0] cpu_1_addrext_2, ram_1_dout;
  wire [23:8] cpu_1_addrext;

  ClkDelay clkdelay_1 (.in_1(clkdelay_2_out_2), .out_2(clkdelay_1_out_2));
  ClkDelay clkdelay_2 (.in_1(clock_1_out), .out_2(clkdelay_2_out_2));
  Clock clock_1 (.out(clock_1_out));
  RAM #(.addrWidth(24), .enables("line")) ram_1 (
    .addr({cpu_1_addrext, cpu_1_addrext_2}), .we(cpu_1_ramwrite), .clk(clkdelay_1_out_2), .din(out_2),
    .dout(ram_1_dout));
  or or_1 (or_1_out, in_1, por_1_out);
  POR por_1 (.out(por_1_out));
  CPU cpu_1 (
    .AddrExtIn({cpu_1_addrext, cpu_1_addrext_2}), .DataEtxIn(out_2), .Clock(clock_1_out), .Reset(or_1_out),
    .AddrExt({cpu_1_addrext, cpu_1_addrext_2}), .DataExtOut(out_2), .RamRead(cpu_1_ramread),
    .RamWrite(cpu_1_ramwrite), .IODSend(cpu_1_iodsend), .IODRead(cpu_1_iodread));
  assign out_2 = cpu_1_ramread ? ram_1_dout : 8'bz;  // Controlled_Buffer controlled_buffer_1
  IOD iod_1 (
    .IODSend(cpu_1_iodsend), .IODRead(cpu_1_iodread), .AddrBusIn(cpu_1_addrext_2), .DataBusIn(out_2),
    .Clock(clock_1_out), .AddrBusOut(cpu_1_addrext_2), .DataBusOut(out_2));
endmodule

module FullAdder1b (
  input  A,
  input  B,
  input  Cin,
  output S,
  output Cout
);

  wire and_1_out, and_2_out, xor_1_out;

  and and_1 (and_1_out, B, A);
  xor xor_1 (xor_1_out, A, B);
  xor xor_2 (S, xor_1_out, Cin);
  and and_2 (and_2_out, xor_1_out, Cin);
  or or_1 (Cout, and_1_out, and_2_out);
endmodule

module AddSub8b (
  input  [7:0] A,
  input  [7:0] B,
  input  Sub,
  input  Cin,
  input  IncDec,
  output [7:0] S,
  output Cout
);

  wire fulladder1b_1_cout, fulladder1b_2_cout, fulladder1b_3_cout, fulladder1b_4_cout, fulladder1b_5_cout,
       fulladder1b_6_cout, fulladder1b_7_cout, fulladder1b_8_cout, xor_1_out, xor_2_out, xor_3_out,
       xor_4_out, xor_5_out, xor_6_out, xor_7_out, xor_8_out, xor_9_out;
  wire [7:0] multiplexer_1_out;

  Multiplexer #(.width(8)) multiplexer_1 (.in0(B), .in1(8'h1), .out(multiplexer_1_out), .sel(IncDec));
  xor xor_1 (xor_1_out, multiplexer_1_out[0], Sub);
  xor xor_2 (xor_2_out, Sub, Cin);
  xor xor_3 (xor_3_out, multiplexer_1_out[4], Sub);
  xor xor_4 (xor_4_out, multiplexer_1_out[1], Sub);
  FullAdder1b fulladder1b_1 (.A(A[0]), .B(xor_1_out), .Cin(xor_2_out), .S(S[0]), .Cout(fulladder1b_1_cout));
  xor xor_5 (xor_5_out, multiplexer_1_out[5], Sub);
  FullAdder1b fulladder1b_2 (.A(A[4]), .B(xor_3_out), .Cin(fulladder1b_7_cout), .S(S[4]), .Cout(fulladder1b_2_cout));
  FullAdder1b fulladder1b_3 (.A(A[1]), .B(xor_4_out), .Cin(fulladder1b_1_cout), .S(S[1]), .Cout(fulladder1b_3_cout));
  FullAdder1b fulladder1b_4 (.A(A[5]), .B(xor_5_out), .Cin(fulladder1b_2_cout), .S(S[5]), .Cout(fulladder1b_4_cout));
  xor xor_6 (xor_6_out, multiplexer_1_out[2], Sub);
  xor xor_7 (xor_7_out, multiplexer_1_out[6], Sub);
  FullAdder1b fulladder1b_5 (.A(A[2]), .B(xor_6_out), .Cin(fulladder1b_3_cout), .S(S[2]), .Cout(fulladder1b_5_cout));
  xor xor_8 (xor_8_out, multiplexer_1_out[7], Sub);
  FullAdder1b fulladder1b_6 (.A(A[6]), .B(xor_7_out), .Cin(fulladder1b_4_cout), .S(S[6]), .Cout(fulladder1b_6_cout));
  xor xor_9 (xor_9_out, multiplexer_1_out[3], Sub);
  FullAdder1b fulladder1b_7 (.A(A[3]), .B(xor_9_out), .Cin(fulladder1b_5_cout), .S(S[3]), .Cout(fulladder1b_7_cout));
  FullAdder1b fulladder1b_8 (.A(A[7]), .B(xor_8_out), .Cin(fulladder1b_6_cout), .S(S[7]), .Cout(fulladder1b_8_cout));
  xor xor_10 (Cout, fulladder1b_8_cout, Sub);
endmodule

module EqualsZ (
  input  [7:0] A,
  output out_2
);

  and and_1 (out_2, ~A[0], ~A[1], ~A[2], ~A[3], ~A[4], ~A[5], ~A[6], ~A[7]);  // AND_Gate
endmodule

module ALU (
  input  [7:0] A,
  input  [7:0] B,
  input  [3:0] opcode,
  output [7:0] S,
  output Ef,
  output Sf,
  output Ff,
  output Nf,
  output Zf,
  output Cf
);

  wire addsub8b_1_cout, and_1_out, and_2_out, and_3_out, and_4_out, and_5_out, comparator_1_eq,
       comparator_1_gt, comparator_1_lt, equalsz_1_out_2, not_1_out, or_1_out, or_2_out;
  wire [7:0] addsub8b_1_s, and8b_out, not8b_out, or8b_out, shifter_1_out, shifter_2_out, shifter_3_out,
       xor8b_out;

  and and_1 (and_1_out, ~opcode[3], ~opcode[2], ~opcode[1], opcode[0]);  // AND_Gate
  or or_1 (or_1_out, and_2_out, and_5_out);
  and and_2 (and_2_out, ~opcode[3], ~opcode[2], opcode[1], opcode[0]);  // AND_Gate
  assign and8b_out = A & B;  // AND_Gate and8b, 8 bits wide
  assign or8b_out = A | B;  // OR_Gate or8b, 8 bits wide
  assign not8b_out = ~A;  // NOT_Gate not8b, 8 bits wide
  Comparator comparator_1 (.a(A), .b(B), .gt(comparator_1_gt), .eq(comparator_1_eq), .lt(comparator_1_lt));
  Shifter shifter_1 (.in(A), .\dist (3'b001), .out(shifter_1_out));
  Shifter #(.shift("ar")) shifter_2 (.in(A), .\dist (3'b001), .out(shifter_2_out));
  Shifter #(.shift("lr")) shifter_3 (.in(A), .\dist (3'b001), .out(shifter_3_out));
  and and_3 (and_3_out, opcode[3], ~opcode[2], opcode[1], opcode[0]);  // AND_Gate
  and and_4 (and_4_out, opcode[3], opcode[2], ~opcode[1], ~opcode[0]);  // AND_Gate
  or or_2 (or_2_out, and_4_out, and_5_out);
  assign xor8b_out = A ^ B;  // XOR_Gate xor8b, 8 bits wide
  and and_5 (and_5_out, opcode[3], opcode[2], ~opcode[1], opcode[0]);  // AND_Gate
  AddSub8b addsub8b_1 (
    .A(A), .B(B), .Sub(or_1_out), .Cin(and_1_out), .IncDec(or_2_out), .S(addsub8b_1_s), .Cout(addsub8b_1_cout));
  BitSelector #(.width(1)) bitselector_1 (.in(comparator_1_eq), .out(Ef), .sel(not_1_out));
  BitSelector #(.width(1)) bitselector_2 (.in(comparator_1_gt), .out(Sf), .sel(not_1_out));
  not not_1 (not_1_out, and_3_out);
  BitSelector #(.width(1)) bitselector_3 (.in(comparator_1_lt), .out(Ff), .sel(not_1_out));
  BitSelector #(.width(1)) bitselector_4 (.in(addsub8b_1_cout), .out(Cf), .sel(and_3_out));
  BitSelector #(.width(1)) bitselector_5 (.in(equalsz_1_out_2), .out(Zf), .sel(and_3_out));
  EqualsZ equalsz_1 (.A({Nf, S[6:0]}), .out_2(equalsz_1_out_2));
  Multiplexer #(.select(4), .width(8)) multiplexer_1 (
    .in0({8{1'b0}}), .in1(addsub8b_1_s), .in2(addsub8b_1_s), .in3(addsub8b_1_s), .in4(addsub8b_1_s),
    .in5(addsub8b_1_s), .in6(and8b_out), .in7(or8b_out), .in8(xor8b_out), .in9(not8b_out),
    .in10(shifter_1_out), .in11(shifter_2_out), .in12(shifter_3_out), .in13({8{1'b0}}), .in14({8{1'b0}}),
    .in15({8{1'b0}}), .out({Nf, S[6:0]}), .sel(opcode));

  assign S[7] = Nf;

  // Notes on the sheet:
  //   CMP
  //   SHL
  //   ASR
  //   SHR
  //   Flags
endmodule

module Registers (
  input  [2:0] RgSel,
  input  Rst,
  input  Clock,
  input  RW,
  input  En,
  input  [7:0] DataIn,
  output [7:0] out_7,
  output [7:0] out_8,
  output [7:0] DataOut
);

  wire clkdelay_1_out_2, EnN, ReadCmd, selA, selAn, selB, selBn, selC, selCn, selD, selDn, selI, selIn, selJ,
       selJn, selX, selXn, selY, selYn, twocycdel_1_enout, WriteA, WriteB, WriteC, WriteD, WriteI, WriteJ,
       WriteX, WriteY;
  wire [7:0] Bout, Cout, Dout, Iout, Jout, register_1_q, Xout, Yout;

  Register A (.D(DataIn), .en(WriteA), .clk(Clock), .Q(out_7), .clr(Rst));
  Register I (.D(DataIn), .en(WriteI), .clk(Clock), .Q(Iout), .clr(Rst));
  Register B (.D(DataIn), .en(WriteB), .clk(Clock), .Q(Bout), .clr(Rst));
  Register J (.D(DataIn), .en(WriteJ), .clk(Clock), .Q(Jout), .clr(Rst));
  Register C (.D(DataIn), .en(WriteC), .clk(Clock), .Q(Cout), .clr(Rst));
  Register X (.D(DataIn), .en(WriteX), .clk(Clock), .Q(Xout), .clr(Rst));
  Register D (.D(DataIn), .en(WriteD), .clk(Clock), .Q(Dout), .clr(Rst));
  Register Y (.D(DataIn), .en(WriteY), .clk(Clock), .Q(Yout), .clr(Rst));
  and and_1 (ReadCmd, ~RW, En);  // AND_Gate
  _7408 u_7408_1 (
    .pin1(selA), .pin2(RW), .pin3(WriteA), .pin4(selB), .pin5(RW), .pin6(WriteB), .pin13(selC), .pin12(RW),
    .pin11(WriteC), .pin10(selD), .pin9(RW), .pin8(WriteD));
  Multiplexer #(.enable("true"), .select(3), .width(8)) multiplexer_1 (
    .in0(out_7), .in1(Bout), .in2(Cout), .in3(Dout), .in4(Iout), .in5(Jout), .in6(Xout), .in7(Yout),
    .out(out_8), .sel(RgSel), .en(ReadCmd));
  ClkDelay clkdelay_1 (.in_1(Clock), .out_2(clkdelay_1_out_2));
  _7408 u_7408_2 (
    .pin1(selI), .pin2(RW), .pin3(WriteI), .pin4(selJ), .pin5(RW), .pin6(WriteJ), .pin13(selX), .pin12(RW),
    .pin11(WriteX), .pin10(selY), .pin9(RW), .pin8(WriteY));
  Register register_1 (.D(out_8), .en(ReadCmd), .clk(clkdelay_1_out_2), .Q(register_1_q), .clr(1'b0));
  TwoCycDel twocycdel_1 (.EnIn(ReadCmd), .Clock(Clock), .EnOut(twocycdel_1_enout));
  assign DataOut = twocycdel_1_enout ? register_1_q : 8'bz;  // Controlled_Buffer controlled_buffer_1
  _74138 u_74138_1 (
    .pin1(RgSel[0]), .pin2(RgSel[1]), .pin3(RgSel[2]), .pin4(EnN), .pin5(EnN), .pin6(En), .pin7(selYn),
    .pin15(selAn), .pin14(selBn), .pin13(selCn), .pin12(selDn), .pin11(selIn), .pin10(selJn), .pin9(selXn));
  _7404 u_7404_1 (
    .pin1(selAn), .pin2(selA), .pin3(selBn), .pin4(selB), .pin5(selCn), .pin6(selC), .pin13(selDn),
    .pin12(selD), .pin11(selIn), .pin10(selI), .pin9(selJn), .pin8(selJ));
  _7404 u_7404_2 (
    .pin1(selXn), .pin2(selX), .pin3(selYn), .pin4(selY), .pin5(En), .pin6(EnN));  // open: pin13, pin12, pin11, pin10, pin9, pin8

  // Other names for the same wires on the sheet: Aout[7:0] = out_7
endmodule

module CPU (
  input  [23:0] AddrExtIn,
  input  [7:0] DataEtxIn,
  input  Clock,
  input  Reset,
  output [23:0] AddrExt,
  output [7:0] DataExtOut,
  output RamRead,
  output RamWrite,
  output IODSend,
  output IODRead
);

  wire clkdelay_1_out_2, clkdelay_2_out_2, controlunit_1_aluaccuastr, controlunit_1_aluaccubstr,
       controlunit_1_aluaccuread, controlunit_1_aluen, controlunit_1_regen, controlunit_1_regrw;
  wire [2:0] controlunit_1_regsel;
  wire [3:0] controlunit_1_aluopcode;
  wire [5:0] alu_1_cf;
  wire [7:0] AccuA_q, AccuALU_q, AccuB_q, alu_1_s, controlunit_1_databusout;

  ClkDelay clkdelay_1 (.in_1(Clock), .out_2(clkdelay_1_out_2));
  ClkDelay clkdelay_2 (.in_1(clkdelay_1_out_2), .out_2(clkdelay_2_out_2));
  Register AccuA (
    .D(controlunit_1_databusout), .en(controlunit_1_aluaccuastr), .clk(clkdelay_2_out_2), .Q(AccuA_q));  // open: clr
  Register AccuB (
    .D(controlunit_1_databusout), .en(controlunit_1_aluaccubstr), .clk(clkdelay_2_out_2), .Q(AccuB_q));  // open: clr
  ControlUnit controlunit_1 (
    .AddrExtIn(AddrExtIn), .DataExtIn(DataEtxIn), .DataBusIn(controlunit_1_databusout), .ClockExt(Clock),
    .Reset(Reset), .AluFlgIn(alu_1_cf), .DataBusOut(controlunit_1_databusout), .AddrExt(AddrExt),
    .DataExtOut(DataExtOut), .RamRead(RamRead), .RamWrite(RamWrite), .AluAccuAStr(controlunit_1_aluaccuastr),
    .AluAccuBStr(controlunit_1_aluaccubstr), .AluAccuRead(controlunit_1_aluaccuread),
    .AluOpCode(controlunit_1_aluopcode), .AluEn(controlunit_1_aluen), .RegSel(controlunit_1_regsel),
    .RegRW(controlunit_1_regrw), .RegEn(controlunit_1_regen), .IODSend(IODSend), .IODRead(IODRead));
  Register #(.trigger("high")) AccuALU (
    .D(alu_1_s), .en(controlunit_1_aluen), .clk(clkdelay_2_out_2), .Q(AccuALU_q));  // open: clr
  ALU alu_1 (
    .A(AccuA_q), .B(AccuB_q), .opcode(controlunit_1_aluopcode), .S(alu_1_s), .Ef(alu_1_cf[5]),
    .Sf(alu_1_cf[4]), .Ff(alu_1_cf[3]), .Nf(alu_1_cf[2]), .Zf(alu_1_cf[1]), .Cf(alu_1_cf[0]));
  assign controlunit_1_databusout = controlunit_1_aluaccuread ? AccuALU_q : 8'bz;  // Controlled_Buffer controlled_buffer_1
  // Registers registers_1: pin names not known; wires that end beside it: Reset, clkdelay_2_out_2, controlunit_1_regrw, controlunit_1_regsel, controlunit_1_regen, controlunit_1_databusout, controlunit_1_databusout
endmodule

module FlagRegister (
  input  StrCuFlg,
  input  StrAluFlg,
  input  [5:0] AluFlgIn,
  input  [1:0] CUFlgIn,
  input  Clock,
  input  Reset,
  input  [7:0] Set,
  input  [7:0] Clear,
  output [7:0] Flags
);

  wire clkdelay_1_out_2, clkdelay_2_out_2, clkdelay_3_out_2, clkdelay_4_out_2, clkdelay_5_out_2,
       clkdelay_6_out_2, clkdelay_7_out_2, clkdelay_8_out_2, or_1_out, or_2_out, or_3_out, or_4_out,
       or_5_out, or_6_out, or_7_out, or_8_out, or_9_out, or_10_out, or_11_out, or_12_out, or_13_out,
       or_14_out, or_15_out, or_16_out, or_17_out, or_18_out, or_19_out, or_20_out, or_21_out, or_22_out,
       or_23_out, or_24_out;

  ClkDelay clkdelay_1 (.in_1(Clock), .out_2(clkdelay_1_out_2));
  Register #(.trigger("high"), .width(1)) Carry (
    .D(or_1_out), .en(or_2_out), .clk(clkdelay_2_out_2), .Q(Flags[0]), .clr(or_3_out));
  or or_1 (or_1_out, AluFlgIn[0], Set[1]);
  or or_2 (or_2_out, StrAluFlg, Set[1]);
  ClkDelay clkdelay_2 (.in_1(clkdelay_1_out_2), .out_2(clkdelay_2_out_2));
  or or_3 (or_3_out, Clear[0], Reset);
  or or_4 (or_4_out, AluFlgIn[5], Set[2]);
  or or_5 (or_5_out, StrAluFlg, Set[2]);
  ClkDelay clkdelay_3 (.in_1(clkdelay_1_out_2), .out_2(clkdelay_3_out_2));
  Register #(.trigger("high"), .width(1)) Equal (
    .D(or_4_out), .en(or_5_out), .clk(clkdelay_3_out_2), .Q(Flags[1]), .clr(or_6_out));
  or or_6 (or_6_out, Clear[1], Reset);
  or or_7 (or_7_out, StrCuFlg, Reset, Set[3]);
  Register #(.trigger("high"), .width(1)) Interrupt (
    .D(or_8_out), .en(or_7_out), .clk(or_9_out), .Q(Flags[2]), .clr(Clear[2]));
  or or_8 (or_8_out, CUFlgIn[1], Reset, Set[3]);
  or or_9 (or_9_out, clkdelay_1_out_2, Reset);
  Register #(.trigger("high"), .width(1)) Negative (
    .D(or_10_out), .en(or_11_out), .clk(clkdelay_4_out_2), .Q(Flags[3]), .clr(or_12_out));
  or or_10 (or_10_out, AluFlgIn[2], Set[4]);
  or or_11 (or_11_out, StrAluFlg, Set[4]);
  or or_12 (or_12_out, Clear[3], Reset);
  ClkDelay clkdelay_4 (.in_1(clkdelay_1_out_2), .out_2(clkdelay_4_out_2));
  Register #(.trigger("high"), .width(1)) Superior (
    .D(or_13_out), .en(or_14_out), .clk(clkdelay_5_out_2), .Q(Flags[4]), .clr(or_15_out));
  or or_13 (or_13_out, AluFlgIn[4], Set[5]);
  or or_14 (or_14_out, StrAluFlg, Set[5]);
  ClkDelay clkdelay_5 (.in_1(clkdelay_1_out_2), .out_2(clkdelay_5_out_2));
  or or_15 (or_15_out, Clear[4], Reset);
  or or_16 (or_16_out, AluFlgIn[1], Set[6]);
  or or_17 (or_17_out, StrAluFlg, Set[6]);
  ClkDelay clkdelay_6 (.in_1(clkdelay_1_out_2), .out_2(clkdelay_6_out_2));
  Register #(.trigger("high"), .width(1)) Zero (
    .D(or_16_out), .en(or_17_out), .clk(clkdelay_6_out_2), .Q(Flags[5]), .clr(or_18_out));
  or or_18 (or_18_out, Clear[5], Reset);
  or or_19 (or_19_out, StrAluFlg, Set[7]);
  Register #(.trigger("high"), .width(1)) InFerior (
    .D(or_20_out), .en(or_19_out), .clk(clkdelay_7_out_2), .Q(Flags[6]), .clr(or_21_out));
  or or_20 (or_20_out, AluFlgIn[3], Set[7]);
  or or_21 (or_21_out, Clear[6], Reset);
  ClkDelay clkdelay_7 (.in_1(clkdelay_1_out_2), .out_2(clkdelay_7_out_2));
  Register #(.trigger("high"), .width(1)) Halted (
    .D(or_22_out), .en(or_23_out), .clk(clkdelay_8_out_2), .Q(Flags[7]), .clr(or_24_out));
  or or_22 (or_22_out, CUFlgIn[0], Set[0]);
  or or_23 (or_23_out, StrCuFlg, Set[0]);
  or or_24 (or_24_out, Clear[7], Reset);
  ClkDelay clkdelay_8 (.in_1(clkdelay_1_out_2), .out_2(clkdelay_8_out_2));

  // Notes on the sheet:
  //   ESFNZC
  //   HI
endmodule

module ControlUnit (
  input  [23:0] AddrExtIn,
  input  [7:0] DataExtIn,
  input  [7:0] DataBusIn,
  input  ClockExt,
  input  Reset,
  input  [5:0] AluFlgIn,
  output [7:0] DataBusOut,
  output [23:0] AddrExt,
  output [7:0] DataExtOut,
  output RamRead,
  output RamWrite,
  output AluAccuAStr,
  output AluAccuBStr,
  output AluAccuRead,
  output [3:0] AluOpCode,
  output AluEn,
  output [2:0] RegSel,
  output RegRW,
  output RegEn,
  output IODSend,
  output IODRead
);

  wire instrexec_1_nextinstr, instrexec_1_pcset, instrexec_1_ramread, instrexec_1_stkadden,
       instrexec_1_stkinc, instrexec_1_stkstep, instrfetch_1_exec, instrfetch_1_pcstep, instrfetch_1_ramread,
       not_1_out, not_2_out, or_1_out, or_2_out, twocycdel_1_enout;
  wire [2:0] instrfetch_1_bytesel, instrreg_1_r1, instrreg_1_r2, instrreg_1_r3, instrreg_1_r4;
  wire [3:0] instrreg_1_addrmode;
  wire [5:0] instrreg_1_opcode;
  wire [7:0] instrreg_1_ex, instrreg_1_v1, instrreg_1_v2;
  wire [23:0] instrexec_1_pcadr, instrreg_1_vx, PC_q, STKPTR_q;

  or or_1 (or_1_out, instrexec_1_nextinstr, Reset);
  not not_1 (not_1_out, Reset);
  InstrReg instrreg_1 (
    .DataIn(DataExtIn), .ByteSelect(instrfetch_1_bytesel), .Write(instrfetch_1_ramread), .Clock(ClockExt),
    .Opcode(instrreg_1_opcode), .AddrMode(instrreg_1_addrmode), .R1(instrreg_1_r1), .R2(instrreg_1_r2),
    .R3(instrreg_1_r3), .R4(instrreg_1_r4), .V1(instrreg_1_v1), .V2(instrreg_1_v2), .Ex(instrreg_1_ex),
    .Vx(instrreg_1_vx));
  InstrFetch instrfetch_1 (
    .Start(or_1_out), .Clock(ClockExt), .Enable(not_1_out), .ByteSel(instrfetch_1_bytesel),
    .RamRead(instrfetch_1_ramread), .Exec(instrfetch_1_exec), .PCstep(instrfetch_1_pcstep));
  or or_2 (or_2_out, instrfetch_1_pcstep, instrexec_1_pcset);
  Counter #(.max('hffffff), .width(24)) PC (
    .clr(Reset), .load(instrexec_1_pcset), .up(1'b1), .count(1'b1), .clk(or_2_out), .D(instrexec_1_pcadr),
    .Q(PC_q));  // open: carry
  InstrExec instrexec_1 (
    .AddrExtIn(AddrExtIn), .DataExtIn(DataExtIn), .DataBusIn(DataBusIn), .Opcode(instrreg_1_opcode),
    .AddrMode(instrreg_1_addrmode), .R1(instrreg_1_r1), .R2(instrreg_1_r2), .R3(instrreg_1_r3),
    .R4(instrreg_1_r4), .V1(instrreg_1_v1), .V2(instrreg_1_v2), .Ex(instrreg_1_ex), .Vx(instrreg_1_vx),
    .Exec(instrfetch_1_exec), .Clock(ClockExt), .AluFlgIn(AluFlgIn), .Reset(Reset), .PCreg(PC_q),
    .RegSel(RegSel), .DataBusOut(DataBusOut), .AddrExtOut(AddrExt), .DataExtOut(DataExtOut),
    .NextInstr(instrexec_1_nextinstr), .AluAccAStr(AluAccuAStr), .AluAccBStr(AluAccuBStr),
    .AluAccuRead(AluAccuRead), .RegRW(RegRW), .RegEn(RegEn), .RamRead(instrexec_1_ramread),
    .RamWrite(RamWrite), .AluOpCode(AluOpCode), .AluEn(AluEn), .IODSend(IODSend), .IODRead(IODRead),
    .StkAddEn(instrexec_1_stkadden), .StkInc(instrexec_1_stkinc), .StkStep(instrexec_1_stkstep),
    .PCSet(instrexec_1_pcset), .PCAdr(instrexec_1_pcadr));
  not not_2 (not_2_out, instrfetch_1_exec);
  assign AddrExt = not_2_out ? PC_q : 24'bz;  // Controlled_Buffer controlled_buffer_1
  Counter #(.max('hffffff), .width(24)) STKPTR (
    .clr(Reset), .load(1'b0), .up(instrexec_1_stkinc), .count(1'b1), .clk(instrexec_1_stkstep), .Q(STKPTR_q));  // open: D, carry
  TwoCycDel twocycdel_1 (.EnIn(instrexec_1_stkadden), .Clock(ClockExt), .EnOut(twocycdel_1_enout));
  assign AddrExt = twocycdel_1_enout ? STKPTR_q : 24'bz;  // Controlled_Buffer controlled_buffer_2
  or or_3 (RamRead, instrfetch_1_ramread, instrexec_1_ramread);
endmodule

module InstrReg (
  input  [7:0] DataIn,
  input  [2:0] ByteSelect,
  input  Write,
  input  Clock,
  output [5:0] Opcode,
  output [3:0] AddrMode,
  output [2:0] R1,
  output [2:0] R2,
  output [2:0] R3,
  output [2:0] R4,
  output [7:0] V1,
  output [7:0] V2,
  output [7:0] Ex,
  output [23:0] Vx
);

  wire and_1_out, and_2_out, and_3_out, and_4_out, and_5_out, clkdelay_1_out_2, decoder_1_out0,
       decoder_1_out1, decoder_1_out2, decoder_1_out3, decoder_1_out4;

  ClkDelay clkdelay_1 (.in_1(Clock), .out_2(clkdelay_1_out_2));
  Decoder #(.enable("false"), .select(3)) decoder_1 (
    .out0(decoder_1_out0), .out1(decoder_1_out1), .out2(decoder_1_out2), .out3(decoder_1_out3),
    .out4(decoder_1_out4), .sel(ByteSelect));  // open: out5, out6, out7
  Register register_1 (.D(DataIn), .en(and_1_out), .clk(clkdelay_1_out_2), .Q({Opcode, AddrMode[3:2]}));  // open: clr
  and and_1 (and_1_out, Write, decoder_1_out0);
  Register register_2 (.D(DataIn), .en(and_2_out), .clk(clkdelay_1_out_2), .Q({AddrMode[1:0], R1, R2}));  // open: clr
  and and_2 (and_2_out, Write, decoder_1_out1);
  Register register_3 (.D(DataIn), .en(and_3_out), .clk(clkdelay_1_out_2), .Q({V1[7:3], R3}));  // open: clr
  and and_3 (and_3_out, Write, decoder_1_out2);
  Register register_4 (.D(DataIn), .en(and_4_out), .clk(clkdelay_1_out_2), .Q(V2));  // open: clr
  and and_4 (and_4_out, Write, decoder_1_out3);
  Register register_5 (.D(DataIn), .en(and_5_out), .clk(clkdelay_1_out_2), .Q(Ex));  // open: clr
  and and_5 (and_5_out, Write, decoder_1_out4);

  assign R4 = Ex[2:0];
  assign V1[2:0] = R3;
  assign Vx = {V1[7:3], R3, V2, Ex};
endmodule

module InstrFetch (
  input  Start,
  input  Clock,
  input  Enable,
  output [2:0] ByteSel,
  output RamRead,
  output Exec,
  output PCstep
);

  wire and_1_out, and_2_out, and_3_out, and_6_out, d_ff_1_q, d_ff_2_q, d_ff_3_qn, t_ff_1_q, t_ff_1_qn;

  and and_1 (and_1_out, Clock, Enable);
  D_Flip_Flop d_ff_1 (.D(and_1_out), .clk(and_1_out), .Q(d_ff_1_q), .reset(Start));  // open: Qn, preset
  D_Flip_Flop d_ff_2 (.D(d_ff_1_q), .clk(and_1_out), .Q(d_ff_2_q), .reset(Start));  // open: Qn, preset
  T_Flip_Flop t_ff_1 (.T(and_2_out), .clk(and_2_out), .Q(t_ff_1_q), .Qn(t_ff_1_qn), .reset(Start));  // open: preset
  and and_2 (and_2_out, and_1_out, d_ff_2_q);
  and and_3 (and_3_out, d_ff_3_qn, t_ff_1_q);
  Counter #(.max('h7), .width(3)) counter_1 (
    .clr(Start), .load(1'b0), .up(1'b1), .count(1'b1), .clk(and_3_out), .Q(ByteSel));  // open: D, carry
  and and_4 (PCstep, d_ff_3_qn, t_ff_1_q);
  and and_5 (RamRead, d_ff_3_qn, t_ff_1_qn);
  D_Flip_Flop d_ff_3 (.D(and_6_out), .clk(and_6_out), .Q(Exec), .Qn(d_ff_3_qn), .reset(Start));  // open: preset
  and and_6 (and_6_out, ByteSel[2], ~ByteSel[1], ByteSel[0]);  // AND_Gate
endmodule

module ClkDelay (
  input  in_1,
  output out_2
);

  wire not_1_out, not_2_out, not_3_out, not_4_out, not_5_out, not_6_out, not_7_out, not_8_out, not_9_out,
       not_10_out, not_11_out, not_12_out, not_13_out, not_14_out, not_15_out, not_16_out, not_17_out,
       not_18_out, not_19_out, not_20_out, not_21_out, not_22_out, not_23_out, not_24_out, not_25_out,
       not_26_out, not_27_out, not_28_out, not_29_out, not_30_out, not_31_out;

  not not_1 (not_1_out, in_1);
  not not_2 (not_2_out, not_1_out);
  not not_3 (not_3_out, not_2_out);
  not not_4 (not_4_out, not_26_out);
  not not_5 (not_5_out, not_4_out);
  not not_6 (not_6_out, not_5_out);
  not not_7 (not_7_out, not_28_out);
  not not_8 (not_8_out, not_7_out);
  not not_9 (not_9_out, not_8_out);
  not not_10 (not_10_out, not_30_out);
  not not_11 (not_11_out, not_10_out);
  not not_12 (not_12_out, not_11_out);
  not not_13 (not_13_out, not_3_out);
  not not_14 (not_14_out, not_13_out);
  not not_15 (not_15_out, not_14_out);
  not not_16 (not_16_out, not_6_out);
  not not_17 (not_17_out, not_16_out);
  not not_18 (not_18_out, not_17_out);
  not not_19 (not_19_out, not_9_out);
  not not_20 (not_20_out, not_19_out);
  not not_21 (not_21_out, not_20_out);
  not not_22 (not_22_out, not_12_out);
  not not_23 (not_23_out, not_22_out);
  not not_24 (not_24_out, not_23_out);
  not not_25 (not_25_out, not_15_out);
  not not_26 (not_26_out, not_25_out);
  not not_27 (not_27_out, not_18_out);
  not not_28 (not_28_out, not_27_out);
  not not_29 (not_29_out, not_21_out);
  not not_30 (not_30_out, not_29_out);
  not not_31 (not_31_out, not_24_out);
  not not_32 (out_2, not_31_out);
endmodule

module InstrExec (
  input  [23:0] AddrExtIn,
  input  [7:0] DataExtIn,
  input  [7:0] DataBusIn,
  input  [5:0] Opcode,
  input  [3:0] AddrMode,
  input  [2:0] R1,
  input  [2:0] R2,
  input  [2:0] R3,
  input  [2:0] R4,
  input  [7:0] V1,
  input  [7:0] V2,
  input  [7:0] Ex,
  input  [23:0] Vx,
  input  Exec,
  input  Clock,
  input  [5:0] AluFlgIn,
  input  Reset,
  input  [23:0] PCreg,
  output [2:0] RegSel,
  output [7:0] DataBusOut,
  output [23:0] AddrExtOut,
  output [7:0] DataExtOut,
  output NextInstr,
  output AluAccAStr,
  output AluAccBStr,
  output AluAccuRead,
  output RegRW,
  output RegEn,
  output RamRead,
  output RamWrite,
  output [3:0] AluOpCode,
  output AluEn,
  output IODSend,
  output IODRead,
  output StkAddEn,
  output StkInc,
  output StkStep,
  output PCSet,
  output [23:0] PCAdr
);

  wire and_1_out, and_2_out, and_3_out, and_4_out, and_5_out, and_6_out, and_7_out, and_8_out, and_9_out,
       and_10_out, and_11_out, and_13_out, and_14_out, and_15_out, and_16_out, and_17_out, and_18_out,
       and_19_out, and_20_out, and_21_out, and_22_out, and_23_out, and_24_out, and_25_out, and_26_out,
       clkdelay_1_out_2, clkdelay_2_out_2, clkdelay_3_out_2, clkdelay_4_out_2, clkdelay_5_out_2,
       clkdelay_6_out_2, clkdelay_8_out_2, d_ff_1_q, d_ff_2_q, decoder_1_out0, decoder_1_out1,
       decoder_1_out2, decoder_1_out3, decoder_1_out4, decoder_1_out5, decoder_1_out6, decoder_1_out7,
       decoder_1_out8, decoder_1_out9, decoder_1_out10, decoder_1_out11, decoder_1_out12, decoder_1_out13,
       decoder_1_out14, decoder_1_out15, decoder_2_out7, opcodedecoder_1_out_5, opcodedecoder_1_out_6,
       opcodedecoder_1_out_7, opcodedecoder_1_out_8, opcodedecoder_1_out_9, opcodedecoder_1_out_10,
       opcodedecoder_1_out_11, opcodedecoder_1_out_15, opcodedecoder_1_out_32, opcodedecoder_1_out_33,
       opcodedecoder_1_out_34, opcodedecoder_1_out_35, opcodedecoder_1_out_36, opcodedecoder_1_out_37,
       opcodedecoder_1_out_40, opcodedecoder_1_out_41, opcodedecoder_1_out_42, opcodedecoder_1_out_43,
       opcodedecoder_1_out_44, opcodedecoder_1_out_45, opcodedecoder_1_out_46, opcodedecoder_1_out_47,
       opcodedecoder_1_out_48, opcodedecoder_1_out_49, opcodedecoder_1_out_50, opcodedecoder_1_out_51,
       opcodedecoder_1_out_52, opcodedecoder_1_out_53, opcodedecoder_1_out_54, or_1_out, or_2_out, or_4_out,
       or_8_out, or_9_out, or_10_out, or_11_out, twocycdel_1_enout, twocycdel_2_enout, twocycdel_3_enout,
       twocycdel_4_enout, twocycdel_5_enout, twocycdel_6_enout, twocycdel_7_enout, twocycdel_8_enout,
       twocycdel_9_enout, twocycdel_10_enout, twocycdel_11_enout;
  wire [3:0] InstrTable_data_3, InstrTable_data_4;
  wire [4:0] InstrCycle_q;
  wire [5:0] controlled_buffer_1_out, InstrTable_data_2;
  wire [6:0] opcodedecoder_1_out_17;
  wire [7:0] AddrAccu1_q, AddrAccu2_q, AddrAccu3_q, bitselector_1_out, flagregister_1_flags,
       opcodedecoder_1_out_24, register_1_q, register_2_q;
  wire [9:8] fulladder1b_1_s;
  wire [11:0] counter_1_q;
  wire [15:14] InstrTable_data;
  wire [23:0] buffer_17_out, buffer_25_out, buffer_49_out, multiplier_1_out, register_3_q;

  and and_1 (and_1_out, Exec, Clock);
  D_Flip_Flop d_ff_1 (.D(and_1_out), .clk(and_1_out), .Q(d_ff_1_q), .reset(clkdelay_6_out_2));  // open: Qn, preset
  Register #(.trigger("high")) register_1 (
    .D(DataBusIn), .en(or_1_out), .clk(clkdelay_1_out_2), .Q(register_1_q));  // open: clr
  ClkDelay clkdelay_1 (.in_1(clkdelay_2_out_2), .out_2(clkdelay_1_out_2));
  ClkDelay clkdelay_2 (.in_1(Clock), .out_2(clkdelay_2_out_2));
  D_Flip_Flop d_ff_2 (.D(d_ff_1_q), .clk(and_1_out), .Q(d_ff_2_q), .reset(clkdelay_6_out_2));  // open: Qn, preset
  and and_2 (and_2_out, Clock, d_ff_2_q);
  FlagRegister flagregister_1 (
    .StrAluFlg(AluEn), .AluFlgIn(AluFlgIn), .Clock(Clock), .Reset(Reset), .Set(opcodedecoder_1_out_24),
    .Clear({1'b0, opcodedecoder_1_out_17}), .Flags(flagregister_1_flags));  // open: StrCuFlg, CUFlgIn
  or or_1 (or_1_out, or_4_out, or_9_out);
  Counter #(.max('h1f), .width(5)) InstrCycle (
    .clr(clkdelay_6_out_2), .load(1'b0), .up(1'b1), .count(1'b1), .clk(and_2_out), .Q(InstrCycle_q));  // open: D, carry
  ROM #(.addrWidth(14), .dataWidth(16)) InstrTable (
    .addr({Opcode, AddrMode[2:0], InstrCycle_q}),
    .data({InstrTable_data, InstrTable_data_2, InstrTable_data_3, InstrTable_data_4}));
  Register register_2 (.D(DataExtIn), .en(or_4_out), .clk(clkdelay_3_out_2), .Q(register_2_q));  // open: clr
  ClkDelay clkdelay_3 (.in_1(clkdelay_4_out_2), .out_2(clkdelay_3_out_2));
  ClkDelay clkdelay_4 (.in_1(Clock), .out_2(clkdelay_4_out_2));
  ClkDelay clkdelay_5 (.in_1(and_1_out), .out_2(clkdelay_5_out_2));
  assign controlled_buffer_1_out = clkdelay_5_out_2 ? InstrTable_data_2 : 6'bz;  // Controlled_Buffer controlled_buffer_1
  ClkDelay clkdelay_6 (.in_1(NextInstr), .out_2(clkdelay_6_out_2));
  Decoder #(.select(4)) decoder_1 (
    .out0(decoder_1_out0), .out1(decoder_1_out1), .out2(decoder_1_out2), .out3(decoder_1_out3),
    .out4(decoder_1_out4), .out5(decoder_1_out5), .out6(decoder_1_out6), .out7(decoder_1_out7),
    .out8(decoder_1_out8), .out9(decoder_1_out9), .out10(decoder_1_out10), .out11(decoder_1_out11),
    .out12(decoder_1_out12), .out13(decoder_1_out13), .out14(decoder_1_out14), .out15(decoder_1_out15),
    .sel(InstrTable_data_3), .en(and_1_out));
  Decoder #(.select(4)) decoder_2 (
    .out7(decoder_2_out7), .sel(InstrTable_data_4), .en(and_1_out));  // open: out0, out1, out2, out3, out4, out5, out6, out8, out9, out10, out11, out12, out13, out14, out15
  or or_2 (or_2_out, decoder_1_out0, decoder_1_out1, decoder_1_out2, decoder_1_out3);
  OpcodeDecoder opcodedecoder_1 (
    .Opcode(controlled_buffer_1_out), .out_43(opcodedecoder_1_out_43), .out_44(opcodedecoder_1_out_44),
    .out_45(opcodedecoder_1_out_45), .out_46(opcodedecoder_1_out_46), .out_47(opcodedecoder_1_out_47),
    .out_48(opcodedecoder_1_out_48), .out_49(opcodedecoder_1_out_49), .out_50(opcodedecoder_1_out_50),
    .out_51(opcodedecoder_1_out_51), .out_52(opcodedecoder_1_out_52), .out_53(opcodedecoder_1_out_53),
    .out_54(opcodedecoder_1_out_54), .out_55(NextInstr), .out_3(AluAccAStr), .out_4(AluAccBStr),
    .out_5(opcodedecoder_1_out_5), .out_6(opcodedecoder_1_out_6), .out_7(opcodedecoder_1_out_7),
    .out_8(opcodedecoder_1_out_8), .out_9(opcodedecoder_1_out_9), .out_10(opcodedecoder_1_out_10),
    .out_11(opcodedecoder_1_out_11), .out_12(RegRW), .out_13(RamRead), .out_14(RamWrite),
    .out_15(opcodedecoder_1_out_15), .out_16(StkInc), .out_17(opcodedecoder_1_out_17[0]),
    .out_18(opcodedecoder_1_out_17[1]), .out_19(opcodedecoder_1_out_17[2]),
    .out_20(opcodedecoder_1_out_17[3]), .out_21(opcodedecoder_1_out_17[4]),
    .out_22(opcodedecoder_1_out_17[5]), .out_23(opcodedecoder_1_out_17[6]),
    .out_24(opcodedecoder_1_out_24[0]), .out_25(opcodedecoder_1_out_24[1]),
    .out_26(opcodedecoder_1_out_24[2]), .out_27(opcodedecoder_1_out_24[3]),
    .out_28(opcodedecoder_1_out_24[4]), .out_29(opcodedecoder_1_out_24[5]),
    .out_30(opcodedecoder_1_out_24[6]), .out_31(opcodedecoder_1_out_24[7]), .out_32(opcodedecoder_1_out_32),
    .out_33(opcodedecoder_1_out_33), .out_34(opcodedecoder_1_out_34), .out_35(opcodedecoder_1_out_35),
    .out_36(opcodedecoder_1_out_36), .out_37(opcodedecoder_1_out_37), .out_38(IODRead), .out_39(IODSend),
    .out_40(opcodedecoder_1_out_40), .out_41(opcodedecoder_1_out_41), .out_42(opcodedecoder_1_out_42));  // open: out_2
  assign RegSel = decoder_1_out0 ? R1 : 3'bz;  // Controlled_Buffer controlled_buffer_2
  assign RegSel = decoder_1_out1 ? R2 : 3'bz;  // Controlled_Buffer controlled_buffer_3
  assign RegSel = decoder_1_out2 ? R3 : 3'bz;  // Controlled_Buffer controlled_buffer_4
  assign RegSel = decoder_1_out3 ? R4 : 3'bz;  // Controlled_Buffer controlled_buffer_5
  or or_3 (AluEn, opcodedecoder_1_out_53, opcodedecoder_1_out_52, opcodedecoder_1_out_51, opcodedecoder_1_out_50, opcodedecoder_1_out_49, opcodedecoder_1_out_48, opcodedecoder_1_out_47, opcodedecoder_1_out_46, opcodedecoder_1_out_45, opcodedecoder_1_out_44, opcodedecoder_1_out_43, opcodedecoder_1_out_42, opcodedecoder_1_out_41);
  assign RegSel = decoder_1_out11 ? 3'b100 : 3'bz;  // Controlled_Buffer controlled_buffer_6
  and and_3 (and_3_out, decoder_2_out7, RegRW);
  and and_4 (and_4_out, or_2_out, opcodedecoder_1_out_11);
  and and_5 (and_5_out, opcodedecoder_1_out_37, flagregister_1_flags[6]);
  and and_6 (and_6_out, opcodedecoder_1_out_36, flagregister_1_flags[5]);
  and and_7 (and_7_out, opcodedecoder_1_out_35, flagregister_1_flags[4]);
  and and_8 (and_8_out, opcodedecoder_1_out_34, flagregister_1_flags[3]);
  and and_9 (and_9_out, opcodedecoder_1_out_33, flagregister_1_flags[1]);
  and and_10 (and_10_out, opcodedecoder_1_out_32, flagregister_1_flags[0]);
  or or_4 (or_4_out, IODRead, RamRead);
  and and_11 (and_11_out, opcodedecoder_1_out_10, decoder_1_out7);
  or or_5 (AluAccuRead, and_11_out, and_3_out);
  or or_6 (RegEn, RegRW, and_4_out);
  and and_12 (StkAddEn, decoder_1_out12, opcodedecoder_1_out_9);
  or or_7 (StkStep, StkInc, opcodedecoder_1_out_15);
  or or_8 (or_8_out, and_5_out, and_6_out, and_7_out, opcodedecoder_1_out_5, and_8_out, and_9_out, and_10_out);
  buf buffer_1 (buffer_17_out[8], PCreg[8]);
  buf buffer_2 (buffer_17_out[9], PCreg[9]);
  buf buffer_3 (buffer_17_out[10], PCreg[10]);
  buf buffer_4 (buffer_17_out[11], PCreg[11]);
  buf buffer_5 (buffer_17_out[12], PCreg[12]);
  buf buffer_6 (buffer_17_out[13], PCreg[13]);
  buf buffer_7 (buffer_17_out[14], PCreg[14]);
  buf buffer_8 (buffer_17_out[15], PCreg[15]);
  buf buffer_9 (buffer_17_out[16], PCreg[16]);
  buf buffer_10 (buffer_17_out[17], PCreg[17]);
  buf buffer_11 (buffer_17_out[18], PCreg[18]);
  buf buffer_12 (buffer_17_out[19], PCreg[19]);
  buf buffer_13 (buffer_17_out[20], PCreg[20]);
  buf buffer_14 (buffer_17_out[21], PCreg[21]);
  buf buffer_15 (buffer_17_out[22], PCreg[22]);
  buf buffer_16 (buffer_17_out[23], PCreg[23]);
  or or_9 (or_9_out, AluAccuRead, RegEn);
  AluOpcodeCoder aluopcodecoder_1 (
    .adcCmd(opcodedecoder_1_out_41), .addCmd(opcodedecoder_1_out_42), .subCmd(opcodedecoder_1_out_43),
    .andCmd(opcodedecoder_1_out_44), .orCmd(opcodedecoder_1_out_45), .xorCmd(opcodedecoder_1_out_46),
    .notCmd(opcodedecoder_1_out_47), .shlCmd(opcodedecoder_1_out_48), .asrCmd(opcodedecoder_1_out_49),
    .shrCmd(opcodedecoder_1_out_50), .cmpCmd(opcodedecoder_1_out_51), .incCmd(opcodedecoder_1_out_52),
    .decCmd(opcodedecoder_1_out_53), .aluOpcode(AluOpCode));
  and and_13 (and_13_out, or_8_out, decoder_1_out5);
  assign PCAdr = and_13_out ? Vx : 24'bz;  // Controlled_Buffer controlled_buffer_7
  buf buffer_17 (buffer_17_out[0], register_2_q[0]);
  buf buffer_18 (buffer_17_out[1], register_2_q[1]);
  buf buffer_19 (buffer_17_out[2], register_2_q[2]);
  buf buffer_20 (buffer_17_out[3], register_2_q[3]);
  buf buffer_21 (buffer_17_out[4], register_2_q[4]);
  buf buffer_22 (buffer_17_out[5], register_2_q[5]);
  buf buffer_23 (buffer_17_out[6], register_2_q[6]);
  buf buffer_24 (buffer_17_out[7], register_2_q[7]);
  and and_14 (and_14_out, or_8_out, decoder_1_out8);
  assign PCAdr = and_14_out ? buffer_17_out : 24'bz;  // Controlled_Buffer controlled_buffer_8
  buf buffer_25 (buffer_25_out[0], PCreg[0]);
  buf buffer_26 (buffer_25_out[1], PCreg[1]);
  buf buffer_27 (buffer_25_out[2], PCreg[2]);
  buf buffer_28 (buffer_25_out[3], PCreg[3]);
  buf buffer_29 (buffer_25_out[4], PCreg[4]);
  buf buffer_30 (buffer_25_out[5], PCreg[5]);
  buf buffer_31 (buffer_25_out[6], PCreg[6]);
  buf buffer_32 (buffer_25_out[7], PCreg[7]);
  buf buffer_33 (buffer_25_out[16], PCreg[16]);
  buf buffer_34 (buffer_25_out[17], PCreg[17]);
  buf buffer_35 (buffer_25_out[18], PCreg[18]);
  buf buffer_36 (buffer_25_out[19], PCreg[19]);
  buf buffer_37 (buffer_25_out[20], PCreg[20]);
  buf buffer_38 (buffer_25_out[21], PCreg[21]);
  buf buffer_39 (buffer_25_out[22], PCreg[22]);
  buf buffer_40 (buffer_25_out[23], PCreg[23]);
  buf buffer_41 (buffer_25_out[8], register_2_q[0]);
  buf buffer_42 (buffer_25_out[9], register_2_q[1]);
  buf buffer_43 (buffer_25_out[10], register_2_q[2]);
  buf buffer_44 (buffer_25_out[11], register_2_q[3]);
  buf buffer_45 (buffer_25_out[12], register_2_q[4]);
  buf buffer_46 (buffer_25_out[13], register_2_q[5]);
  buf buffer_47 (buffer_25_out[14], register_2_q[6]);
  buf buffer_48 (buffer_25_out[15], register_2_q[7]);
  TwoCycDel twocycdel_1 (.EnIn(or_4_out), .Clock(Clock), .EnOut(twocycdel_1_enout));
  assign DataBusOut = twocycdel_1_enout ? register_2_q : 8'bz;  // Controlled_Buffer controlled_buffer_9
  and and_15 (and_15_out, decoder_1_out4, opcodedecoder_1_out_10);
  TwoCycDel twocycdel_2 (.EnIn(and_15_out), .Clock(Clock), .EnOut(twocycdel_2_enout));
  assign DataBusOut = twocycdel_2_enout ? V1 : 8'bz;  // Controlled_Buffer controlled_buffer_10
  BitSelector #(.group(8)) bitselector_1 (.in(register_1_q), .out(bitselector_1_out), .sel(decoder_1_out4));
  and and_16 (and_16_out, or_8_out, decoder_1_out9);
  assign PCAdr = and_16_out ? buffer_25_out : 24'bz;  // Controlled_Buffer controlled_buffer_11
  buf buffer_49 (buffer_49_out[0], PCreg[0]);
  buf buffer_50 (buffer_49_out[1], PCreg[1]);
  buf buffer_51 (buffer_49_out[2], PCreg[2]);
  buf buffer_52 (buffer_49_out[3], PCreg[3]);
  buf buffer_53 (buffer_49_out[4], PCreg[4]);
  buf buffer_54 (buffer_49_out[5], PCreg[5]);
  buf buffer_55 (buffer_49_out[6], PCreg[6]);
  buf buffer_56 (buffer_49_out[7], PCreg[7]);
  buf buffer_57 (buffer_49_out[8], PCreg[8]);
  buf buffer_58 (buffer_49_out[9], PCreg[9]);
  buf buffer_59 (buffer_49_out[10], PCreg[10]);
  buf buffer_60 (buffer_49_out[11], PCreg[11]);
  buf buffer_61 (buffer_49_out[12], PCreg[12]);
  buf buffer_62 (buffer_49_out[13], PCreg[13]);
  buf buffer_63 (buffer_49_out[14], PCreg[14]);
  buf buffer_64 (buffer_49_out[15], PCreg[15]);
  Register #(.trigger("high")) AddrAccu1 (
    .D(bitselector_1_out), .en(opcodedecoder_1_out_6), .clk(Clock), .Q(AddrAccu1_q));  // open: clr
  Register #(.trigger("high")) AddrAccu2 (
    .D(bitselector_1_out), .en(opcodedecoder_1_out_7), .clk(Clock), .Q(AddrAccu2_q));  // open: clr
  Register #(.trigger("high")) AddrAccu3 (
    .D(bitselector_1_out), .en(opcodedecoder_1_out_8), .clk(Clock), .Q(AddrAccu3_q));  // open: clr
  or or_10 (or_10_out, decoder_1_out7, decoder_1_out8);
  buf buffer_65 (buffer_49_out[16], register_2_q[0]);
  buf buffer_66 (buffer_49_out[17], register_2_q[1]);
  buf buffer_67 (buffer_49_out[18], register_2_q[2]);
  buf buffer_68 (buffer_49_out[19], register_2_q[3]);
  buf buffer_69 (buffer_49_out[20], register_2_q[4]);
  buf buffer_70 (buffer_49_out[21], register_2_q[5]);
  buf buffer_71 (buffer_49_out[22], register_2_q[6]);
  buf buffer_72 (buffer_49_out[23], register_2_q[7]);
  and and_17 (and_17_out, or_10_out, opcodedecoder_1_out_10);
  and and_18 (and_18_out, or_8_out, decoder_1_out10);
  assign PCAdr = and_18_out ? buffer_49_out : 24'bz;  // Controlled_Buffer controlled_buffer_12
  TwoCycDel twocycdel_3 (.EnIn(and_17_out), .Clock(Clock), .EnOut(twocycdel_3_enout));
  assign DataExtOut = twocycdel_3_enout ? register_1_q : 8'bz;  // Controlled_Buffer controlled_buffer_13
  and and_19 (and_19_out, or_8_out, decoder_1_out6);
  assign PCAdr = and_19_out ? {AddrAccu3_q, AddrAccu2_q, AddrAccu1_q} : 24'bz;  // Controlled_Buffer controlled_buffer_14
  ClkDelay clkdelay_7 (.in_1(or_8_out), .out_2(PCSet));
  assign AddrExtOut = twocycdel_4_enout ? {AddrAccu3_q, AddrAccu2_q, AddrAccu1_q} : 24'bz;  // Controlled_Buffer controlled_buffer_15
  TwoCycDel twocycdel_4 (.EnIn(and_20_out), .Clock(Clock), .EnOut(twocycdel_4_enout));
  and and_20 (and_20_out, decoder_1_out6, opcodedecoder_1_out_9);
  assign DataExtOut = twocycdel_5_enout ? PCreg[7:0] : 8'bz;  // Controlled_Buffer controlled_buffer_16
  and and_21 (and_21_out, decoder_1_out15, opcodedecoder_1_out_10);
  TwoCycDel twocycdel_5 (.EnIn(and_21_out), .Clock(Clock), .EnOut(twocycdel_5_enout));
  and and_22 (and_22_out, decoder_1_out5, opcodedecoder_1_out_9);
  and and_23 (and_23_out, decoder_1_out8, opcodedecoder_1_out_9);
  and and_24 (and_24_out, opcodedecoder_1_out_9, decoder_1_out4);
  assign AddrExtOut = twocycdel_6_enout ? Vx : 24'bz;  // Controlled_Buffer controlled_buffer_17
  TwoCycDel twocycdel_6 (.EnIn(and_22_out), .Clock(Clock), .EnOut(twocycdel_6_enout));
  TwoCycDel twocycdel_7 (.EnIn(and_23_out), .Clock(Clock), .EnOut(twocycdel_7_enout));
  and and_25 (and_25_out, decoder_1_out14, opcodedecoder_1_out_10);
  assign DataExtOut = twocycdel_8_enout ? PCreg[15:8] : 8'bz;  // Controlled_Buffer controlled_buffer_18
  TwoCycDel twocycdel_8 (.EnIn(and_25_out), .Clock(Clock), .EnOut(twocycdel_8_enout));
  assign AddrExtOut = twocycdel_7_enout ? {{16{1'b0}}, register_1_q} : 24'bz;  // Controlled_Buffer controlled_buffer_19
  assign AddrExtOut = and_24_out ? {{16{1'b0}}, V1} : 24'bz;  // Controlled_Buffer controlled_buffer_20
  and and_26 (and_26_out, decoder_1_out13, opcodedecoder_1_out_10);
  Register #(.width(24)) register_3 (
    .D(AddrExtIn), .en(clkdelay_8_out_2), .clk(clkdelay_8_out_2), .Q(register_3_q));  // open: clr
  ClkDelay clkdelay_8 (.in_1(and_24_out), .out_2(clkdelay_8_out_2));
  assign DataExtOut = twocycdel_9_enout ? PCreg[23:16] : 8'bz;  // Controlled_Buffer controlled_buffer_21
  TwoCycDel twocycdel_9 (.EnIn(and_26_out), .Clock(Clock), .EnOut(twocycdel_9_enout));
  Multiplier #(.width(24)) multiplier_1 (.a(register_3_q), .b(24'h3), .out(multiplier_1_out));  // open: cin, cout
  FullAdder1b fulladder1b_1 (
    .A(multiplier_1_out[8]), .B(multiplier_1_out[9]), .Cin(1'b1), .S(fulladder1b_1_s[8]),
    .Cout(fulladder1b_1_s[9]));
  TwoCycDel twocycdel_10 (.EnIn(opcodedecoder_1_out_40), .Clock(Clock), .EnOut(twocycdel_10_enout));
  assign AddrExtOut = twocycdel_10_enout ? {multiplier_1_out[23:10], fulladder1b_1_s, multiplier_1_out[7:0]} : 24'bz;  // Controlled_Buffer controlled_buffer_22
  or or_11 (or_11_out, opcodedecoder_1_out_40, opcodedecoder_1_out_54);
  Counter #(.max('h3ff), .width(12)) counter_1 (
    .clr(1'b0), .load(opcodedecoder_1_out_40), .up(opcodedecoder_1_out_54), .count(1'b1), .clk(or_11_out),
    .D({multiplier_1_out[11:10], fulladder1b_1_s, multiplier_1_out[7:0]}), .Q(counter_1_q));  // open: carry
  assign AddrExtOut = twocycdel_11_enout ? {multiplier_1_out[23:12], counter_1_q} : 24'bz;  // Controlled_Buffer controlled_buffer_23
  TwoCycDel twocycdel_11 (.EnIn(opcodedecoder_1_out_54), .Clock(Clock), .EnOut(twocycdel_11_enout));

  // Notes on the sheet:
  //   contents of InstrTable (hex, n*v repeats v):
  //   3500 287*0 900 100 910 200 2700 a07 3500 25*0 900 100 840 200 2700 a07 3500 25*0 900 100 750 b00 200
  //   2700 a07 3500 184*0 900 100 910 200 2800 a07 3500 25*0 900 100 840 200 2800 a07 3500 25*0 900 100
  //   750 b00 200 2800 a07 3500 184*0 900 100 910 200 2a00 a07 3500 25*0 900 100 840 200 2a00 a07 3500
  //   25*0 900 100 750 b00 200 2a00 a07 3500 312*0 7c0 8d0 c00 e00 7c0 8e0 c00 e00 7c0 8f0 c00 e00 900 600
  //   910 500 920 400 360 3500 12*0 7c0 8d0 c00 e00 7c0 8e0 c00 e00 7c0 8f0 c00 e00 350 3500 50*0 f00 3500
  //   254*0 1000 3500 254*0 1100 3500 254*0 1200 3500 254*0 1300 3500 254*0 1400 3500 254*0 1500 3500
  //   286*0 900 100 910 200 3100 3500 26*0 900 100 840 200 3100 3500 26*0 900 100 750 b00 200 3100 3500
  //   185*0 900 100 3300 a07 3500 123*0 900 600 910 500 920 400 760 b00 100 3300 760 870 c00 3500 18*0 750
  //   b00 100 3300 750 870 c00 3500 56*0 1600 3500 286*0 910 780 2400 a08 3500 251*0 900 400 540 640 910
  //   760 880 2500 3500 247*0 900 100 3300 a07 3500 123*0 900 600 910 500 920 400 760 b00 100 3200 760 870
  //   c00 3500 18*0 750 b00 100 3200 750 870 c00 3500 280*0 7c0 8d0 c00 e00 7c0 8e0 c00 e00 7c0 8f0 c00
  //   e00 740 2600 b00 600 3400 b00 500 3400 b00 400 360 3500 424*0 900 600 910 500 920 400 1e60 3500 24*0
  //   1e50 3500 222*0 900 600 910 500 920 400 1f60 3500 24*0 1f50 3500 222*0 900 600 910 500 920 400 2060
  //   3500 24*0 2050 3500 222*0 900 600 910 500 920 400 360 3500 24*0 350 3500 222*0 900 600 910 500 920
  //   400 2160 3500 24*0 2150 3500 222*0 900 600 910 500 920 400 2260 3500 24*0 2250 3500 222*0 900 600
  //   910 500 920 400 2360 3500 24*0 2350 3500 158*0 900 600 910 500 920 400 930 880 760 c00 3500 21*0 900
  //   750 880 c00 3500 219*0 900 600 910 500 920 400 760 b00 a38 3500 22*0 750 b00 a08 3500 156*0 910 a08
  //   3500 29*0 840 a08 3500 221*0 900 100 2d00 a07 3500 155*0 750 b00 100 2d00 750 870 c00 3500 88*0 900
  //   100 910 200 2b00 a07 3500 25*0 900 100 840 200 2b00 a07 3500 25*0 900 100 750 b00 200 2b00 a07 3500
  //   184*0 d00 7c0 b00 a08 3500 251*0 900 7c0 880 c00 e00 3500 250*0 d00 7c0 b00 380 d00 7c0 b00 390 d00
  //   7c0 b00 3a0 3500 243*0 900 100 2e00 a07 3500 251*0 900 100 2f00 a07 3500 251*0 900 100 3000 a07 3500
  //   219*0 1700 3500 254*0 1800 3500 254*0 1900 3500 254*0 1a00 3500 254*0 1b00 3500 254*0 1c00 3500
  //   254*0 1d00 3500 286*0 900 100 910 200 2900 a07 3500 25*0 900 100 840 200 2900 a07 3500 25*0 900 100
  //   750 b00 200 2900 a07 3500 184*0 900 100 910 200 2c00 a07 3500 25*0 900 100 840 200 2c00 a07 3500
  //   25*0 900 100 750 b00 200 2c00 a07 3500 408*0 9b0 7c0 880 c00 e00 ab8 1100 7c0 8d0 c00 e00 7c0 8e0
  //   c00 e00 7c0 8f0 c00 e00 2600 b00 600 3400 b00 500 3400 b00 400 360 3500
  //   µoper1
  //   µoper2
  //   µopcode
  //   IVT Address Calculation
endmodule

module OpcodeDecoder (
  input  [5:0] Opcode,
  output out_2,
  output out_3,
  output out_4,
  output out_5,
  output out_6,
  output out_7,
  output out_8,
  output out_9,
  output out_10,
  output out_11,
  output out_12,
  output out_13,
  output out_14,
  output out_15,
  output out_16,
  output out_17,
  output out_18,
  output out_19,
  output out_20,
  output out_21,
  output out_22,
  output out_23,
  output out_24,
  output out_25,
  output out_26,
  output out_27,
  output out_28,
  output out_29,
  output out_30,
  output out_31,
  output out_32,
  output out_33,
  output out_34,
  output out_35,
  output out_36,
  output out_37,
  output out_38,
  output out_39,
  output out_40,
  output out_41,
  output out_42,
  output out_43,
  output out_44,
  output out_45,
  output out_46,
  output out_47,
  output out_48,
  output out_49,
  output out_50,
  output out_51,
  output out_52,
  output out_53,
  output out_54,
  output out_55
);

  wire not_1_out;

  not not_1 (not_1_out, Opcode[5]);
  Decoder #(.select(5)) decoder_1 (
    .out0(out_2), .out1(out_3), .out2(out_4), .out3(out_5), .out4(out_6), .out5(out_7), .out6(out_8),
    .out7(out_9), .out8(out_10), .out9(out_11), .out10(out_12), .out11(out_13), .out12(out_14),
    .out13(out_15), .out14(out_16), .out15(out_17), .out16(out_18), .out17(out_19), .out18(out_20),
    .out19(out_21), .out20(out_22), .out21(out_23), .out22(out_24), .out23(out_25), .out24(out_26),
    .out25(out_27), .out26(out_28), .out27(out_29), .out28(out_30), .out29(out_31), .out30(out_32),
    .out31(out_33), .sel(Opcode[4:0]), .en(not_1_out));
  Decoder #(.select(5)) decoder_2 (
    .out0(out_34), .out1(out_35), .out2(out_36), .out3(out_37), .out4(out_38), .out5(out_39), .out6(out_40),
    .out7(out_41), .out8(out_42), .out9(out_43), .out10(out_44), .out11(out_45), .out12(out_46),
    .out13(out_47), .out14(out_48), .out15(out_49), .out16(out_50), .out17(out_51), .out18(out_52),
    .out19(out_53), .out20(out_54), .out21(out_55), .sel(Opcode[4:0]), .en(Opcode[5]));  // open: out22, out23, out24, out25, out26, out27, out28, out29, out30, out31
endmodule

module AluOpcodeCoder (
  input  adcCmd,
  input  addCmd,
  input  subCmd,
  input  andCmd,
  input  orCmd,
  input  xorCmd,
  input  notCmd,
  input  shlCmd,
  input  asrCmd,
  input  shrCmd,
  input  cmpCmd,
  input  incCmd,
  input  decCmd,
  output [3:0] aluOpcode
);

  or or_1 (aluOpcode[0], adcCmd, subCmd, orCmd, notCmd, asrCmd, cmpCmd, decCmd);
  or or_2 (aluOpcode[1], addCmd, subCmd, xorCmd, notCmd, shrCmd, cmpCmd);
  or or_3 (aluOpcode[2], andCmd, orCmd, xorCmd, notCmd, incCmd, decCmd);
  or or_4 (aluOpcode[3], shlCmd, asrCmd, shrCmd, cmpCmd, incCmd, decCmd);
endmodule

module TwoCycDel (
  input  EnIn,
  input  Clock,
  output EnOut
);

  wire clkdelay_1_out_2, clkdelay_2_out_2, d_ff_1_q, d_ff_2_q;

  ClkDelay clkdelay_1 (.in_1(Clock), .out_2(clkdelay_1_out_2));
  ClkDelay clkdelay_2 (.in_1(clkdelay_1_out_2), .out_2(clkdelay_2_out_2));
  D_Flip_Flop d_ff_1 (.D(EnIn), .clk(clkdelay_2_out_2), .Q(d_ff_1_q));  // open: Qn, preset, reset
  D_Flip_Flop d_ff_2 (.D(d_ff_1_q), .clk(clkdelay_2_out_2), .Q(d_ff_2_q));  // open: Qn, preset, reset
  or or_1 (EnOut, d_ff_2_q, EnIn, d_ff_1_q);
endmodule

module AddrReset (
  input  Reset,
  input  Clock,
  output R,
  output Load,
  output Step,
  output [23:0] Address
);

  wire d_ff_1_q;

  D_Flip_Flop d_ff_1 (.D(Reset), .clk(Clock), .Q(d_ff_1_q));  // open: Qn, preset, reset
  D_Flip_Flop d_ff_2 (.D(d_ff_1_q), .clk(Clock), .Q(Step));  // open: Qn, preset, reset
  or or_1 (Load, Step, Reset, d_ff_1_q);
  assign Address = Load ? 24'h400 : 24'bz;  // Controlled_Buffer controlled_buffer_1

  assign R = Reset;
endmodule

module IOD (
  input  IODSend,
  input  IODRead,
  input  [7:0] AddrBusIn,
  input  [7:0] DataBusIn,
  input  Clock,
  output [7:0] AddrBusOut,
  output [7:0] DataBusOut
);

  wire and_1_out, and_2_out, and_3_out, and_4_out, and_5_out, and_6_out, twocycdel_1_enout, twocycdel_2_enout;
  wire [7:0] register_1_q, register_2_q;

  and and_1 (and_1_out, AddrBusIn[0], AddrBusIn[1], ~AddrBusIn[2], ~AddrBusIn[3], ~AddrBusIn[4], AddrBusIn[5], ~AddrBusIn[6], AddrBusIn[7]);  // AND_Gate
  and and_2 (and_2_out, ~AddrBusIn[0], AddrBusIn[1], ~AddrBusIn[2], ~AddrBusIn[3], AddrBusIn[4], AddrBusIn[5], AddrBusIn[6], ~AddrBusIn[7]);  // AND_Gate
  Register #(.trigger("high")) register_1 (.D(DataBusIn), .en(and_3_out), .clk(Clock), .Q(register_1_q));  // open: clr
  and and_3 (and_3_out, IODSend, and_1_out);
  Register #(.trigger("high")) register_2 (.D(DataBusIn), .en(and_4_out), .clk(Clock), .Q(register_2_q));  // open: clr
  and and_4 (and_4_out, IODSend, and_2_out);
  and and_5 (and_5_out, IODRead, and_1_out);
  and and_6 (and_6_out, IODRead, and_2_out);
  TwoCycDel twocycdel_1 (.EnIn(and_5_out), .Clock(Clock), .EnOut(twocycdel_1_enout));
  TwoCycDel twocycdel_2 (.EnIn(and_6_out), .Clock(Clock), .EnOut(twocycdel_2_enout));
  assign DataBusOut = twocycdel_1_enout ? register_1_q : 8'bz;  // Controlled_Buffer controlled_buffer_1
  assign DataBusOut = twocycdel_2_enout ? register_2_q : 8'bz;  // Controlled_Buffer controlled_buffer_2
endmodule

module test (
  input  En,
  input  RW,
  input  Clock,
  input  [2:0] RgSel,
  input  [7:0] DataBusIn,
  output [7:0] DataBusOut
);

  wire A0, A1, A2, A3, A4, A5, A6, A7, B0, B1, B2, B3, B4, B5, B6, B7, Buf1En, Buf2En, Buf3En, Buf4En, C0,
       C1, C2, C3, C4, C5, C6, C7, D0, D1, D2, D3, D4, D5, D6, D7, I0, I1, I2, I3, I4, I5, I6, I7, J0, J1,
       J2, J3, J4, J5, J6, J7, Mul12, Mul12En, Mul12EnN, Mul12Out0, Mul12Out1, Mul12Out2, Mul12Out3,
       Mul12Out4, Mul12Out5, Mul12Out6, Mul12Out7, Mul34, Mul34En, Mul34EnN, Mul34Out0, Mul34Out1, Mul34Out2,
       Mul34Out3, Mul34Out4, Mul34Out5, Mul34Out6, Mul34Out7, Mul56, Mul56En, Mul56EnN, Mul56Out0, Mul56Out1,
       Mul56Out2, Mul56Out3, Mul56Out4, Mul56Out5, Mul56Out6, Mul56Out7, Mul78, Mul78En, Mul78EnN, Mul78Out0,
       Mul78Out1, Mul78Out2, Mul78Out3, Mul78Out4, Mul78Out5, Mul78Out6, Mul78Out7, n74139_1_pin1, ReadCmd,
       WriteA, WriteB, WriteC, WriteD, WriteI, WriteJ, WriteX, WriteY, X0, X1, X2, X3, X4, X5, X6, X7, Y0,
       Y1, Y2, Y3, Y4, Y5, Y6, Y7;

  _74377 u_74377_1 (
    .pin1(WriteA), .pin2(A0), .pin3(DataBusIn[0]), .pin4(DataBusIn[1]), .pin5(A1), .pin6(A2),
    .pin7(DataBusIn[2]), .pin8(DataBusIn[3]), .pin9(A3), .pin19(A7), .pin18(DataBusIn[7]),
    .pin17(DataBusIn[6]), .pin16(A6), .pin15(A5), .pin14(DataBusIn[5]), .pin13(DataBusIn[4]), .pin12(A4),
    .pin11(Clock));
  _74157 u_74157_1 (
    .pin1(RgSel[0]), .pin2(A0), .pin3(B0), .pin4(Mul12Out0), .pin5(A1), .pin6(B1), .pin7(Mul12Out1),
    .pin15(Mul12En), .pin14(A3), .pin13(B3), .pin12(Mul12Out3), .pin11(A2), .pin10(B2), .pin9(Mul12Out2));
  _74157 u_74157_2 (
    .pin1(RgSel[0]), .pin2(A4), .pin3(B4), .pin4(Mul12Out4), .pin5(A5), .pin6(B5), .pin7(Mul12Out5),
    .pin15(Mul12En), .pin14(A7), .pin13(B7), .pin12(Mul12Out7), .pin11(A6), .pin10(B6), .pin9(Mul12Out6));
  _74377 u_74377_2 (
    .pin1(WriteB), .pin2(B0), .pin3(DataBusIn[0]), .pin4(DataBusIn[1]), .pin5(B1), .pin6(B2),
    .pin7(DataBusIn[2]), .pin8(DataBusIn[3]), .pin9(B3), .pin19(B7), .pin18(DataBusIn[7]),
    .pin17(DataBusIn[6]), .pin16(B6), .pin15(B5), .pin14(DataBusIn[5]), .pin13(DataBusIn[4]), .pin12(B4),
    .pin11(Clock));
  _74157 u_74157_3 (
    .pin1(RgSel[0]), .pin2(C0), .pin3(D0), .pin4(Mul34Out0), .pin5(C1), .pin6(D1), .pin7(Mul34Out1),
    .pin15(Mul34En), .pin14(C3), .pin13(D3), .pin12(Mul34Out3), .pin11(C2), .pin10(D2), .pin9(Mul34Out2));
  _74157 u_74157_4 (
    .pin1(RgSel[0]), .pin2(C4), .pin3(D4), .pin4(Mul34Out4), .pin5(C5), .pin6(D5), .pin7(Mul34Out5),
    .pin15(Mul34En), .pin14(C7), .pin13(D7), .pin12(Mul34Out7), .pin11(C6), .pin10(D6), .pin9(Mul34Out6));
  _74377 u_74377_3 (
    .pin1(WriteC), .pin2(C0), .pin3(DataBusIn[0]), .pin4(DataBusIn[1]), .pin5(C1), .pin6(C2),
    .pin7(DataBusIn[2]), .pin8(DataBusIn[3]), .pin9(C3), .pin19(C7), .pin18(DataBusIn[7]),
    .pin17(DataBusIn[6]), .pin16(C6), .pin15(C5), .pin14(DataBusIn[5]), .pin13(DataBusIn[4]), .pin12(C4),
    .pin11(Clock));
  _74157 u_74157_5 (
    .pin1(RgSel[0]), .pin2(I0), .pin3(J0), .pin4(Mul56Out0), .pin5(I1), .pin6(J1), .pin7(Mul56Out1),
    .pin15(Mul56En), .pin14(I3), .pin13(J3), .pin12(Mul56Out3), .pin11(I2), .pin10(J2), .pin9(Mul56Out2));
  _74157 u_74157_6 (
    .pin1(RgSel[0]), .pin2(I4), .pin3(J4), .pin4(Mul56Out4), .pin5(I5), .pin6(J5), .pin7(Mul56Out5),
    .pin15(Mul56En), .pin14(I7), .pin13(J7), .pin12(Mul56Out7), .pin11(I6), .pin10(J6), .pin9(Mul56Out6));
  _74377 u_74377_4 (
    .pin1(WriteD), .pin2(D0), .pin3(DataBusIn[0]), .pin4(DataBusIn[1]), .pin5(D1), .pin6(D2),
    .pin7(DataBusIn[2]), .pin8(DataBusIn[3]), .pin9(D3), .pin19(D7), .pin18(DataBusIn[7]),
    .pin17(DataBusIn[6]), .pin16(D6), .pin15(D5), .pin14(DataBusIn[5]), .pin13(DataBusIn[4]), .pin12(D4),
    .pin11(Clock));
  _74157 u_74157_7 (
    .pin1(RgSel[0]), .pin2(X0), .pin3(Y0), .pin4(Mul78Out0), .pin5(X1), .pin6(Y1), .pin7(Mul78Out1),
    .pin15(Mul78En), .pin14(X3), .pin13(Y3), .pin12(Mul78Out3), .pin11(X2), .pin10(Y2), .pin9(Mul78Out2));
  _74157 u_74157_8 (
    .pin1(RgSel[0]), .pin2(X4), .pin3(Y4), .pin4(Mul78Out4), .pin5(X5), .pin6(Y5), .pin7(Mul78Out5),
    .pin15(Mul78En), .pin14(X7), .pin13(Y7), .pin12(Mul78Out7), .pin11(X6), .pin10(Y6), .pin9(Mul78Out6));
  _74377 u_74377_5 (
    .pin1(WriteI), .pin2(I0), .pin3(DataBusIn[0]), .pin4(DataBusIn[1]), .pin5(I1), .pin6(I2),
    .pin7(DataBusIn[2]), .pin8(DataBusIn[3]), .pin9(I3), .pin19(I7), .pin18(DataBusIn[7]),
    .pin17(DataBusIn[6]), .pin16(I6), .pin15(I5), .pin14(DataBusIn[5]), .pin13(DataBusIn[4]), .pin12(I4),
    .pin11(Clock));
  _74244 u_74244_1 (
    .pin1(Buf1En), .pin2(Mul12Out0), .pin3(DataBusOut[7]), .pin4(Mul12Out1), .pin5(DataBusOut[6]),
    .pin6(Mul12Out2), .pin7(DataBusOut[5]), .pin8(Mul12Out3), .pin9(DataBusOut[4]), .pin19(Buf1En),
    .pin18(DataBusOut[0]), .pin17(Mul12Out7), .pin16(DataBusOut[1]), .pin15(Mul12Out6),
    .pin14(DataBusOut[2]), .pin13(Mul12Out5), .pin12(DataBusOut[3]), .pin11(Mul12Out4));
  _74244 u_74244_2 (
    .pin1(Buf2En), .pin2(Mul34Out0), .pin3(DataBusOut[7]), .pin4(Mul34Out1), .pin5(DataBusOut[6]),
    .pin6(Mul34Out2), .pin7(DataBusOut[5]), .pin8(Mul34Out3), .pin9(DataBusOut[4]), .pin19(Buf2En),
    .pin18(DataBusOut[0]), .pin17(Mul34Out7), .pin16(DataBusOut[1]), .pin15(Mul34Out6),
    .pin14(DataBusOut[2]), .pin13(Mul34Out5), .pin12(DataBusOut[3]), .pin11(Mul34Out4));
  _74377 u_74377_6 (
    .pin1(WriteJ), .pin2(J0), .pin3(DataBusIn[0]), .pin4(DataBusIn[1]), .pin5(J1), .pin6(J2),
    .pin7(DataBusIn[2]), .pin8(DataBusIn[3]), .pin9(J3), .pin19(J7), .pin18(DataBusIn[7]),
    .pin17(DataBusIn[6]), .pin16(J6), .pin15(J5), .pin14(DataBusIn[5]), .pin13(DataBusIn[4]), .pin12(J4),
    .pin11(Clock));
  _74244 u_74244_3 (
    .pin1(Buf3En), .pin2(Mul56Out0), .pin3(DataBusOut[7]), .pin4(Mul56Out1), .pin5(DataBusOut[6]),
    .pin6(Mul56Out2), .pin7(DataBusOut[5]), .pin8(Mul56Out3), .pin9(DataBusOut[4]), .pin19(Buf3En),
    .pin18(DataBusOut[0]), .pin17(Mul56Out7), .pin16(DataBusOut[1]), .pin15(Mul56Out6),
    .pin14(DataBusOut[2]), .pin13(Mul56Out5), .pin12(DataBusOut[3]), .pin11(Mul56Out4));
  _74244 u_74244_4 (
    .pin1(Buf4En), .pin2(Mul78Out0), .pin3(DataBusOut[7]), .pin4(Mul78Out1), .pin5(DataBusOut[6]),
    .pin6(Mul78Out2), .pin7(DataBusOut[5]), .pin8(Mul78Out3), .pin9(DataBusOut[4]), .pin19(Buf4En),
    .pin18(DataBusOut[0]), .pin17(Mul78Out7), .pin16(DataBusOut[1]), .pin15(Mul78Out6),
    .pin14(DataBusOut[2]), .pin13(Mul78Out5), .pin12(DataBusOut[3]), .pin11(Mul78Out4));
  _74377 u_74377_7 (
    .pin1(WriteX), .pin2(X0), .pin3(DataBusIn[0]), .pin4(DataBusIn[1]), .pin5(X1), .pin6(X2),
    .pin7(DataBusIn[2]), .pin8(DataBusIn[3]), .pin9(X3), .pin19(X7), .pin18(DataBusIn[7]),
    .pin17(DataBusIn[6]), .pin16(X6), .pin15(X5), .pin14(DataBusIn[5]), .pin13(DataBusIn[4]), .pin12(X4),
    .pin11(Clock));
  _74139 u_74139_1 (
    .pin1(n74139_1_pin1), .pin2(RgSel[1]), .pin3(RgSel[2]), .pin4(Mul12), .pin5(Mul34), .pin6(Mul56),
    .pin7(Mul78));  // open: pin15, pin14, pin13, pin12, pin11, pin10, pin9
  _74138 u_74138_1 (
    .pin1(RgSel[0]), .pin2(RgSel[1]), .pin3(RgSel[2]), .pin4(ReadCmd), .pin5(ReadCmd), .pin6(En),
    .pin7(WriteY), .pin15(WriteA), .pin14(WriteB), .pin13(WriteC), .pin12(WriteD), .pin11(WriteI),
    .pin10(WriteJ), .pin9(WriteX));
  _74377 u_74377_8 (
    .pin1(WriteY), .pin2(Y0), .pin3(DataBusIn[0]), .pin4(DataBusIn[1]), .pin5(Y1), .pin6(Y2),
    .pin7(DataBusIn[2]), .pin8(DataBusIn[3]), .pin9(Y3), .pin19(Y7), .pin18(DataBusIn[7]),
    .pin17(DataBusIn[6]), .pin16(Y6), .pin15(Y5), .pin14(DataBusIn[5]), .pin13(DataBusIn[4]), .pin12(Y4),
    .pin11(Clock));
  _7432 u_7432_1 (
    .pin1(Mul12), .pin2(RW), .pin3(Mul12En), .pin4(Mul34), .pin5(RW), .pin6(Mul34En), .pin13(Mul78),
    .pin12(RW), .pin11(Mul78En), .pin10(Mul56), .pin9(RW), .pin8(Mul56En));
  _7400 u_7400_1 (
    .pin1(Mul12EnN), .pin2(En), .pin3(Buf1En), .pin4(Mul34EnN), .pin5(En), .pin6(Buf2En), .pin13(Mul78EnN),
    .pin12(En), .pin11(Buf4En), .pin10(Mul56EnN), .pin9(En), .pin8(Buf3En));
  _7404 u_7404_1 (
    .pin1(RW), .pin2(ReadCmd), .pin3(Mul12En), .pin4(Mul12EnN), .pin5(Mul34En), .pin6(Mul34EnN),
    .pin13(Mul78En), .pin12(Mul78EnN), .pin11(Mul56En), .pin10(Mul56EnN));  // open: pin9, pin8
  // also tied to GND on the sheet: n74139_1_pin1

  // Other names for the same wires on the sheet: dIN0 = DataBusIn[0]; dIN1 = DataBusIn[1]; dIN2 = DataBusIn[2];
  //   dIN3 = DataBusIn[3]; dIN4 = DataBusIn[4]; dIN5 = DataBusIn[5]; dIN6 = DataBusIn[6]; dIN7 = DataBusIn[7];
  //   out0 = DataBusOut[0]; out1 = DataBusOut[1]; out2 = DataBusOut[2]; out3 = DataBusOut[3]; out4 = DataBusOut[4];
  //   out5 = DataBusOut[5]; out6 = DataBusOut[6]; out7 = DataBusOut[7]; WriteCmd = RW

  // Notes on the sheet:
  //   A
  //   Mul1
  //   Mul2
  //   B
  //   Mul3
  //   Mul4
  //   C
  //   Mul5
  //   Mul6
  //   D
  //   Mul7
  //   Mul8
  //   I
  //   Buffer1
  //   Buffer2
  //   J
  //   Buffer3
  //   Buffer4
  //   X
  //   2-4 Decoder
  //   3-8 Decoder
  //   Y
  //   Quad OR
endmodule
