// Logisim project add8_ttl.circ as structural Verilog: 1 circuit, main circuit add8
module add8 (
  input  [7:0] A,
  input  [7:0] B,
  input  Cin,
  output [7:0] S,
  output Cout
);

  wire U2_pin7;

  _74283 U2 (
    .pin1(S[5]), .pin2(B[5]), .pin3(A[5]), .pin4(S[4]), .pin5(A[4]), .pin6(B[4]), .pin7(U2_pin7),
    .pin15(B[6]), .pin14(A[6]), .pin13(S[6]), .pin12(A[7]), .pin11(B[7]), .pin10(S[7]), .pin9(Cout));
  _74283 U1 (
    .pin1(S[1]), .pin2(B[1]), .pin3(A[1]), .pin4(S[0]), .pin5(A[0]), .pin6(B[0]), .pin7(Cin), .pin15(B[2]),
    .pin14(A[2]), .pin13(S[2]), .pin12(A[3]), .pin11(B[3]), .pin10(S[3]), .pin9(U2_pin7));

  // Notes on the sheet:
  //   bits 7..4
  //   bits 3..0
endmodule
