// Logisim project add_sub8.circ as structural Verilog: 1 circuit, main circuit add_sub8
module add_sub8 (
  input  add_sub8_sub,
  input  add_sub8_usec,
  input  add_sub8_cin,
  input  [7:0] add_sub8_a,
  input  [7:0] add_sub8_b,
  output add_sub8_c,
  output [7:0] add_sub8_s
);

  wire U1_pin3, U1_pin4, U1_pin13, U2_pin4, U2_pin10, U3_pin7, U3_pin9, U4_pin9;
  wire [7:0] U5_pin11;

  _7486 U5 (
    .pin1(add_sub8_b[3]), .pin2(add_sub8_sub), .pin3(U5_pin11[3]), .pin4(add_sub8_sub), .pin5(add_sub8_b[2]),
    .pin6(U5_pin11[2]), .pin13(add_sub8_b[0]), .pin12(add_sub8_sub), .pin11(U5_pin11[0]),
    .pin10(add_sub8_sub), .pin9(add_sub8_b[1]), .pin8(U5_pin11[1]));
  _7486 U6 (
    .pin1(add_sub8_b[7]), .pin2(add_sub8_sub), .pin3(U5_pin11[7]), .pin4(add_sub8_sub), .pin5(add_sub8_b[6]),
    .pin6(U5_pin11[6]), .pin13(add_sub8_b[4]), .pin12(add_sub8_sub), .pin11(U5_pin11[4]),
    .pin10(add_sub8_sub), .pin9(add_sub8_b[5]), .pin8(U5_pin11[5]));
  _7408 U1 (
    .pin1(add_sub8_usec), .pin2(add_sub8_cin), .pin3(U1_pin3), .pin4(U1_pin4), .pin5(U1_pin4),
    .pin13(U1_pin13), .pin12(U1_pin13), .pin10(U1_pin13), .pin9(U1_pin13));  // open: pin6, pin11, pin8
  _74283 U3 (
    .pin1(add_sub8_s[1]), .pin2(U5_pin11[1]), .pin3(add_sub8_a[1]), .pin4(add_sub8_s[0]),
    .pin5(add_sub8_a[0]), .pin6(U5_pin11[0]), .pin7(U3_pin7), .pin15(U5_pin11[2]), .pin14(add_sub8_a[2]),
    .pin13(add_sub8_s[2]), .pin12(add_sub8_a[3]), .pin11(U5_pin11[3]), .pin10(add_sub8_s[3]), .pin9(U3_pin9));
  _74283 U4 (
    .pin1(add_sub8_s[5]), .pin2(U5_pin11[5]), .pin3(add_sub8_a[5]), .pin4(add_sub8_s[4]),
    .pin5(add_sub8_a[4]), .pin6(U5_pin11[4]), .pin7(U3_pin9), .pin15(U5_pin11[6]), .pin14(add_sub8_a[6]),
    .pin13(add_sub8_s[6]), .pin12(add_sub8_a[7]), .pin11(U5_pin11[7]), .pin10(add_sub8_s[7]), .pin9(U4_pin9));
  _7486 U2 (
    .pin1(add_sub8_sub), .pin2(U4_pin9), .pin3(add_sub8_c), .pin4(U2_pin4), .pin5(U2_pin4),
    .pin13(add_sub8_sub), .pin12(U1_pin3), .pin11(U3_pin7), .pin10(U2_pin10), .pin9(U2_pin10));  // open: pin6, pin8
  // also tied to GND on the sheet: {U1_pin13, U1_pin4, U2_pin10, U2_pin4}

  // Notes on the sheet:
  //   U6: B inversion, bits 7..4
  //   U5: B inversion, bits 3..0
  //   U1: carry in enable = usec AND cin
  //   U2: carry/borrow inversion for SUB
endmodule
