// Logisim project addr.circ as structural Verilog: 1 circuit, main circuit addr
module addr (
  input  clk,
  input  rst_n,
  input  [1:0] addr_base_sel,
  input  [1:0] addr_base_oe_n,
  input  addr_off_sel,
  input  [1:0] addr_off_oe_n,
  input  addr_inv,
  input  addr_cin,
  input  addr_lat_ld_n,
  input  addr_pc_ld_n,
  input  addr_sp_ld_n,
  input  [1:0] addr_lat_oe_n,
  input  [1:0] addr_pc_oe_n,
  input  [1:0] addr_sp_oe_n,
  input  [7:0] addr_bus_a,
  input  [7:0] addr_bus_b,
  input  [7:0] addr_v1,
  input  [7:0] addr_v2,
  input  [7:0] addr_bus_addr_lo_in,
  output [7:0] addr_bus_addr_hi,
  output [7:0] addr_bus_addr_lo,
  output [7:0] addr_bus_out,
  output addr_cout
);

  wire addr_base_0, addr_base_1, addr_base_2, addr_base_3, addr_base_4, addr_base_5, addr_base_6,
       addr_base_7, addr_base_8, addr_base_9, addr_base_10, addr_base_11, addr_base_12, addr_base_13,
       addr_base_14, addr_base_15, addr_c4_0, addr_c4_1, addr_c4_2, addr_ivt_8, addr_lat_0, addr_lat_1,
       addr_lat_2, addr_lat_3, addr_lat_4, addr_lat_5, addr_lat_6, addr_lat_7, addr_lat_8, addr_lat_9,
       addr_lat_10, addr_lat_11, addr_lat_12, addr_lat_13, addr_lat_14, addr_lat_15, addr_off_0, addr_off_1,
       addr_off_2, addr_off_3, addr_off_4, addr_off_5, addr_off_6, addr_off_7, addr_off_8, addr_off_9,
       addr_off_10, addr_off_11, addr_off_12, addr_off_13, addr_off_14, addr_off_15, addr_offx_0,
       addr_offx_1, addr_offx_2, addr_offx_3, addr_offx_4, addr_offx_5, addr_offx_6, addr_offx_7,
       addr_offx_8, addr_offx_9, addr_offx_10, addr_offx_11, addr_offx_12, addr_offx_13, addr_offx_14,
       addr_offx_15, addr_pc_0, addr_pc_1, addr_pc_2, addr_pc_3, addr_pc_4, addr_pc_5, addr_pc_6, addr_pc_7,
       addr_pc_8, addr_pc_9, addr_pc_10, addr_pc_11, addr_pc_12, addr_pc_13, addr_pc_14, addr_pc_15,
       addr_pc_d_9, addr_pc_d_10, addr_pc_d_11, addr_pc_d_12, addr_pc_d_13, addr_pc_d_14, addr_pc_d_15,
       addr_sp_0, addr_sp_1, addr_sp_2, addr_sp_3, addr_sp_4, addr_sp_5, addr_sp_6, addr_sp_7, addr_sp_8,
       addr_sp_9, addr_sp_10, addr_sp_11, addr_sp_12, addr_sp_13, addr_sp_14, addr_sp_15, addr_sum_0,
       addr_sum_1, addr_sum_2, addr_sum_3, addr_sum_4, addr_sum_5, addr_sum_6, addr_sum_7, addr_sum_8,
       addr_sum_9, addr_sum_10, addr_sum_11, addr_sum_12, addr_sum_13, addr_sum_14, addr_sum_15, U1_pin3,
       U2_pin13, U6_pin19, U8_pin3, U8_pin13, U12_pin19, U14_pin3, U14_pin13, U18_pin19, U20_pin3, U20_pin13,
       U24_pin19, U26_pin1, U26_pin3, U26_pin6, U26_pin10, U26_pin13, U29_pin19, U31_pin1, U31_pin3,
       U31_pin6, U31_pin10, U31_pin13, U34_pin19;

  _74153 U1 (
    .pin1(addr_base_oe_n[0]), .pin2(addr_base_sel[1]), .pin3(U1_pin3), .pin4(addr_bus_b[0]),
    .pin5(addr_sp_0), .pin6(addr_pc_0), .pin7(addr_base_0), .pin15(addr_base_oe_n[0]),
    .pin14(addr_base_sel[0]), .pin13(addr_bus_addr_lo_in[0]), .pin12(addr_bus_b[1]), .pin11(addr_sp_1),
    .pin10(addr_pc_1), .pin9(addr_base_1));
  _74153 U7 (
    .pin1(addr_base_oe_n[0]), .pin2(addr_base_sel[1]), .pin3(addr_bus_addr_lo_in[1]), .pin4(addr_bus_b[2]),
    .pin5(addr_sp_2), .pin6(addr_pc_2), .pin7(addr_base_2), .pin15(addr_base_oe_n[0]),
    .pin14(addr_base_sel[0]), .pin13(addr_bus_addr_lo_in[2]), .pin12(addr_bus_b[3]), .pin11(addr_sp_3),
    .pin10(addr_pc_3), .pin9(addr_base_3));
  _74153 U13 (
    .pin1(addr_base_oe_n[0]), .pin2(addr_base_sel[1]), .pin3(addr_bus_addr_lo_in[3]), .pin4(addr_bus_b[4]),
    .pin5(addr_sp_4), .pin6(addr_pc_4), .pin7(addr_base_4), .pin15(addr_base_oe_n[0]),
    .pin14(addr_base_sel[0]), .pin13(addr_bus_addr_lo_in[4]), .pin12(addr_bus_b[5]), .pin11(addr_sp_5),
    .pin10(addr_pc_5), .pin9(addr_base_5));
  _74153 U19 (
    .pin1(addr_base_oe_n[0]), .pin2(addr_base_sel[1]), .pin3(addr_bus_addr_lo_in[5]), .pin4(addr_bus_b[6]),
    .pin5(addr_sp_6), .pin6(addr_pc_6), .pin7(addr_base_6), .pin15(addr_base_oe_n[0]),
    .pin14(addr_base_sel[0]), .pin13(addr_bus_addr_lo_in[6]), .pin12(addr_bus_b[7]), .pin11(addr_sp_7),
    .pin10(addr_pc_7), .pin9(addr_base_7));
  _74157 U25 (
    .pin1(addr_off_sel), .pin2(addr_v2[0]), .pin3(addr_v1[0]), .pin4(addr_off_0), .pin5(addr_v2[1]),
    .pin6(addr_v1[1]), .pin7(addr_off_1), .pin15(addr_off_oe_n[0]), .pin14(addr_v2[3]), .pin13(addr_v1[3]),
    .pin12(addr_off_3), .pin11(addr_v2[2]), .pin10(addr_v1[2]), .pin9(addr_off_2));
  _74157 U30 (
    .pin1(addr_off_sel), .pin2(addr_v2[4]), .pin3(addr_v1[4]), .pin4(addr_off_4), .pin5(addr_v2[5]),
    .pin6(addr_v1[5]), .pin7(addr_off_5), .pin15(addr_off_oe_n[0]), .pin14(addr_v2[7]), .pin13(addr_v1[7]),
    .pin12(addr_off_7), .pin11(addr_v2[6]), .pin10(addr_v1[6]), .pin9(addr_off_6));
  _74153 U2 (
    .pin1(addr_base_oe_n[1]), .pin2(addr_base_sel[1]), .pin3(addr_ivt_8), .pin4(addr_bus_a[0]),
    .pin5(addr_sp_8), .pin6(addr_pc_8), .pin7(addr_base_8), .pin15(addr_base_oe_n[1]),
    .pin14(addr_base_sel[0]), .pin13(U2_pin13), .pin12(addr_bus_a[1]), .pin11(addr_sp_9), .pin10(addr_pc_9),
    .pin9(addr_base_9));
  _74153 U8 (
    .pin1(addr_base_oe_n[1]), .pin2(addr_base_sel[1]), .pin3(U8_pin3), .pin4(addr_bus_a[2]),
    .pin5(addr_sp_10), .pin6(addr_pc_10), .pin7(addr_base_10), .pin15(addr_base_oe_n[1]),
    .pin14(addr_base_sel[0]), .pin13(U8_pin13), .pin12(addr_bus_a[3]), .pin11(addr_sp_11),
    .pin10(addr_pc_11), .pin9(addr_base_11));
  _74153 U14 (
    .pin1(addr_base_oe_n[1]), .pin2(addr_base_sel[1]), .pin3(U14_pin3), .pin4(addr_bus_a[4]),
    .pin5(addr_sp_12), .pin6(addr_pc_12), .pin7(addr_base_12), .pin15(addr_base_oe_n[1]),
    .pin14(addr_base_sel[0]), .pin13(U14_pin13), .pin12(addr_bus_a[5]), .pin11(addr_sp_13),
    .pin10(addr_pc_13), .pin9(addr_base_13));
  _74153 U20 (
    .pin1(addr_base_oe_n[1]), .pin2(addr_base_sel[1]), .pin3(U20_pin3), .pin4(addr_bus_a[6]),
    .pin5(addr_sp_14), .pin6(addr_pc_14), .pin7(addr_base_14), .pin15(addr_base_oe_n[1]),
    .pin14(addr_base_sel[0]), .pin13(U20_pin13), .pin12(addr_bus_a[7]), .pin11(addr_sp_15),
    .pin10(addr_pc_15), .pin9(addr_base_15));
  _74157 U26 (
    .pin1(U26_pin1), .pin2(addr_v1[0]), .pin3(U26_pin3), .pin4(addr_off_8), .pin5(addr_v1[1]),
    .pin6(U26_pin6), .pin7(addr_off_9), .pin15(addr_off_oe_n[1]), .pin14(addr_v1[3]), .pin13(U26_pin13),
    .pin12(addr_off_11), .pin11(addr_v1[2]), .pin10(U26_pin10), .pin9(addr_off_10));
  _74157 U31 (
    .pin1(U31_pin1), .pin2(addr_v1[4]), .pin3(U31_pin3), .pin4(addr_off_12), .pin5(addr_v1[5]),
    .pin6(U31_pin6), .pin7(addr_off_13), .pin15(addr_off_oe_n[1]), .pin14(addr_v1[7]), .pin13(U31_pin13),
    .pin12(addr_off_15), .pin11(addr_v1[6]), .pin10(U31_pin10), .pin9(addr_off_14));
  _7486 U3 (
    .pin1(addr_off_0), .pin2(addr_inv), .pin3(addr_offx_0), .pin4(addr_off_1), .pin5(addr_inv),
    .pin6(addr_offx_1), .pin13(addr_inv), .pin12(addr_off_3), .pin11(addr_offx_3), .pin10(addr_inv),
    .pin9(addr_off_2), .pin8(addr_offx_2));
  _7486 U9 (
    .pin1(addr_off_4), .pin2(addr_inv), .pin3(addr_offx_4), .pin4(addr_off_5), .pin5(addr_inv),
    .pin6(addr_offx_5), .pin13(addr_inv), .pin12(addr_off_7), .pin11(addr_offx_7), .pin10(addr_inv),
    .pin9(addr_off_6), .pin8(addr_offx_6));
  _7486 U15 (
    .pin1(addr_off_8), .pin2(addr_inv), .pin3(addr_offx_8), .pin4(addr_off_9), .pin5(addr_inv),
    .pin6(addr_offx_9), .pin13(addr_inv), .pin12(addr_off_11), .pin11(addr_offx_11), .pin10(addr_inv),
    .pin9(addr_off_10), .pin8(addr_offx_10));
  _7486 U21 (
    .pin1(addr_off_12), .pin2(addr_inv), .pin3(addr_offx_12), .pin4(addr_off_13), .pin5(addr_inv),
    .pin6(addr_offx_13), .pin13(addr_inv), .pin12(addr_off_15), .pin11(addr_offx_15), .pin10(addr_inv),
    .pin9(addr_off_14), .pin8(addr_offx_14));
  _7408 U27 (
    .pin1(addr_sum_9), .pin2(rst_n), .pin3(addr_pc_d_9), .pin4(addr_sum_10), .pin5(rst_n),
    .pin6(addr_pc_d_10), .pin13(rst_n), .pin12(addr_sum_12), .pin11(addr_pc_d_12), .pin10(rst_n),
    .pin9(addr_sum_11), .pin8(addr_pc_d_11));
  _7408 U32 (
    .pin1(addr_sum_13), .pin2(rst_n), .pin3(addr_pc_d_13), .pin4(addr_sum_14), .pin5(rst_n),
    .pin6(addr_pc_d_14), .pin13(rst_n), .pin12(addr_bus_addr_lo_in[7]), .pin11(addr_ivt_8), .pin10(rst_n),
    .pin9(addr_sum_15), .pin8(addr_pc_d_15));
  _74283 U4 (
    .pin1(addr_sum_1), .pin2(addr_offx_1), .pin3(addr_base_1), .pin4(addr_sum_0), .pin5(addr_base_0),
    .pin6(addr_offx_0), .pin7(addr_cin), .pin15(addr_offx_2), .pin14(addr_base_2), .pin13(addr_sum_2),
    .pin12(addr_base_3), .pin11(addr_offx_3), .pin10(addr_sum_3), .pin9(addr_c4_0));
  _74283 U10 (
    .pin1(addr_sum_5), .pin2(addr_offx_5), .pin3(addr_base_5), .pin4(addr_sum_4), .pin5(addr_base_4),
    .pin6(addr_offx_4), .pin7(addr_c4_0), .pin15(addr_offx_6), .pin14(addr_base_6), .pin13(addr_sum_6),
    .pin12(addr_base_7), .pin11(addr_offx_7), .pin10(addr_sum_7), .pin9(addr_c4_1));
  _74283 U16 (
    .pin1(addr_sum_9), .pin2(addr_offx_9), .pin3(addr_base_9), .pin4(addr_sum_8), .pin5(addr_base_8),
    .pin6(addr_offx_8), .pin7(addr_c4_1), .pin15(addr_offx_10), .pin14(addr_base_10), .pin13(addr_sum_10),
    .pin12(addr_base_11), .pin11(addr_offx_11), .pin10(addr_sum_11), .pin9(addr_c4_2));
  _74283 U22 (
    .pin1(addr_sum_13), .pin2(addr_offx_13), .pin3(addr_base_13), .pin4(addr_sum_12), .pin5(addr_base_12),
    .pin6(addr_offx_12), .pin7(addr_c4_2), .pin15(addr_offx_14), .pin14(addr_base_14), .pin13(addr_sum_14),
    .pin12(addr_base_15), .pin11(addr_offx_15), .pin10(addr_sum_15), .pin9(addr_cout));
  _74377 U5 (
    .pin1(addr_lat_ld_n), .pin2(addr_lat_8), .pin3(addr_sum_8), .pin4(addr_sum_9), .pin5(addr_lat_9),
    .pin6(addr_lat_10), .pin7(addr_sum_10), .pin8(addr_sum_11), .pin9(addr_lat_11), .pin19(addr_lat_15),
    .pin18(addr_sum_15), .pin17(addr_sum_14), .pin16(addr_lat_14), .pin15(addr_lat_13), .pin14(addr_sum_13),
    .pin13(addr_sum_12), .pin12(addr_lat_12), .pin11(clk));
  _74377 U11 (
    .pin1(addr_lat_ld_n), .pin2(addr_lat_0), .pin3(addr_sum_0), .pin4(addr_sum_1), .pin5(addr_lat_1),
    .pin6(addr_lat_2), .pin7(addr_sum_2), .pin8(addr_sum_3), .pin9(addr_lat_3), .pin19(addr_lat_7),
    .pin18(addr_sum_7), .pin17(addr_sum_6), .pin16(addr_lat_6), .pin15(addr_lat_5), .pin14(addr_sum_5),
    .pin13(addr_sum_4), .pin12(addr_lat_4), .pin11(clk));
  _74377 U17 (
    .pin1(addr_pc_ld_n), .pin2(addr_pc_8), .pin3(addr_sum_8), .pin4(addr_pc_d_9), .pin5(addr_pc_9),
    .pin6(addr_pc_10), .pin7(addr_pc_d_10), .pin8(addr_pc_d_11), .pin9(addr_pc_11), .pin19(addr_pc_15),
    .pin18(addr_pc_d_15), .pin17(addr_pc_d_14), .pin16(addr_pc_14), .pin15(addr_pc_13), .pin14(addr_pc_d_13),
    .pin13(addr_pc_d_12), .pin12(addr_pc_12), .pin11(clk));
  _74377 U23 (
    .pin1(addr_pc_ld_n), .pin2(addr_pc_0), .pin3(addr_sum_0), .pin4(addr_sum_1), .pin5(addr_pc_1),
    .pin6(addr_pc_2), .pin7(addr_sum_2), .pin8(addr_sum_3), .pin9(addr_pc_3), .pin19(addr_pc_7),
    .pin18(addr_sum_7), .pin17(addr_sum_6), .pin16(addr_pc_6), .pin15(addr_pc_5), .pin14(addr_sum_5),
    .pin13(addr_sum_4), .pin12(addr_pc_4), .pin11(clk));
  _74377 U28 (
    .pin1(addr_sp_ld_n), .pin2(addr_sp_8), .pin3(addr_sum_8), .pin4(addr_sum_9), .pin5(addr_sp_9),
    .pin6(addr_sp_10), .pin7(addr_sum_10), .pin8(addr_sum_11), .pin9(addr_sp_11), .pin19(addr_sp_15),
    .pin18(addr_sum_15), .pin17(addr_sum_14), .pin16(addr_sp_14), .pin15(addr_sp_13), .pin14(addr_sum_13),
    .pin13(addr_sum_12), .pin12(addr_sp_12), .pin11(clk));
  _74377 U33 (
    .pin1(addr_sp_ld_n), .pin2(addr_sp_0), .pin3(addr_sum_0), .pin4(addr_sum_1), .pin5(addr_sp_1),
    .pin6(addr_sp_2), .pin7(addr_sum_2), .pin8(addr_sum_3), .pin9(addr_sp_3), .pin19(addr_sp_7),
    .pin18(addr_sum_7), .pin17(addr_sum_6), .pin16(addr_sp_6), .pin15(addr_sp_5), .pin14(addr_sum_5),
    .pin13(addr_sum_4), .pin12(addr_sp_4), .pin11(clk));
  _74541 U6 (
    .pin1(addr_lat_oe_n[1]), .pin2(addr_lat_8), .pin3(addr_lat_9), .pin4(addr_lat_10), .pin5(addr_lat_11),
    .pin6(addr_lat_12), .pin7(addr_lat_13), .pin8(addr_lat_14), .pin9(addr_lat_15), .pin19(U6_pin19),
    .pin18(addr_bus_addr_hi[0]), .pin17(addr_bus_addr_hi[1]), .pin16(addr_bus_addr_hi[2]),
    .pin15(addr_bus_addr_hi[3]), .pin14(addr_bus_addr_hi[4]), .pin13(addr_bus_addr_hi[5]),
    .pin12(addr_bus_addr_hi[6]), .pin11(addr_bus_addr_hi[7]));
  _74541 U12 (
    .pin1(addr_lat_oe_n[0]), .pin2(addr_lat_0), .pin3(addr_lat_1), .pin4(addr_lat_2), .pin5(addr_lat_3),
    .pin6(addr_lat_4), .pin7(addr_lat_5), .pin8(addr_lat_6), .pin9(addr_lat_7), .pin19(U12_pin19),
    .pin18(addr_bus_addr_lo[0]), .pin17(addr_bus_addr_lo[1]), .pin16(addr_bus_addr_lo[2]),
    .pin15(addr_bus_addr_lo[3]), .pin14(addr_bus_addr_lo[4]), .pin13(addr_bus_addr_lo[5]),
    .pin12(addr_bus_addr_lo[6]), .pin11(addr_bus_addr_lo[7]));
  _74541 U18 (
    .pin1(addr_pc_oe_n[1]), .pin2(addr_pc_8), .pin3(addr_pc_9), .pin4(addr_pc_10), .pin5(addr_pc_11),
    .pin6(addr_pc_12), .pin7(addr_pc_13), .pin8(addr_pc_14), .pin9(addr_pc_15), .pin19(U18_pin19),
    .pin18(addr_bus_out[0]), .pin17(addr_bus_out[1]), .pin16(addr_bus_out[2]), .pin15(addr_bus_out[3]),
    .pin14(addr_bus_out[4]), .pin13(addr_bus_out[5]), .pin12(addr_bus_out[6]), .pin11(addr_bus_out[7]));
  _74541 U24 (
    .pin1(addr_pc_oe_n[0]), .pin2(addr_pc_0), .pin3(addr_pc_1), .pin4(addr_pc_2), .pin5(addr_pc_3),
    .pin6(addr_pc_4), .pin7(addr_pc_5), .pin8(addr_pc_6), .pin9(addr_pc_7), .pin19(U24_pin19),
    .pin18(addr_bus_out[0]), .pin17(addr_bus_out[1]), .pin16(addr_bus_out[2]), .pin15(addr_bus_out[3]),
    .pin14(addr_bus_out[4]), .pin13(addr_bus_out[5]), .pin12(addr_bus_out[6]), .pin11(addr_bus_out[7]));
  _74541 U29 (
    .pin1(addr_sp_oe_n[1]), .pin2(addr_sp_8), .pin3(addr_sp_9), .pin4(addr_sp_10), .pin5(addr_sp_11),
    .pin6(addr_sp_12), .pin7(addr_sp_13), .pin8(addr_sp_14), .pin9(addr_sp_15), .pin19(U29_pin19),
    .pin18(addr_bus_out[0]), .pin17(addr_bus_out[1]), .pin16(addr_bus_out[2]), .pin15(addr_bus_out[3]),
    .pin14(addr_bus_out[4]), .pin13(addr_bus_out[5]), .pin12(addr_bus_out[6]), .pin11(addr_bus_out[7]));
  _74541 U34 (
    .pin1(addr_sp_oe_n[0]), .pin2(addr_sp_0), .pin3(addr_sp_1), .pin4(addr_sp_2), .pin5(addr_sp_3),
    .pin6(addr_sp_4), .pin7(addr_sp_5), .pin8(addr_sp_6), .pin9(addr_sp_7), .pin19(U34_pin19),
    .pin18(addr_bus_out[0]), .pin17(addr_bus_out[1]), .pin16(addr_bus_out[2]), .pin15(addr_bus_out[3]),
    .pin14(addr_bus_out[4]), .pin13(addr_bus_out[5]), .pin12(addr_bus_out[6]), .pin11(addr_bus_out[7]));
  // also tied to GND on the sheet: {U1_pin3, U26_pin1, U26_pin3, U26_pin6, U31_pin1, U31_pin3, U31_pin6, U26_pin13, U26_pin10, U31_pin13, U31_pin10, U6_pin19, U12_pin19, U18_pin19, U24_pin19, U29_pin19, U34_pin19}
  // also tied to VCC on the sheet: {U8_pin3, U14_pin3, U20_pin3, U2_pin13, U8_pin13, U14_pin13, U20_pin13}

  // Other names for the same wires on the sheet: addr_base_oe_n_0 = addr_base_oe_n[0];
  //   addr_base_oe_n_1 = addr_base_oe_n[1]; addr_base_sel_0 = addr_base_sel[0]; addr_base_sel_1 = addr_base_sel[1];
  //   addr_bus_a_0 = addr_bus_a[0]; addr_bus_a_1 = addr_bus_a[1]; addr_bus_a_2 = addr_bus_a[2];
  //   addr_bus_a_3 = addr_bus_a[3]; addr_bus_a_4 = addr_bus_a[4]; addr_bus_a_5 = addr_bus_a[5];
  //   addr_bus_a_6 = addr_bus_a[6]; addr_bus_a_7 = addr_bus_a[7]; addr_bus_addr_hi_0 = addr_bus_addr_hi[0];
  //   addr_bus_addr_hi_1 = addr_bus_addr_hi[1]; addr_bus_addr_hi_2 = addr_bus_addr_hi[2];
  //   addr_bus_addr_hi_3 = addr_bus_addr_hi[3]; addr_bus_addr_hi_4 = addr_bus_addr_hi[4];
  //   addr_bus_addr_hi_5 = addr_bus_addr_hi[5]; addr_bus_addr_hi_6 = addr_bus_addr_hi[6];
  //   addr_bus_addr_hi_7 = addr_bus_addr_hi[7]; addr_bus_addr_lo_0 = addr_bus_addr_lo[0];
  //   addr_bus_addr_lo_1 = addr_bus_addr_lo[1]; addr_bus_addr_lo_2 = addr_bus_addr_lo[2];
  //   addr_bus_addr_lo_3 = addr_bus_addr_lo[3]; addr_bus_addr_lo_4 = addr_bus_addr_lo[4];
  //   addr_bus_addr_lo_5 = addr_bus_addr_lo[5]; addr_bus_addr_lo_6 = addr_bus_addr_lo[6];
  //   addr_bus_addr_lo_7 = addr_bus_addr_lo[7]; addr_bus_addr_lo_in_0 = addr_bus_addr_lo_in[0];
  //   addr_bus_addr_lo_in_1 = addr_bus_addr_lo_in[1]; addr_bus_addr_lo_in_2 = addr_bus_addr_lo_in[2];
  //   addr_bus_addr_lo_in_3 = addr_bus_addr_lo_in[3]; addr_bus_addr_lo_in_4 = addr_bus_addr_lo_in[4];
  //   addr_bus_addr_lo_in_5 = addr_bus_addr_lo_in[5]; addr_bus_addr_lo_in_6 = addr_bus_addr_lo_in[6];
  //   addr_bus_addr_lo_in_7 = addr_bus_addr_lo_in[7]; addr_bus_b_0 = addr_bus_b[0]; addr_bus_b_1 = addr_bus_b[1];
  //   addr_bus_b_2 = addr_bus_b[2]; addr_bus_b_3 = addr_bus_b[3]; addr_bus_b_4 = addr_bus_b[4];
  //   addr_bus_b_5 = addr_bus_b[5]; addr_bus_b_6 = addr_bus_b[6]; addr_bus_b_7 = addr_bus_b[7];
  //   addr_bus_out_0 = addr_bus_out[0]; addr_bus_out_1 = addr_bus_out[1]; addr_bus_out_2 = addr_bus_out[2];
  //   addr_bus_out_3 = addr_bus_out[3]; addr_bus_out_4 = addr_bus_out[4]; addr_bus_out_5 = addr_bus_out[5];
  //   addr_bus_out_6 = addr_bus_out[6]; addr_bus_out_7 = addr_bus_out[7]; addr_lat_oe_n_0 = addr_lat_oe_n[0];
  //   addr_lat_oe_n_1 = addr_lat_oe_n[1]; addr_off_oe_n_0 = addr_off_oe_n[0]; addr_off_oe_n_1 = addr_off_oe_n[1];
  //   addr_pc_oe_n_0 = addr_pc_oe_n[0]; addr_pc_oe_n_1 = addr_pc_oe_n[1]; addr_sp_oe_n_0 = addr_sp_oe_n[0];
  //   addr_sp_oe_n_1 = addr_sp_oe_n[1]; addr_v1_0 = addr_v1[0]; addr_v1_1 = addr_v1[1]; addr_v1_2 = addr_v1[2];
  //   addr_v1_3 = addr_v1[3]; addr_v1_4 = addr_v1[4]; addr_v1_5 = addr_v1[5]; addr_v1_6 = addr_v1[6];
  //   addr_v1_7 = addr_v1[7]; addr_v2_0 = addr_v2[0]; addr_v2_1 = addr_v2[1]; addr_v2_2 = addr_v2[2];
  //   addr_v2_3 = addr_v2[3]; addr_v2_4 = addr_v2[4]; addr_v2_5 = addr_v2[5]; addr_v2_6 = addr_v2[6];
  //   addr_v2_7 = addr_v2[7]

  // Notes on the sheet:
  //   BASE bits 1..0
  //   BASE bits 3..2
  //   BASE bits 5..4
  //   BASE bits 7..6
  //   OFFSET bits 3..0: V2 / V1
  //   OFFSET bits 7..4: V2 / V1
  //   BASE bits 9..8
  //   BASE bits 11..10
  //   BASE bits 13..12
  //   BASE bits 15..14
  //   OFFSET bits 11..8: V1
  //   OFFSET bits 15..12: V1
  //   OFFSET xor inv, bits 3..0
  //   OFFSET xor inv, bits 7..4
  //   OFFSET xor inv, bits 11..8
  //   OFFSET xor inv, bits 15..12
  //   reset: PC bits 15..12
  //   reset: PC 11..9, IVT p7
  //   adder bits 3..0
  //   adder bits 7..4
  //   adder bits 11..8
  //   adder bits 15..12
  //   address latch high byte
  //   address latch low byte
  //   PC high byte
  //   PC low byte
  //   SP high byte
  //   SP low byte
  //   latch high → address bus
  //   latch low → address bus
  //   PC high → data bus
  //   PC low → data bus
  //   SP high → data bus
  //   SP low → data bus
endmodule
