// Logisim project add8.circ as structural Verilog: 1 circuit, main circuit add8
module add8 (
  input  [7:0] add8_a,
  input  [7:0] add8_b,
  input  add8_cin,
  output [7:0] add8_s,
  output add8_cout
);

  wire U1_pin7;

  _74283 U1 (
    .pin1(add8_s[5]), .pin2(add8_b[5]), .pin3(add8_a[5]), .pin4(add8_s[4]), .pin5(add8_a[4]),
    .pin6(add8_b[4]), .pin7(U1_pin7), .pin15(add8_b[6]), .pin14(add8_a[6]), .pin13(add8_s[6]),
    .pin12(add8_a[7]), .pin11(add8_b[7]), .pin10(add8_s[7]), .pin9(add8_cout));
  _74283 U2 (
    .pin1(add8_s[1]), .pin2(add8_b[1]), .pin3(add8_a[1]), .pin4(add8_s[0]), .pin5(add8_a[0]),
    .pin6(add8_b[0]), .pin7(add8_cin), .pin15(add8_b[2]), .pin14(add8_a[2]), .pin13(add8_s[2]),
    .pin12(add8_a[3]), .pin11(add8_b[3]), .pin10(add8_s[3]), .pin9(U1_pin7));

  // Notes on the sheet:
  //   bits 7..4
  //   bits 3..0
endmodule
