// Logisim project add_sub8.circ as structural Verilog: 1 circuit, main circuit add_sub8
module add_sub8 (
  input  add_sub8_sub,
  input  add_sub8_use_c,
  input  add_sub8_cin,
  input  [7:0] add_sub8_a,
  input  [7:0] add_sub8_b,
  output [7:0] add_sub8_s,
  output add_sub8_c
);

  wire add_sub8_c4, add_sub8_c_hi0, add_sub8_c_hi1, add_sub8_c_lo, U2_pin7, U3_pin7, U4_pin15, U6_pin7,
       U7_pin5, U7_pin6, U7_pin10, U7_pin11, U7_pin13, U7_pin14, U7_pin15, U8_pin1, U8_pin10, U8_pin11,
       U9_pin1;
  wire [7:0] U5_pin3;
  wire [7:4] U2_pin4, U3_pin4;

  _7486 U1 (
    .pin1(add_sub8_b[4]), .pin2(add_sub8_sub), .pin3(U5_pin3[4]), .pin4(add_sub8_b[5]), .pin5(add_sub8_sub),
    .pin6(U5_pin3[5]), .pin13(add_sub8_sub), .pin12(add_sub8_b[7]), .pin11(U5_pin3[7]), .pin10(add_sub8_sub),
    .pin9(add_sub8_b[6]), .pin8(U5_pin3[6]));
  _7486 U5 (
    .pin1(add_sub8_b[0]), .pin2(add_sub8_sub), .pin3(U5_pin3[0]), .pin4(add_sub8_b[1]), .pin5(add_sub8_sub),
    .pin6(U5_pin3[1]), .pin13(add_sub8_sub), .pin12(add_sub8_b[3]), .pin11(U5_pin3[3]), .pin10(add_sub8_sub),
    .pin9(add_sub8_b[2]), .pin8(U5_pin3[2]));
  _7408 U8 (
    .pin1(U8_pin1), .pin2(U8_pin1), .pin4(U8_pin1), .pin5(U8_pin1), .pin13(add_sub8_use_c),
    .pin12(add_sub8_cin), .pin11(U8_pin11), .pin10(U8_pin10), .pin9(U8_pin10));  // open: pin3, pin6, pin8
  _74283 U2 (
    .pin1(U2_pin4[5]), .pin2(U5_pin3[5]), .pin3(add_sub8_a[5]), .pin4(U2_pin4[4]), .pin5(add_sub8_a[4]),
    .pin6(U5_pin3[4]), .pin7(U2_pin7), .pin15(U5_pin3[6]), .pin14(add_sub8_a[6]), .pin13(U2_pin4[6]),
    .pin12(add_sub8_a[7]), .pin11(U5_pin3[7]), .pin10(U2_pin4[7]), .pin9(add_sub8_c_hi0));
  _74283 U6 (
    .pin1(add_sub8_s[1]), .pin2(U5_pin3[1]), .pin3(add_sub8_a[1]), .pin4(add_sub8_s[0]),
    .pin5(add_sub8_a[0]), .pin6(U5_pin3[0]), .pin7(U6_pin7), .pin15(U5_pin3[2]), .pin14(add_sub8_a[2]),
    .pin13(add_sub8_s[2]), .pin12(add_sub8_a[3]), .pin11(U5_pin3[3]), .pin10(add_sub8_s[3]),
    .pin9(add_sub8_c_lo));
  _7486 U9 (
    .pin1(U9_pin1), .pin2(U9_pin1), .pin4(U9_pin1), .pin5(U9_pin1), .pin13(U8_pin11), .pin12(add_sub8_sub),
    .pin11(U6_pin7), .pin10(add_sub8_sub), .pin9(add_sub8_c4), .pin8(add_sub8_c));  // open: pin3, pin6
  _74283 U3 (
    .pin1(U3_pin4[5]), .pin2(U5_pin3[5]), .pin3(add_sub8_a[5]), .pin4(U3_pin4[4]), .pin5(add_sub8_a[4]),
    .pin6(U5_pin3[4]), .pin7(U3_pin7), .pin15(U5_pin3[6]), .pin14(add_sub8_a[6]), .pin13(U3_pin4[6]),
    .pin12(add_sub8_a[7]), .pin11(U5_pin3[7]), .pin10(U3_pin4[7]), .pin9(add_sub8_c_hi1));
  _74157 U4 (
    .pin1(add_sub8_c_lo), .pin2(U2_pin4[4]), .pin3(U3_pin4[4]), .pin4(add_sub8_s[4]), .pin5(U2_pin4[5]),
    .pin6(U3_pin4[5]), .pin7(add_sub8_s[5]), .pin15(U4_pin15), .pin14(U2_pin4[7]), .pin13(U3_pin4[7]),
    .pin12(add_sub8_s[7]), .pin11(U2_pin4[6]), .pin10(U3_pin4[6]), .pin9(add_sub8_s[6]));
  _74157 U7 (
    .pin1(add_sub8_c_lo), .pin2(add_sub8_c_hi0), .pin3(add_sub8_c_hi1), .pin4(add_sub8_c4), .pin5(U7_pin5),
    .pin6(U7_pin6), .pin15(U7_pin15), .pin14(U7_pin14), .pin13(U7_pin13), .pin11(U7_pin11), .pin10(U7_pin10));  // open: pin7, pin12, pin9
  // also tied to GND on the sheet: {U8_pin10, U8_pin1, U2_pin7, U9_pin1, U4_pin15, U7_pin10, U7_pin11, U7_pin13, U7_pin14, U7_pin15, U7_pin5, U7_pin6}
  // also tied to VCC on the sheet: U3_pin7

  // Notes on the sheet:
  //   b 7..4 xor sub
  //   b 3..0 xor sub
  //   use_c and cin
  //   bits 7..4, cin 0
  //   bits 3..0
  //   carry in, c flag
  //   bits 7..4, cin 1
  //   s 7..4: cin 0 or 1
  //   carry out: cin 0 or 1
endmodule
