// Logisim project alu.circ as structural Verilog: 1 circuit, main circuit alu
module alu (
  input  [3:0] alu_op,
  input  alu_cin,
  input  [7:0] alu_a,
  input  [7:0] alu_b,
  output [7:0] alu_r,
  output alu_c,
  output alu_n,
  output alu_z,
  output alu_s,
  output alu_e,
  output alu_f
);

  wire alu_c_add;
  wire [7:0] alu_and, alu_or, alu_shl, alu_sr, alu_sum, alu_xor;

  add_sub8 add_sub8_1 (
    .add_sub8_sub(alu_op[0]), .add_sub8_use_c(alu_op[1]), .add_sub8_cin(alu_cin), .add_sub8_c(alu_c_add),
    .add_sub8_a(alu_a), .add_sub8_b(alu_b), .add_sub8_s(alu_sum));
  logic8 logic8_1 (.logic8_a(alu_a), .logic8_b(alu_b), .logic8_and(alu_and), .logic8_or(alu_or), .logic8_xor(alu_xor));
  shift8 shift8_1 (
    .shift8_sel(alu_op[3]), .shift8_asr(alu_op[0]), .shift8_c_add(alu_c_add), .shift8_c(alu_c),
    .shift8_a(alu_a), .shift8_shl(alu_shl), .shift8_sr(alu_sr));
  rmux8 rmux8_1 (
    .rmux8_op(alu_op), .rmux8_sum(alu_sum), .rmux8_and(alu_and), .rmux8_or(alu_or), .rmux8_xor(alu_xor),
    .rmux8_a(alu_a), .rmux8_shl(alu_shl), .rmux8_sr(alu_sr), .rmux8_r(alu_r));
  flags8 flags8_1 (.flags8_n(alu_n), .flags8_z(alu_z), .flags8_r(alu_r));
  cmp8 cmp8_1 (.cmp8_s(alu_s), .cmp8_e(alu_e), .cmp8_f(alu_f), .cmp8_a(alu_a), .cmp8_b(alu_b));

  // Other names for the same wires on the sheet: alu_op_0 = alu_op[0]; alu_op_1 = alu_op[1]; alu_op_2 = alu_op[2];
  //   alu_op_3 = alu_op[3]
endmodule
