// Logisim project arith8.circ as structural Verilog: 1 circuit, main circuit arith8
module arith8 (
  input  arith8_one,
  input  arith8_sub,
  input  arith8_use_c,
  input  arith8_cin,
  input  [7:0] arith8_a,
  input  [7:0] arith8_b,
  output [7:0] arith8_s,
  output arith8_c
);

  wire U1_pin3, U1_pin6, U1_pin10, U1_pin13, U1_pin15, U2_pin3, U2_pin6, U2_pin10, U2_pin13, U2_pin15;
  wire [7:0] U2_pin4;

  _74157 U1 (
    .pin1(arith8_one), .pin2(arith8_b[4]), .pin3(U1_pin3), .pin4(U2_pin4[4]), .pin5(arith8_b[5]),
    .pin6(U1_pin6), .pin7(U2_pin4[5]), .pin15(U1_pin15), .pin14(arith8_b[7]), .pin13(U1_pin13),
    .pin12(U2_pin4[7]), .pin11(arith8_b[6]), .pin10(U1_pin10), .pin9(U2_pin4[6]));
  _74157 U2 (
    .pin1(arith8_one), .pin2(arith8_b[0]), .pin3(U2_pin3), .pin4(U2_pin4[0]), .pin5(arith8_b[1]),
    .pin6(U2_pin6), .pin7(U2_pin4[1]), .pin15(U2_pin15), .pin14(arith8_b[3]), .pin13(U2_pin13),
    .pin12(U2_pin4[3]), .pin11(arith8_b[2]), .pin10(U2_pin10), .pin9(U2_pin4[2]));
  add_sub8 add_sub8_1 (
    .add_sub8_sub(arith8_sub), .add_sub8_use_c(arith8_use_c), .add_sub8_cin(arith8_cin),
    .add_sub8_c(arith8_c), .add_sub8_a(arith8_a), .add_sub8_b(U2_pin4), .add_sub8_s(arith8_s));
  // also tied to GND on the sheet: {U1_pin10, U1_pin13, U1_pin15, U2_pin10, U2_pin13, U2_pin15, U1_pin3, U1_pin6, U2_pin6}
  // also tied to VCC on the sheet: U2_pin3

  // Notes on the sheet:
  //   b or 01, bits 7..4
  //   b or 01, bits 3..0
endmodule
