// Logisim project cmp8.circ as structural Verilog: 1 circuit, main circuit cmp8
module cmp8 (
  input  [7:0] cmp8_a,
  input  [7:0] cmp8_b,
  output cmp8_s,
  output cmp8_e,
  output cmp8_f
);

  wire U1_pin2, U1_pin3, U1_pin4, U1_pin5, U1_pin6, U1_pin7;

  _7485 U1 (
    .pin1(cmp8_b[3]), .pin2(U1_pin2), .pin3(U1_pin3), .pin4(U1_pin4), .pin5(U1_pin5), .pin6(U1_pin6),
    .pin7(U1_pin7), .pin15(cmp8_a[3]), .pin14(cmp8_b[2]), .pin13(cmp8_a[2]), .pin12(cmp8_a[1]),
    .pin11(cmp8_b[1]), .pin10(cmp8_a[0]), .pin9(cmp8_b[0]));
  _7485 U2 (
    .pin1(cmp8_b[7]), .pin2(U1_pin7), .pin3(U1_pin6), .pin4(U1_pin5), .pin5(cmp8_s), .pin6(cmp8_e),
    .pin7(cmp8_f), .pin15(cmp8_a[7]), .pin14(cmp8_b[6]), .pin13(cmp8_a[6]), .pin12(cmp8_a[5]),
    .pin11(cmp8_b[5]), .pin10(cmp8_a[4]), .pin9(cmp8_b[4]));
  // also tied to GND on the sheet: {U1_pin2, U1_pin4}
  // also tied to VCC on the sheet: U1_pin3

  // Notes on the sheet:
  //   bits 3..0
  //   bits 7..4
endmodule
