// Logisim project flags8.circ as structural Verilog: 1 circuit, main circuit flags8
module flags8 (
  input  [7:0] flags8_r,
  input  flags8_c,
  output flags8_n,
  output flags8_f,
  output flags8_z,
  output flags8_e,
  output flags8_s
);

  wire U1_pin6, U1_pin8, U1_pin11, U1_pin12, U2_pin1, U2_pin2, U2_pin3, U2_pin4, U2_pin5, U2_pin13, U3_pin5,
       U3_pin6, U3_pin8, U3_pin9, U3_pin11, U3_pin12;

  _7427 U1 (
    .pin1(flags8_r[0]), .pin2(flags8_r[1]), .pin3(flags8_r[3]), .pin4(flags8_r[4]), .pin5(flags8_r[5]),
    .pin6(U1_pin6), .pin13(flags8_r[2]), .pin12(U1_pin12), .pin11(U1_pin11), .pin10(flags8_r[7]),
    .pin9(flags8_r[6]), .pin8(U1_pin8));
  _7411 U2 (
    .pin1(U2_pin1), .pin2(U2_pin2), .pin3(U2_pin3), .pin4(U2_pin4), .pin5(U2_pin5), .pin13(U2_pin13),
    .pin11(U1_pin8), .pin10(U1_pin6), .pin9(U1_pin12), .pin8(flags8_e));  // open: pin6, pin12
  _7402 U3 (
    .pin1(flags8_s), .pin2(flags8_c), .pin3(flags8_e), .pin5(U3_pin5), .pin6(U3_pin6), .pin12(U3_pin12),
    .pin11(U3_pin11), .pin9(U3_pin9), .pin8(U3_pin8));  // open: pin4, pin13, pin10

  assign flags8_f = flags8_c;
  assign flags8_n = flags8_r[7];
  assign flags8_z = flags8_e;
  // also tied to GND on the sheet: {U1_pin11, U2_pin13, U3_pin8, U3_pin9, U3_pin11, U3_pin12, U2_pin1, U2_pin2, U2_pin3, U2_pin4, U2_pin5, U3_pin5, U3_pin6}

  // Notes on the sheet:
  //   z: nor of r
  //   z: and
  //   s = nor(c, z)
endmodule
