// Logisim project logic8.circ as structural Verilog: 1 circuit, main circuit logic8
module logic8 (
  input  [7:0] logic8_a,
  input  [7:0] logic8_b,
  output [7:0] logic8_and,
  output [7:0] logic8_or,
  output [7:0] logic8_xor
);

  _7408 U1 (
    .pin1(logic8_a[4]), .pin2(logic8_b[4]), .pin3(logic8_and[4]), .pin4(logic8_a[5]), .pin5(logic8_b[5]),
    .pin6(logic8_and[5]), .pin13(logic8_b[7]), .pin12(logic8_a[7]), .pin11(logic8_and[7]),
    .pin10(logic8_b[6]), .pin9(logic8_a[6]), .pin8(logic8_and[6]));
  _7408 U4 (
    .pin1(logic8_a[0]), .pin2(logic8_b[0]), .pin3(logic8_and[0]), .pin4(logic8_a[1]), .pin5(logic8_b[1]),
    .pin6(logic8_and[1]), .pin13(logic8_b[3]), .pin12(logic8_a[3]), .pin11(logic8_and[3]),
    .pin10(logic8_b[2]), .pin9(logic8_a[2]), .pin8(logic8_and[2]));
  _7432 U2 (
    .pin1(logic8_a[4]), .pin2(logic8_b[4]), .pin3(logic8_or[4]), .pin4(logic8_a[5]), .pin5(logic8_b[5]),
    .pin6(logic8_or[5]), .pin13(logic8_b[7]), .pin12(logic8_a[7]), .pin11(logic8_or[7]), .pin10(logic8_b[6]),
    .pin9(logic8_a[6]), .pin8(logic8_or[6]));
  _7432 U5 (
    .pin1(logic8_a[0]), .pin2(logic8_b[0]), .pin3(logic8_or[0]), .pin4(logic8_a[1]), .pin5(logic8_b[1]),
    .pin6(logic8_or[1]), .pin13(logic8_b[3]), .pin12(logic8_a[3]), .pin11(logic8_or[3]), .pin10(logic8_b[2]),
    .pin9(logic8_a[2]), .pin8(logic8_or[2]));
  _7486 U3 (
    .pin1(logic8_a[4]), .pin2(logic8_b[4]), .pin3(logic8_xor[4]), .pin4(logic8_a[5]), .pin5(logic8_b[5]),
    .pin6(logic8_xor[5]), .pin13(logic8_b[7]), .pin12(logic8_a[7]), .pin11(logic8_xor[7]),
    .pin10(logic8_b[6]), .pin9(logic8_a[6]), .pin8(logic8_xor[6]));
  _7486 U6 (
    .pin1(logic8_a[0]), .pin2(logic8_b[0]), .pin3(logic8_xor[0]), .pin4(logic8_a[1]), .pin5(logic8_b[1]),
    .pin6(logic8_xor[1]), .pin13(logic8_b[3]), .pin12(logic8_a[3]), .pin11(logic8_xor[3]),
    .pin10(logic8_b[2]), .pin9(logic8_a[2]), .pin8(logic8_xor[2]));

  // Notes on the sheet:
  //   a and b, bits 7..4
  //   a and b, bits 3..0
  //   a or b, bits 7..4
  //   a or b, bits 3..0
  //   a xor b, bits 7..4
  //   a xor b, bits 3..0
endmodule
