// Logisim project rmux8.circ as structural Verilog: 1 circuit, main circuit rmux8
module rmux8 (
  input  [3:0] rmux8_op,
  input  [7:0] rmux8_sum,
  input  [7:0] rmux8_and,
  input  [7:0] rmux8_or,
  input  [7:0] rmux8_xor,
  input  [7:0] rmux8_a,
  input  [7:0] rmux8_shl,
  input  [7:0] rmux8_sr,
  output [7:0] rmux8_r
);

  wire rmux8_and_oe_n, rmux8_not_oe_n, rmux8_or_oe_n, rmux8_shl_oe_n, rmux8_sr_oe_n, rmux8_xor_oe_n,
       rmux8_y5_n, rmux8_y6_n, rmux8_y7_n, U1_pin4, U1_pin5, U2_pin3, U2_pin4, U2_pin5, U2_pin9, U2_pin10,
       U2_pin11, U4_pin19, U5_pin19, U6_pin19, U7_pin19, U8_pin19, U9_pin19;

  _74138 U1 (
    .pin1(rmux8_op[0]), .pin2(rmux8_op[1]), .pin3(rmux8_op[2]), .pin4(U1_pin4), .pin5(U1_pin5),
    .pin6(rmux8_op[3]), .pin7(rmux8_y7_n), .pin15(rmux8_and_oe_n), .pin14(rmux8_or_oe_n),
    .pin13(rmux8_xor_oe_n), .pin12(rmux8_not_oe_n), .pin11(rmux8_shl_oe_n), .pin10(rmux8_y5_n),
    .pin9(rmux8_y6_n));
  _7411 U2 (
    .pin1(rmux8_y5_n), .pin2(rmux8_y6_n), .pin3(U2_pin3), .pin4(U2_pin4), .pin5(U2_pin5), .pin13(rmux8_y7_n),
    .pin12(rmux8_sr_oe_n), .pin11(U2_pin11), .pin10(U2_pin10), .pin9(U2_pin9));  // open: pin6, pin8
  _74240 U3 (
    .pin1(rmux8_not_oe_n), .pin2(rmux8_a[0]), .pin3(rmux8_r[7]), .pin4(rmux8_a[1]), .pin5(rmux8_r[6]),
    .pin6(rmux8_a[2]), .pin7(rmux8_r[5]), .pin8(rmux8_a[3]), .pin9(rmux8_r[4]), .pin19(rmux8_not_oe_n),
    .pin18(rmux8_r[0]), .pin17(rmux8_a[7]), .pin16(rmux8_r[1]), .pin15(rmux8_a[6]), .pin14(rmux8_r[2]),
    .pin13(rmux8_a[5]), .pin12(rmux8_r[3]), .pin11(rmux8_a[4]));
  _74541 U4 (
    .pin1(rmux8_op[3]), .pin2(rmux8_sum[0]), .pin3(rmux8_sum[1]), .pin4(rmux8_sum[2]), .pin5(rmux8_sum[3]),
    .pin6(rmux8_sum[4]), .pin7(rmux8_sum[5]), .pin8(rmux8_sum[6]), .pin9(rmux8_sum[7]), .pin19(U4_pin19),
    .pin18(rmux8_r[0]), .pin17(rmux8_r[1]), .pin16(rmux8_r[2]), .pin15(rmux8_r[3]), .pin14(rmux8_r[4]),
    .pin13(rmux8_r[5]), .pin12(rmux8_r[6]), .pin11(rmux8_r[7]));
  _74541 U5 (
    .pin1(rmux8_and_oe_n), .pin2(rmux8_and[0]), .pin3(rmux8_and[1]), .pin4(rmux8_and[2]),
    .pin5(rmux8_and[3]), .pin6(rmux8_and[4]), .pin7(rmux8_and[5]), .pin8(rmux8_and[6]), .pin9(rmux8_and[7]),
    .pin19(U5_pin19), .pin18(rmux8_r[0]), .pin17(rmux8_r[1]), .pin16(rmux8_r[2]), .pin15(rmux8_r[3]),
    .pin14(rmux8_r[4]), .pin13(rmux8_r[5]), .pin12(rmux8_r[6]), .pin11(rmux8_r[7]));
  _74541 U6 (
    .pin1(rmux8_or_oe_n), .pin2(rmux8_or[0]), .pin3(rmux8_or[1]), .pin4(rmux8_or[2]), .pin5(rmux8_or[3]),
    .pin6(rmux8_or[4]), .pin7(rmux8_or[5]), .pin8(rmux8_or[6]), .pin9(rmux8_or[7]), .pin19(U6_pin19),
    .pin18(rmux8_r[0]), .pin17(rmux8_r[1]), .pin16(rmux8_r[2]), .pin15(rmux8_r[3]), .pin14(rmux8_r[4]),
    .pin13(rmux8_r[5]), .pin12(rmux8_r[6]), .pin11(rmux8_r[7]));
  _74541 U7 (
    .pin1(rmux8_xor_oe_n), .pin2(rmux8_xor[0]), .pin3(rmux8_xor[1]), .pin4(rmux8_xor[2]),
    .pin5(rmux8_xor[3]), .pin6(rmux8_xor[4]), .pin7(rmux8_xor[5]), .pin8(rmux8_xor[6]), .pin9(rmux8_xor[7]),
    .pin19(U7_pin19), .pin18(rmux8_r[0]), .pin17(rmux8_r[1]), .pin16(rmux8_r[2]), .pin15(rmux8_r[3]),
    .pin14(rmux8_r[4]), .pin13(rmux8_r[5]), .pin12(rmux8_r[6]), .pin11(rmux8_r[7]));
  _74541 U8 (
    .pin1(rmux8_shl_oe_n), .pin2(rmux8_shl[0]), .pin3(rmux8_shl[1]), .pin4(rmux8_shl[2]),
    .pin5(rmux8_shl[3]), .pin6(rmux8_shl[4]), .pin7(rmux8_shl[5]), .pin8(rmux8_shl[6]), .pin9(rmux8_shl[7]),
    .pin19(U8_pin19), .pin18(rmux8_r[0]), .pin17(rmux8_r[1]), .pin16(rmux8_r[2]), .pin15(rmux8_r[3]),
    .pin14(rmux8_r[4]), .pin13(rmux8_r[5]), .pin12(rmux8_r[6]), .pin11(rmux8_r[7]));
  _74541 U9 (
    .pin1(rmux8_sr_oe_n), .pin2(rmux8_sr[0]), .pin3(rmux8_sr[1]), .pin4(rmux8_sr[2]), .pin5(rmux8_sr[3]),
    .pin6(rmux8_sr[4]), .pin7(rmux8_sr[5]), .pin8(rmux8_sr[6]), .pin9(rmux8_sr[7]), .pin19(U9_pin19),
    .pin18(rmux8_r[0]), .pin17(rmux8_r[1]), .pin16(rmux8_r[2]), .pin15(rmux8_r[3]), .pin14(rmux8_r[4]),
    .pin13(rmux8_r[5]), .pin12(rmux8_r[6]), .pin11(rmux8_r[7]));
  // also tied to GND on the sheet: {U1_pin4, U1_pin5, U2_pin9, U2_pin10, U2_pin11, U2_pin3, U2_pin4, U2_pin5, U4_pin19, U5_pin19, U6_pin19, U7_pin19, U8_pin19, U9_pin19}

  // Other names for the same wires on the sheet: rmux8_sum_oe_n = rmux8_op[3]

  // Notes on the sheet:
  //   U1: op -> enables
  //   U2: sr enable
  //   U3: not a
  //   U4: sum
  //   U5: and
  //   U6: or
  //   U7: xor
  //   U8: shl
  //   U9: sr
endmodule
