// Logisim project shift8.circ as structural Verilog: 1 circuit, main circuit shift8
module shift8 (
  input  shift8_sel,
  input  shift8_asr,
  input  shift8_c_add,
  input  [7:0] shift8_a,
  output [7:0] shift8_sr,
  output [7:0] shift8_shl,
  output shift8_c
);

  wire U1_pin1, U1_pin10, U1_pin11, U1_pin12, U1_pin15;

  _74153 U1 (
    .pin1(U1_pin1), .pin2(shift8_sel), .pin3(shift8_a[0]), .pin4(shift8_a[7]), .pin5(shift8_c_add),
    .pin6(shift8_c_add), .pin7(shift8_c), .pin15(U1_pin15), .pin14(shift8_asr), .pin13(shift8_a[7]),
    .pin12(U1_pin12), .pin11(U1_pin11), .pin10(U1_pin10), .pin9(shift8_sr[7]));

  assign shift8_shl = {shift8_a[6:0], 1'b0};
  assign shift8_sr[6:0] = shift8_a[7:1];
  // also tied to GND on the sheet: {U1_pin10, U1_pin11, U1_pin12, U1_pin15, U1_pin1}

  // Other names for the same wires on the sheet: shift8_fill = shift8_sr[7]

  // Notes on the sheet:
  //   sr = fill, a7..a1
  //   shl = a6..a0, 0
  //   c select, ASR fill
endmodule
