// Logisim project 74574.circ as structural Verilog: 2 circuits, main circuit ttl74574
module ttl74574 (
  input  D0,
  input  D1,
  input  D2,
  input  D3,
  input  D4,
  input  D5,
  input  nOE,
  input  D6,
  input  D7,
  input  CP,
  input  VCC,
  input  GND,
  output Q0,
  output Q1,
  output Q2,
  output Q3,
  output Q4,
  output Q5,
  output Q6,
  output Q7
);

  wire not_1_out;
  wire [7:0] register_1_q;

  Register #(.width(8)) register_1 (
    .D({D7, D6, D5, D4, D3, D2, D1, D0}), .en(1'b1), .clk(CP), .Q(register_1_q), .clr(1'b0));
  assign {Q7, Q6, Q5, Q4, Q3, Q2, Q1, Q0} = not_1_out ? register_1_q : 8'bz;  // Controlled_Buffer controlled_buffer_1
  not not_1 (not_1_out, nOE);

  // Notes on the sheet:
  //   74HCT574 (TI SCHS183E): edge-triggered, outputs off when /OE is high
endmodule

module test_74574 (
  input  oe_n,
  input  cp,
  input  [7:0] d,
  output [7:0] q
);

  ttl74574 U1 (
    .nOE(oe_n), .D0(d[0]), .D1(d[1]), .D2(d[2]), .D3(d[3]), .D4(d[4]), .D5(d[5]), .D6(d[6]), .D7(d[7]),
    .CP(cp), .Q7(q[7]), .Q6(q[6]), .Q5(q[5]), .Q4(q[4]), .Q3(q[3]), .Q2(q[2]), .Q1(q[1]), .Q0(q[0]));  // open: GND, VCC

  // Other names for the same wires on the sheet: d_0 = d[0]; d_1 = d[1]; d_2 = d[2]; d_3 = d[3]; d_4 = d[4];
  //   d_5 = d[5]; d_6 = d[6]; d_7 = d[7]; q_0 = q[0]; q_1 = q[1]; q_2 = q[2]; q_3 = q[3]; q_4 = q[4]; q_5 = q[5];
  //   q_6 = q[6]; q_7 = q[7]
endmodule
