// Logisim project 74595.circ as structural Verilog: 2 circuits, main circuit ttl74595
module ttl74595 (
  input  SER,
  input  SRCLK,
  input  nSRCLR,
  input  RCLK,
  input  nOE,
  input  VCC,
  input  GND,
  output QH_prime,
  output QA,
  output QB,
  output QC,
  output QD,
  output QE,
  output QF,
  output QG,
  output QH
);

  wire not_1_out, not_2_out;
  wire [6:0] s;
  wire [7:0] register_2_q;

  Register #(.width(8)) register_1 (.D({s, SER}), .en(1'b1), .clk(SRCLK), .Q({QH_prime, s}), .clr(not_1_out));
  not not_1 (not_1_out, nSRCLR);
  Register #(.width(8)) register_2 (.D({QH_prime, s}), .en(1'b1), .clk(RCLK), .Q(register_2_q), .clr(1'b0));
  not not_2 (not_2_out, nOE);
  assign {QH, QG, QF, QE, QD, QC, QB, QA} = not_2_out ? register_2_q : 8'bz;  // Controlled_Buffer controlled_buffer_1

  // Other names for the same wires on the sheet: s[7] = QH_prime; s7 = QH_prime

  // Notes on the sheet:
  //   shift register: bit 0 = QA takes SER on SRCLK rising; cleared by /SRCLR low
  //   storage register: takes the shift register on RCLK rising; QA-QH off when /OE is high
endmodule

module test_74595 (
  input  oe_n,
  input  srclr_n,
  input  srclk,
  input  rclk,
  input  ser,
  output [7:0] q,
  output qh_s
);

  ttl74595 U1 (
    .QB(q[1]), .QC(q[2]), .QD(q[3]), .QE(q[4]), .QF(q[5]), .QG(q[6]), .QH(q[7]), .QH_prime(qh_s),
    .nSRCLR(srclr_n), .SRCLK(srclk), .RCLK(rclk), .nOE(oe_n), .SER(ser), .QA(q[0]));  // open: GND, VCC

  // Other names for the same wires on the sheet: q_0 = q[0]; q_1 = q[1]; q_2 = q[2]; q_3 = q[3]; q_4 = q[4];
  //   q_5 = q[5]; q_6 = q[6]; q_7 = q[7]
endmodule
