// Logisim project as6c1008.circ as structural Verilog: 2 circuits, main circuit ttlas6c1008
module ttlas6c1008 (
  input  A0,
  input  A1,
  input  A2,
  input  A3,
  input  A4,
  input  A5,
  input  A6,
  input  A7,
  input  A8,
  input  A9,
  input  A10,
  input  A11,
  input  A12,
  input  A13,
  input  A14,
  input  A15,
  input  A16,
  input  DQ0_in,
  input  DQ1_in,
  input  DQ2_in,
  input  DQ3_in,
  input  DQ4_in,
  input  DQ5_in,
  input  DQ6_in,
  input  DQ7_in,
  input  nCE,
  input  CE2,
  input  nOE,
  input  nWE,
  input  VCC,
  input  GND,
  output DQ0,
  output DQ1,
  output DQ2,
  output DQ3,
  output DQ4,
  output DQ5,
  output DQ6,
  output DQ7,
  output NC
);

  wire ce, oe, read, we, write;
  wire [7:0] ram_1_dout;

  not not_1 (ce, nCE);
  not not_2 (oe, nOE);
  not not_3 (we, nWE);
  RAM #(.addrWidth(17), .dataWidth(8), .databus("bibus"), .enables("byte"), .trigger("high"), .\type ("volatile")) ram_1 (
    .addr({A16, A15, A14, A13, A12, A11, A10, A9, A8, A7, A6, A5, A4, A3, A2, A1, A0}), .we(write),
    .oe(1'b1), .din({DQ7_in, DQ6_in, DQ5_in, DQ4_in, DQ3_in, DQ2_in, DQ1_in, DQ0_in}), .dout(ram_1_dout));
  and and_1 (write, ce, CE2, we, 1'b1);
  and and_2 (read, ce, CE2, oe, nWE);
  assign {DQ7, DQ6, DQ5, DQ4, DQ3, DQ2, DQ1, DQ0} = read ? ram_1_dout : 8'bz;  // Controlled_Buffer controlled_buffer_1

  // Notes on the sheet:
  //   AS6C1008 (Alliance v1.0): 128 K x 8 SRAM, level write, outputs off while writing
endmodule

module test_as6c1008 (
  input  ce_n,
  input  ce2,
  input  oe_n,
  input  we_n,
  input  [16:0] a,
  input  [7:0] din,
  output [7:0] dq
);

  ttlas6c1008 U1 (
    .A16(a[16]), .A14(a[14]), .A12(a[12]), .A7(a[7]), .A6(a[6]), .A5(a[5]), .A4(a[4]), .A3(a[3]), .A2(a[2]),
    .A1(a[1]), .A0(a[0]), .DQ0(dq[0]), .DQ1(dq[1]), .DQ2(dq[2]), .DQ3(dq[3]), .DQ4(dq[4]), .DQ5(dq[5]),
    .DQ6(dq[6]), .DQ7(dq[7]), .nCE(ce_n), .A10(a[10]), .nOE(oe_n), .A11(a[11]), .A9(a[9]), .A8(a[8]),
    .A13(a[13]), .nWE(we_n), .CE2(ce2), .A15(a[15]), .DQ0_in(din[0]), .DQ1_in(din[1]), .DQ2_in(din[2]),
    .DQ3_in(din[3]), .DQ4_in(din[4]), .DQ5_in(din[5]), .DQ6_in(din[6]), .DQ7_in(din[7]));  // open: NC, GND, VCC

  // Other names for the same wires on the sheet: a_0 = a[0]; a_1 = a[1]; a_2 = a[2]; a_3 = a[3]; a_4 = a[4];
  //   a_5 = a[5]; a_6 = a[6]; a_7 = a[7]; a_8 = a[8]; a_9 = a[9]; a_10 = a[10]; a_11 = a[11]; a_12 = a[12];
  //   a_13 = a[13]; a_14 = a[14]; a_15 = a[15]; a_16 = a[16]; din_0 = din[0]; din_1 = din[1]; din_2 = din[2];
  //   din_3 = din[3]; din_4 = din[4]; din_5 = din[5]; din_6 = din[6]; din_7 = din[7]; dq_0 = dq[0]; dq_1 = dq[1];
  //   dq_2 = dq[2]; dq_3 = dq[3]; dq_4 = dq[4]; dq_5 = dq[5]; dq_6 = dq[6]; dq_7 = dq[7]
endmodule
