// Logisim project at28c256.circ as structural Verilog: 2 circuits, main circuit ttlat28c256
module ttlat28c256 (
  input  A0,
  input  A1,
  input  A2,
  input  A3,
  input  A4,
  input  A5,
  input  A6,
  input  A7,
  input  A8,
  input  A9,
  input  A10,
  input  A11,
  input  A12,
  input  A13,
  input  A14,
  input  nCE,
  input  nOE,
  input  nWE,
  input  VCC,
  input  GND,
  input  [3:0] IMAGE,
  output I_O0,
  output I_O1,
  output I_O2,
  output I_O3,
  output I_O4,
  output I_O5,
  output I_O6,
  output I_O7
);

  wire ce, oe, read;
  wire [7:0] rom_1_data;

  not not_1 (ce, nCE);
  not not_2 (oe, nOE);
  ROM #(.addrWidth(19), .dataWidth(8)) rom_1 (
    .addr({IMAGE, A14, A13, A12, A11, A10, A9, A8, A7, A6, A5, A4, A3, A2, A1, A0}), .data(rom_1_data));
  and and_1 (read, ce, oe, 1'b1, 1'b1);
  assign {I_O7, I_O6, I_O5, I_O4, I_O3, I_O2, I_O1, I_O0} = read ? rom_1_data : 8'bz;  // Controlled_Buffer controlled_buffer_1

  // Other names for the same wires on the sheet: IMAGE_0 = IMAGE[0]; IMAGE_1 = IMAGE[1]; IMAGE_2 = IMAGE[2];
  //   IMAGE_3 = IMAGE[3]

  // Notes on the sheet:
  //   contents of rom_1 (hex, n*v repeats v):
  //   5a 7f a4 c9 ee 13 38 5d 82 a7 cc f1 16 3b 60 85 aa cf f4 19 3e 63 88 ad d2 f7 1c 41 66 8b b0 d5 fa
  //   1f 44 69 8e b3 d8 fd 22 47 6c 91 b6 db 0 25 4a 6f 94 b9 de 3 28 4d 72 97 bc e1 6 2b 50 75 9a bf e4 9
  //   2e 53 78 9d c2 e7 c 31 56 7b a0 c5 ea f 34 59 7e a3 c8 ed 12 37 5c 81 a6 cb f0 15 3a 5f 84 a9 ce f3
  //   18 3d 62 87 ac d1 f6 1b 40 65 8a af d4 f9 1e 43 68 8d b2 d7 fc 21 46 6b 90 b5 da ff 24 49 6e 93 b8
  //   dd 2 27 4c 71 96 bb e0 5 2a 4f 74 99 be e3 8 2d 52 77 9c c1 e6 b 30 55 7a 9f c4 e9 e 33 58 7d a2 c7
  //   ec 11 36 5b 80 a5 ca ef 14 39 5e 83 a8 cd f2 17 3c 61 86 ab d0 f5 1a 3f 64 89 ae d3 f8 1d 42 67 8c
  //   b1 d6 fb 20 45 6a 8f b4 d9 fe 23 48 6d 92 b7 dc 1 26 4b 70 95 ba df 4 29 4e 73 98 bd e2 7 2c 51 76
  //   9b c0 e5 a 2f 54 79 9e c3 e8 d 32 57 7c a1 c6 eb 10 35 65 8a af d4 f9 1e 43 68 8d b2 d7 fc 21 46 6b
  //   90 b5 da ff 24 49 6e 93 b8 dd 2 27 4c 71 96 bb e0 5 2a 4f 74 99 be e3 8 2d 52 77 9c c1 e6 b 30 55 7a
  //   9f c4 e9 e 33 58 7d a2 c7 ec 11 36 5b 80 a5 ca ef 14 39 5e 83 a8 cd f2 17 3c 61 86 ab d0 f5 1a 3f 64
  //   89 ae d3 f8 1d 42 67 8c b1 d6 fb 20 45 6a 8f b4 d9 fe 23 48 6d 92 b7 dc 1 26 4b 70 95 ba df 4 29 4e
  //   73 98 bd e2 7 2c 51 76 9b c0 e5 a 2f 54 79 9e c3 e8 d 32 57 7c a1 c6 eb 10 35 5a 7f a4 c9 ee 13 38
  //   5d 82 a7 cc f1 16 3b 60 85 aa cf f4 19 3e 63 88 ad d2 f7 1c 41 66 8b b0 d5 fa 1f 44 69 8e b3 d8 fd
  //   22 47 6c 91 b6 db 0 25 4a 6f 94 b9 de 3 28 4d 72 97 bc e1 6 2b 50 75 9a bf e4 9 2e 53 78 9d c2 e7 c
  //   31 56 7b a0 c5 ea f 34 59 7e a3 c8 ed 12 37 5c 81 a6 cb f0 15 3a 5f 84 a9 ce f3 18 3d 62 87 ac d1 f6
  //   1b 40 70 95 ba df 4 29 4e 73 98 bd e2 7 2c 51 76 9b c0 e5 a 2f 54 79 9e c3 e8 d 32 57 7c a1 c6 eb 10
  //   35 5a 7f a4 c9 ee 13 38 5d 82 a7 cc f1 16 3b 60 85 aa cf f4 19 3e 63 88 ad d2 f7 1c 41 66 8b b0 d5
  //   fa 1f 44 69 8e b3 d8 fd 22 47 6c 91 b6 db 0 25 4a 6f 94 b9 de 3 28 4d 72 97 bc e1 6 2b 50 75 9a bf
  //   e4 9 2e 53 78 9d c2 e7 c 31 56 7b a0 c5 ea f 34 59 7e a3 c8 ed 12 37 5c 81 a6 cb f0 15 3a 5f 84 a9
  //   ce f3 18 3d 62 87 ac d1 f6 1b 40 65 8a af d4 f9 1e 43 68 8d b2 d7 fc 21 46 6b 90 b5 da ff 24 49 6e
  //   93 b8 dd 2 27 4c 71 96 bb e0 5 2a 4f 74 99 be e3 8 2d 52 77 9c c1 e6 b 30 55 7a 9f c4 e9 e 33 58 7d
  //   a2 c7 ec 11 36 5b 80 a5 ca ef 14 39 5e 83 a8 cd f2 17 3c 61 86 ab d0 f5 1a 3f 64 89 ae d3 f8 1d 42
  //   67 8c b1 d6 fb 20 45 6a 8f b4 d9 fe 23 48 6d 92 b7 dc 1 26 4b 7b a0 c5 ea f 34 59 7e a3 c8 ed 12 37
  //   5c 81 a6 cb f0 15 3a 5f 84 a9 ce f3 18 3d 62 87 ac d1 f6 1b 40 65 8a af d4 f9 1e 43 68 8d b2 d7 fc
  //   21 46 6b 90 b5 da ff 24 49 6e 93 b8 dd 2 27 4c 71 96 bb e0 5 2a 4f 74 99 be e3 8 2d 52 77 9c c1 e6 b
  //   30 55 7a 9f c4 e9 e 33 58 7d a2 c7 ec 11 36 5b 80 a5 ca ef 14 39 5e 83 a8 cd f2 17 3c 61 86 ab d0 f5
  //   1a 3f 64 89 ae d3 f8 1d 42 67 8c b1 d6 fb 20 45 6a 8f b4 d9 fe 23 48 6d 92 b7 dc 1 26 4b 70 95 ba df
  //   4 29 4e 73 98 bd e2 7 2c 51 76 9b c0 e5 a 2f 54 79 9e c3 e8 d 32 57 7c a1 c6 eb 10 35 5a 7f a4 c9 ee
  //   13 38 5d 82 a7 cc f1 16 3b 60 85 aa cf f4 19 3e 63 88 ad d2 f7 1c 41 66 8b b0 d5 fa 1f 44 69 8e b3
  //   d8 fd 22 47 6c 91 b6 db 0 25 4a 6f 94 b9 de 3 28 4d 72 97 bc e1 6 2b 50 75 9a bf e4 9 2e 53 78 9d c2
  //   e7 c 31 56 86 ab d0 f5 1a 3f 64 89 ae d3 f8 1d 42 67 8c b1 d6 fb 20 45 6a 8f b4 d9 fe 23 48 6d 92 b7
  //   dc 1 26 4b 70 95 ba df 4 29 4e 73 98 bd e2 7 2c 51 76 9b c0 e5 a 2f 54 79 9e c3 e8 d 32 57 7c a1 c6
  //   eb 10 35 5a 7f a4 c9 ee 13 38 5d 82 a7 cc f1 16 3b 60 85 aa cf f4 19 3e 63 88 ad d2 f7 1c 41 66 8b
  //   b0 d5 fa 1f 44 69 8e b3 d8 fd 22 47 6c 91 b6 db 0 25 4a 6f 94 b9 de 3 28 4d 72 97 bc e1 6 2b 50 75
  //   9a bf e4 9 2e 53 78 9d c2 e7 c 31 56 7b a0 c5 ea f 34 59 7e a3 c8 ed 12 37 5c 81 a6 cb f0 15 3a 5f
  //   84 a9 ce f3 18 3d 62 87 ac d1 f6 1b 40 65 8a af d4 f9 1e 43 68 8d b2 d7 fc 21 46 6b 90 b5 da ff 24
  //   49 6e 93 b8 dd 2 27 4c 71 96 bb e0 5 2a 4f 74 99 be e3 8 2d 52 77 9c c1 e6 b 30 55 7a 9f c4 e9 e 33
  //   58 7d a2 c7 ec 11 36 5b 80 a5 ca ef 14 39 5e 83 a8 cd f2 17 3c 61 91 b6 db 0 25 4a 6f 94 b9 de 3 28
  //   4d 72 97 bc e1 6 2b 50 75 9a bf e4 9 2e 53 78 9d c2 e7 c 31 56 7b a0 c5 ea f 34 59 7e a3 c8 ed 12 37
  //   5c 81 a6 cb f0 15 3a 5f 84 a9 ce f3 18 3d 62 87 ac d1 f6 1b 40 65 8a af d4 f9 1e 43 68 8d b2 d7 fc
  //   21 46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
  //   AT28C256 (Microchip DS20006386B), read only: 16 images of 32 KiB, IMAGE picks one (0-1 boot ROM, 2-8 microcode, 9-15 erased)
endmodule

module test_at28c256 (
  input  ce_n,
  input  oe_n,
  input  we_n,
  input  [3:0] image,
  input  [14:0] a,
  output [7:0] q
);

  ttlat28c256 U1 (
    .A14(a[14]), .A12(a[12]), .A7(a[7]), .A6(a[6]), .A5(a[5]), .A4(a[4]), .A3(a[3]), .A2(a[2]), .A1(a[1]),
    .A0(a[0]), .I_O0(q[0]), .I_O1(q[1]), .I_O2(q[2]), .I_O3(q[3]), .I_O4(q[4]), .I_O5(q[5]), .I_O6(q[6]),
    .I_O7(q[7]), .nCE(ce_n), .A10(a[10]), .nOE(oe_n), .A11(a[11]), .A9(a[9]), .A8(a[8]), .A13(a[13]),
    .nWE(we_n), .IMAGE(image));  // open: GND, VCC

  // Other names for the same wires on the sheet: a_0 = a[0]; a_1 = a[1]; a_2 = a[2]; a_3 = a[3]; a_4 = a[4];
  //   a_5 = a[5]; a_6 = a[6]; a_7 = a[7]; a_8 = a[8]; a_9 = a[9]; a_10 = a[10]; a_11 = a[11]; a_12 = a[12];
  //   a_13 = a[13]; a_14 = a[14]; q_0 = q[0]; q_1 = q[1]; q_2 = q[2]; q_3 = q[3]; q_4 = q[4]; q_5 = q[5]; q_6 = q[6];
  //   q_7 = q[7]
endmodule
