// Logisim project test_74165.circ as structural Verilog: 1 circuit, main circuit test_74165
module test_74165 (
  input  sh_ld_n,
  input  clk,
  input  clk_inh,
  input  ser,
  input  [7:0] p,
  output qh,
  output qh_n
);

  _74165 U1 (
    .pin1(sh_ld_n), .pin2(clk), .pin3(p[4]), .pin4(p[5]), .pin5(p[6]), .pin6(p[7]), .pin7(qh_n),
    .pin15(clk_inh), .pin14(p[3]), .pin13(p[2]), .pin12(p[1]), .pin11(p[0]), .pin10(ser), .pin9(qh));

  // Other names for the same wires on the sheet: p_0 = p[0]; p_1 = p[1]; p_2 = p[2]; p_3 = p[3]; p_4 = p[4];
  //   p_5 = p[5]; p_6 = p[6]; p_7 = p[7]

  // Notes on the sheet:
  //   Logisim's own 74165: behaviour vs the TI datasheet
endmodule
