// Logisim project test_74377.circ as structural Verilog: 1 circuit, main circuit test_74377
module test_74377 (
  input  cp,
  input  e_n,
  input  [7:0] d,
  output [7:0] q
);

  _74377 U1 (
    .pin1(e_n), .pin2(q[0]), .pin3(d[0]), .pin4(d[1]), .pin5(q[1]), .pin6(q[2]), .pin7(d[2]), .pin8(d[3]),
    .pin9(q[3]), .pin19(q[7]), .pin18(d[7]), .pin17(d[6]), .pin16(q[6]), .pin15(q[5]), .pin14(d[5]),
    .pin13(d[4]), .pin12(q[4]), .pin11(cp));

  // Other names for the same wires on the sheet: d_0 = d[0]; d_1 = d[1]; d_2 = d[2]; d_3 = d[3]; d_4 = d[4];
  //   d_5 = d[5]; d_6 = d[6]; d_7 = d[7]; q_0 = q[0]; q_1 = q[1]; q_2 = q[2]; q_3 = q[3]; q_4 = q[4]; q_5 = q[5];
  //   q_6 = q[6]; q_7 = q[7]

  // Notes on the sheet:
  //   Logisim's own 74377: behaviour vs the TI datasheet
endmodule
