// Logisim project test_74670.circ as structural Verilog: 1 circuit, main circuit test_74670
module test_74670 (
  input  we_n,
  input  re_n,
  input  [1:0] wa,
  input  [1:0] ra,
  input  [3:0] d,
  output [3:0] q
);

  _74670 U1 (
    .pin1(d[1]), .pin2(d[2]), .pin3(d[3]), .pin4(ra[1]), .pin5(ra[0]), .pin6(q[3]), .pin7(q[2]),
    .pin15(d[0]), .pin14(wa[0]), .pin13(wa[1]), .pin12(we_n), .pin11(re_n), .pin10(q[0]), .pin9(q[1]));

  // Other names for the same wires on the sheet: d_0 = d[0]; d_1 = d[1]; d_2 = d[2]; d_3 = d[3]; q_0 = q[0];
  //   q_1 = q[1]; q_2 = q[2]; q_3 = q[3]; ra_0 = ra[0]; ra_1 = ra[1]; wa_0 = wa[0]; wa_1 = wa[1]

  // Notes on the sheet:
  //   Logisim's own 74670: behaviour vs the TI datasheet
endmodule
