// Logisim project cpu.circ as structural Verilog
module alu (
);

  add_sub8 add_sub8_1 ();  // open: add_sub8_Sub, add_sub8_UseC, add_sub8_Cin, add_sub8_A, add_sub8_B, add_sub8_S, add_sub8_C
endmodule

module add_sub8 (
  input  add_sub8_Sub,
  input  add_sub8_UseC,
  input  add_sub8_Cin,
  input  [7:0] add_sub8_A,
  input  [7:0] add_sub8_B,
  output add_sub8_C,
  output [7:0] add_sub8_S
);

  wire n7408_1_pin3, n7408_1_pin4, n7408_1_pin13, n7486_3_pin4, n7486_3_pin10, n74283_1_pin7, n74283_1_pin9,
       n74283_2_pin9;
  wire [7:0] n7486_1_pin11;

  _7486 u_7486_1 (
    .pin1(add_sub8_B[3]), .pin2(add_sub8_Sub), .pin3(n7486_1_pin11[3]), .pin4(add_sub8_Sub),
    .pin5(add_sub8_B[2]), .pin6(n7486_1_pin11[2]), .pin13(add_sub8_B[0]), .pin12(add_sub8_Sub),
    .pin11(n7486_1_pin11[0]), .pin10(add_sub8_Sub), .pin9(add_sub8_B[1]), .pin8(n7486_1_pin11[1]));
  _7486 u_7486_2 (
    .pin1(add_sub8_B[7]), .pin2(add_sub8_Sub), .pin3(n7486_1_pin11[7]), .pin4(add_sub8_Sub),
    .pin5(add_sub8_B[6]), .pin6(n7486_1_pin11[6]), .pin13(add_sub8_B[4]), .pin12(add_sub8_Sub),
    .pin11(n7486_1_pin11[4]), .pin10(add_sub8_Sub), .pin9(add_sub8_B[5]), .pin8(n7486_1_pin11[5]));
  _7408 u_7408_1 (
    .pin1(add_sub8_UseC), .pin2(add_sub8_Cin), .pin3(n7408_1_pin3), .pin4(n7408_1_pin4), .pin5(n7408_1_pin4),
    .pin13(n7408_1_pin13), .pin12(n7408_1_pin13), .pin10(n7408_1_pin13), .pin9(n7408_1_pin13));  // open: pin6, pin11, pin8
  _74283 u_74283_1 (
    .pin1(add_sub8_S[1]), .pin2(n7486_1_pin11[1]), .pin3(add_sub8_A[1]), .pin4(add_sub8_S[0]),
    .pin5(add_sub8_A[0]), .pin6(n7486_1_pin11[0]), .pin7(n74283_1_pin7), .pin15(n7486_1_pin11[2]),
    .pin14(add_sub8_A[2]), .pin13(add_sub8_S[2]), .pin12(add_sub8_A[3]), .pin11(n7486_1_pin11[3]),
    .pin10(add_sub8_S[3]), .pin9(n74283_1_pin9));
  _74283 u_74283_2 (
    .pin1(add_sub8_S[5]), .pin2(n7486_1_pin11[5]), .pin3(add_sub8_A[5]), .pin4(add_sub8_S[4]),
    .pin5(add_sub8_A[4]), .pin6(n7486_1_pin11[4]), .pin7(n74283_1_pin9), .pin15(n7486_1_pin11[6]),
    .pin14(add_sub8_A[6]), .pin13(add_sub8_S[6]), .pin12(add_sub8_A[7]), .pin11(n7486_1_pin11[7]),
    .pin10(add_sub8_S[7]), .pin9(n74283_2_pin9));
  _7486 u_7486_3 (
    .pin1(add_sub8_Sub), .pin2(n74283_2_pin9), .pin3(add_sub8_C), .pin4(n7486_3_pin4), .pin5(n7486_3_pin4),
    .pin13(add_sub8_Sub), .pin12(n7408_1_pin3), .pin11(n74283_1_pin7), .pin10(n7486_3_pin10),
    .pin9(n7486_3_pin10));  // open: pin6, pin8
  // also tied to GND on the sheet: {n7408_1_pin13, n7408_1_pin4, n7486_3_pin10, n7486_3_pin4}
endmodule
