// Logisim project test_cpu.circ as structural Verilog: 1 circuit, main circuit test_cpu
module test_cpu (
  output halt,
  output [5:0] clk,
  output clk_wr_n,
  output clk_mem_wr_n,
  output rst_n,
  output rst_early,
  output rst_rc,
  output [7:0] bus_data,
  output [15:0] bus_addr,
  output [7:0] bus_a,
  output [7:0] bus_b,
  output [7:0] mem_d,
  output [7:0] alu_r,
  output [7:0] flag_reg,
  output addr_cout,
  output [3:0] alu_op,
  output [3:0] flags_op,
  output flags_bit_val,
  output flags_oe_n,
  output regs_we_n,
  output [1:0] regs_a_sel,
  output [1:0] regs_cu_idx,
  output [1:0] regs_cu_bank_n,
  output [1:0] regs_b_sel,
  output regs_a_lat_oe_n,
  output regs_b_lat_oe_n,
  output regs_const_oe_n,
  output regs_const_0,
  output regs_a_bus_oe_n,
  output regs_res_oe_n,
  output [1:0] addr_base_sel,
  output [1:0] addr_base_oe_n,
  output addr_off_sel,
  output [1:0] addr_off_oe_n,
  output addr_inv,
  output addr_cin,
  output addr_lat_ld_n,
  output addr_pc_ld_n,
  output addr_sp_ld_n,
  output [1:0] addr_lat_oe_n,
  output [1:0] addr_pc_oe_n,
  output [1:0] addr_sp_oe_n,
  output ir_b0_ld_n,
  output ir_b1_ld_n,
  output ir_v1_ld_n,
  output ir_v2_ld_n,
  output mem_re,
  output mem_oe_n,
  output mem_we_n,
  output mem_wbuf_oe_n,
  output mem_rom_oe_n,
  output ie,
  output rw,
  output inr,
  output [5:0] ir_op,
  output [3:0] ir_mode,
  output [2:0] ir_r1,
  output [2:0] ir_r2,
  output [2:0] ir_r3,
  output ir_r1_2_n,
  output ir_r2_2_n,
  output ir_r3_2_n,
  output [7:0] ir_v1,
  output [7:0] ir_v2,
  output \int ,
  output vec
);

  wire arm, arm_n, fire, hold, in_rd, inr_n, int_d, int_d_n, int_d_na, int_d_nb, osc, port_rd, port_rd_n,
       port_rd_na, port_rd_nb, port_we, rc, rc_tc, rw_n, trig_port, U1_pin1, U1_pin3, U1_pin4, U1_pin5,
       U1_pin6, U1_pin7, U1_pin9, U1_pin10, U2_pin1, U2_pin2, U2_pin4, U2_pin10, U2_pin11, U2_pin12,
       U2_pin13, vec_d, wr;
  wire [3:0] pport;
  wire [7:0] cnt, cnt_d, dec_q, iod_bus_addr_lo, iod_bus_data, port_q;
  wire [7:1] one_q;

  Clock clock_1 (.out(osc));
  _74161 U1 (
    .pin1(U1_pin1), .pin2(osc), .pin3(U1_pin3), .pin4(U1_pin4), .pin5(U1_pin5), .pin6(U1_pin6),
    .pin7(U1_pin7), .pin15(rc_tc), .pin10(U1_pin10), .pin9(U1_pin9));  // open: pin14, pin13, pin12, pin11
  _7474 U2 (
    .pin1(U2_pin1), .pin2(U2_pin2), .pin3(rc_tc), .pin4(U2_pin4), .pin5(rc), .pin13(U2_pin13),
    .pin12(U2_pin12), .pin11(U2_pin11), .pin10(U2_pin10));  // open: pin6, pin9, pin8
  not not_1 (rw_n, rw);
  not not_2 (wr, clk_wr_n);
  not not_3 (inr_n, inr);
  and and_1 (port_we, ie, rw_n, wr, 1'b1);
  and and_2 (in_rd, ie, rw, 1'b1, 1'b1);
  and and_3 (trig_port, bus_addr[4], bus_addr[5], bus_addr[6], bus_addr[7]);
  and and_4 (arm, ie, rw_n, trig_port, 1'b1);
  not not_4 (arm_n, arm);
  and and_5 (hold, \int , inr_n, 1'b1, 1'b1);
  and and_6 (vec_d, \int , inr, 1'b1, 1'b1);
  not not_5 (port_rd_na, in_rd);
  not not_6 (port_rd_nb, vec);
  not not_7 (int_d_na, fire);
  not not_8 (int_d_nb, hold);
  and and_7 (port_rd_n, port_rd_na, port_rd_nb, 1'b1, 1'b1);
  assign cnt_d = arm ? bus_data : 8'bz;  // Controlled_Buffer controlled_buffer_1
  assign cnt_d = arm_n ? dec_q : 8'bz;  // Controlled_Buffer controlled_buffer_2
  and and_8 (int_d_n, int_d_na, int_d_nb, 1'b1, 1'b1);
  not not_9 (port_rd, port_rd_n);
  not not_10 (int_d, int_d_n);
  RAM #(.addrWidth(8), .dataWidth(8), .databus("bibus"), .enables("byte"), .trigger("high"), .\type ("volatile")) ram_1 (
    .addr(bus_addr[7:0]), .we(port_we), .oe(1'b1), .din(bus_data), .dout(port_q));
  Register #(.width(8)) register_1 (.D(cnt_d), .en(1'b1), .clk(clk[5]), .Q(cnt), .clr(1'b0));
  Register #(.width(4)) register_2 (.D(bus_addr[3:0]), .en(arm), .clk(clk[5]), .Q(pport), .clr(1'b0));
  D_Flip_Flop d_ff_1 (.D(int_d), .clk(clk[5]), .Q(\int ), .preset(1'b0), .reset(1'b0));  // open: Qn
  D_Flip_Flop d_ff_2 (.D(vec_d), .clk(clk[5]), .Q(vec), .preset(1'b0), .reset(1'b0));  // open: Qn
  cpu_main main_1 (
    .osc(osc), .rc(rc), .\int (\int ), .iod_bus_data(iod_bus_data), .iod_bus_addr_lo(iod_bus_addr_lo),
    .clk(clk), .clk_wr_n(clk_wr_n), .clk_mem_wr_n(clk_mem_wr_n), .rst_n(rst_n), .rst_early(rst_early),
    .rst_rc(rst_rc), .bus_data(bus_data), .bus_addr(bus_addr), .bus_a(bus_a), .bus_b(bus_b), .mem_d(mem_d),
    .alu_r(alu_r), .out_18(flag_reg), .addr_cout(addr_cout), .alu_op(alu_op), .flags_op(flags_op),
    .flags_bit_val(flags_bit_val), .flags_oe_n(flags_oe_n), .regs_we_n(regs_we_n), .regs_a_sel(regs_a_sel),
    .regs_cu_idx(regs_cu_idx), .regs_cu_bank_n(regs_cu_bank_n), .regs_b_sel(regs_b_sel),
    .regs_a_lat_oe_n(regs_a_lat_oe_n), .regs_b_lat_oe_n(regs_b_lat_oe_n), .regs_const_oe_n(regs_const_oe_n),
    .regs_const_0(regs_const_0), .regs_a_bus_oe_n(regs_a_bus_oe_n), .regs_res_oe_n(regs_res_oe_n),
    .addr_base_sel(addr_base_sel), .addr_base_oe_n(addr_base_oe_n), .addr_off_sel(addr_off_sel),
    .addr_off_oe_n(addr_off_oe_n), .addr_inv(addr_inv), .addr_cin(addr_cin), .addr_lat_ld_n(addr_lat_ld_n),
    .addr_pc_ld_n(addr_pc_ld_n), .addr_sp_ld_n(addr_sp_ld_n), .addr_lat_oe_n(addr_lat_oe_n),
    .addr_pc_oe_n(addr_pc_oe_n), .addr_sp_oe_n(addr_sp_oe_n), .ir_b0_ld_n(ir_b0_ld_n),
    .ir_b1_ld_n(ir_b1_ld_n), .ir_v1_ld_n(ir_v1_ld_n), .ir_v2_ld_n(ir_v2_ld_n), .mem_re(mem_re),
    .mem_oe_n(mem_oe_n), .mem_we_n(mem_we_n), .mem_wbuf_oe_n(mem_wbuf_oe_n), .mem_rom_oe_n(mem_rom_oe_n),
    .ie(ie), .rw(rw), .inr(inr), .ir_op(ir_op), .ir_mode(ir_mode), .ir_r1(ir_r1), .ir_r2(ir_r2),
    .ir_r3(ir_r3), .ir_r1_2_n(ir_r1_2_n), .ir_r2_2_n(ir_r2_2_n), .ir_r3_2_n(ir_r3_2_n), .ir_v1(ir_v1),
    .ir_v2(ir_v2));
  assign iod_bus_data = port_rd ? port_q : 8'bz;  // Controlled_Buffer controlled_buffer_3
  ROM #(.addrWidth(8), .dataWidth(8)) rom_1 (.addr(cnt), .data(dec_q));
  ROM #(.addrWidth(8), .dataWidth(8)) rom_2 (.addr(cnt), .data({one_q, fire}));
  assign iod_bus_addr_lo = vec ? {4'b0000, pport} : 8'bz;  // Controlled_Buffer controlled_buffer_4

  assign halt = 1'b0;
  // also tied to GND on the sheet: {U1_pin3, U1_pin4, U1_pin5, U1_pin6, U2_pin12, U2_pin11}
  // also tied to VCC on the sheet: {U1_pin1, U1_pin7, U2_pin1, U2_pin2, U2_pin4, U1_pin10, U1_pin9, U2_pin13, U2_pin10}

  // Other names for the same wires on the sheet: lo[7:0] = bus_addr[7:0]; lo4[3:0] = bus_addr[3:0];
  //   lo_4 = bus_addr[4]; lo_5 = bus_addr[5]; lo_6 = bus_addr[6]; lo_7 = bus_addr[7]; clk_5 = clk[5]; one_q[0] = fire;
  //   vec_addr[3:0] = pport

  // Notes on the sheet:
  //   reset RC: rc rises after 15 osc periods
  //   IOD stub: OUT Fp, v (v > 0) raises INT v steps later for port p; vector step: 00:p, latch p
  //   IOD stub: port latches (OUT writes, IN and the vector step read)
  //   contents of rom_1 (hex, n*v repeats v):
  //   0 0 1 2 3 4 5 6 7 8 9 a b c d e f 10 11 12 13 14 15 16 17 18 19 1a 1b 1c 1d 1e 1f 20 21 22 23 24 25
  //   26 27 28 29 2a 2b 2c 2d 2e 2f 30 31 32 33 34 35 36 37 38 39 3a 3b 3c 3d 3e 3f 40 41 42 43 44 45 46
  //   47 48 49 4a 4b 4c 4d 4e 4f 50 51 52 53 54 55 56 57 58 59 5a 5b 5c 5d 5e 5f 60 61 62 63 64 65 66 67
  //   68 69 6a 6b 6c 6d 6e 6f 70 71 72 73 74 75 76 77 78 79 7a 7b 7c 7d 7e 7f 80 81 82 83 84 85 86 87 88
  //   89 8a 8b 8c 8d 8e 8f 90 91 92 93 94 95 96 97 98 99 9a 9b 9c 9d 9e 9f a0 a1 a2 a3 a4 a5 a6 a7 a8 a9
  //   aa ab ac ad ae af b0 b1 b2 b3 b4 b5 b6 b7 b8 b9 ba bb bc bd be bf c0 c1 c2 c3 c4 c5 c6 c7 c8 c9 ca
  //   cb cc cd ce cf d0 d1 d2 d3 d4 d5 d6 d7 d8 d9 da db dc dd de df e0 e1 e2 e3 e4 e5 e6 e7 e8 e9 ea eb
  //   ec ed ee ef f0 f1 f2 f3 f4 f5 f6 f7 f8 f9 fa fb fc fd fe
  //   contents of rom_2 (hex, n*v repeats v):
  //   0 1 0 0 0 0 0 0 0 0 0 0 0 0 0 0 0 0 0 0 0 0 0 0 0 0 0 0 0 0 0 0 0 0 0 0 0 0 0 0 0 0 0 0 0 0 0 0 0 0
  //   0 0 0 0 0 0 0 0 0 0 0 0 0 0 0 0 0 0 0 0 0 0 0 0 0 0 0 0 0 0 0 0 0 0 0 0 0 0 0 0 0 0 0 0 0 0 0 0 0 0
  //   0 0 0 0 0 0 0 0 0 0 0 0 0 0 0 0 0 0 0 0 0 0 0 0 0 0 0 0 0 0 0 0 0 0 0 0 0 0 0 0 0 0 0 0 0 0 0 0 0 0
  //   0 0 0 0 0 0 0 0 0 0 0 0 0 0 0 0 0 0 0 0 0 0 0 0 0 0 0 0 0 0 0 0 0 0 0 0 0 0 0 0 0 0 0 0 0 0 0 0 0 0
  //   0 0 0 0 0 0 0 0 0 0 0 0 0 0 0 0 0 0 0 0 0 0 0 0 0 0 0 0 0 0 0 0 0 0 0 0 0 0 0 0 0 0 0 0 0 0 0 0 0 0
  //   0 0 0 0 0 0
endmodule
