// Logisim project clkgen.circ as structural Verilog: 1 circuit, main circuit clkgen
module clkgen (
  input  clkgen_osc,
  input  clkgen_rc,
  output [5:0] clk,
  output clk_wr_n,
  output clk_mem_wr_n,
  output rst_n,
  output rst_early,
  output rst_rc
);

  wire clkgen_clk_n, clkgen_clk_q, clkgen_osc_n, clkgen_q2, clkgen_q2_n, clkgen_rst_clr_n,
       clkgen_rst_early_n, clkgen_wr_n, U1_pin1, U1_pin4, U1_pin10, U1_pin13, U2_pin4, U2_pin5, U2_pin9,
       U2_pin10, U2_pin11, U3_pin1, U3_pin19, U4_pin5, U4_pin9, U4_pin11, U4_pin13, U5_pin2, U5_pin4,
       U5_pin10;

  _7474 U1 (
    .pin1(U1_pin1), .pin2(clkgen_clk_n), .pin3(clkgen_osc), .pin4(U1_pin4), .pin5(clkgen_clk_q),
    .pin6(clkgen_clk_n), .pin13(U1_pin13), .pin12(clkgen_clk_q), .pin11(clkgen_osc_n), .pin10(U1_pin10),
    .pin9(clkgen_q2), .pin8(clkgen_q2_n));
  _7414 U4 (
    .pin1(clkgen_rc), .pin2(rst_rc), .pin3(rst_rc), .pin4(clkgen_rst_clr_n), .pin5(U4_pin5),
    .pin13(U4_pin13), .pin11(U4_pin11), .pin9(U4_pin9));  // open: pin6, pin12, pin10, pin8
  _7410 U2 (
    .pin1(clkgen_clk_n), .pin2(clkgen_osc), .pin3(clkgen_osc), .pin4(U2_pin4), .pin5(U2_pin5),
    .pin6(clkgen_osc_n), .pin13(clkgen_q2), .pin12(clkgen_wr_n), .pin11(U2_pin11), .pin10(U2_pin10),
    .pin9(U2_pin9));  // open: pin8
  _7474 U5 (
    .pin1(clkgen_rst_clr_n), .pin2(U5_pin2), .pin3(clk[5]), .pin4(U5_pin4), .pin5(clkgen_rst_early_n),
    .pin6(rst_early), .pin13(clkgen_rst_clr_n), .pin12(clkgen_rst_early_n), .pin11(clk[5]), .pin10(U5_pin10),
    .pin9(rst_n));  // open: pin8
  _74541 U3 (
    .pin1(U3_pin1), .pin2(clkgen_clk_q), .pin3(clkgen_clk_q), .pin4(clkgen_clk_q), .pin5(clkgen_clk_q),
    .pin6(clkgen_clk_q), .pin7(clkgen_clk_q), .pin8(clkgen_wr_n), .pin9(clkgen_q2_n), .pin19(U3_pin19),
    .pin18(clk[0]), .pin17(clk[1]), .pin16(clk[2]), .pin15(clk[3]), .pin14(clk[4]), .pin13(clk[5]),
    .pin12(clk_wr_n), .pin11(clk_mem_wr_n));
  // also tied to GND on the sheet: {U4_pin5, U4_pin13, U4_pin11, U4_pin9, U2_pin11, U2_pin10, U2_pin9, U3_pin1, U3_pin19}
  // also tied to VCC on the sheet: {U1_pin1, U1_pin4, U1_pin13, U1_pin10, U2_pin4, U2_pin5, U5_pin2, U5_pin4, U5_pin10}

  // Other names for the same wires on the sheet: clk_0 = clk[0]; clk_1 = clk[1]; clk_2 = clk[2]; clk_3 = clk[3];
  //   clk_4 = clk[4]; clk_5 = clk[5]

  // Notes on the sheet:
  //   clock: FF1 = clk (osc / 2), FF2 = clk on the osc fall (C6)
  //   reset: RC -> rst_rc -> /CLR (C17, C24)
  //   clk bits: 0 ir, 1 addr, 2 cu (574s 1-5), 3 cu (574s 6-8, 175s, 377), 4 regs + flags, 5 the reset flip-flops + the IOD (cu-decisions.md section 14)
  //   clk_wr_n = NAND3(clk_n, osc, Q2); NOT osc for FF2
  //   reset synchroniser: FF1 rst_early, FF2 rst_n (C17)
  //   clock buffer: 6 clk branches, clk_wr_n, clk_mem_wr_n
endmodule
