// Logisim project cu.circ as structural Verilog: 1 circuit, main circuit cu
module cu (
  input  [1:0] clk,
  input  rst_n,
  input  rst_early,
  input  rst_rc,
  input  [7:0] cu_bus_in,
  input  [5:0] cu_ir_op,
  input  [3:0] cu_ir_mode,
  input  cu_flag_c,
  input  cu_flag_e,
  input  cu_flag_i,
  input  cu_flag_n,
  input  cu_flag_s,
  input  cu_flag_z,
  input  cu_flag_f,
  input  cu_flag_h,
  input  cu_int,
  input  cu_addr_cout,
  output [3:0] cu_alu_op,
  output [3:0] cu_flags_op,
  output cu_flags_bit_val,
  output cu_flags_oe_n,
  output cu_regs_we_n,
  output [1:0] cu_regs_a_sel,
  output [1:0] cu_regs_cu_idx,
  output [1:0] cu_regs_cu_bank_n,
  output [1:0] cu_regs_b_sel,
  output cu_regs_a_lat_oe_n,
  output cu_regs_b_lat_oe_n,
  output cu_regs_const_oe_n,
  output cu_regs_const_0,
  output cu_regs_a_bus_oe_n,
  output cu_regs_res_oe_n,
  output [1:0] cu_addr_base_sel,
  output [1:0] cu_addr_base_oe_n,
  output cu_addr_off_sel,
  output [1:0] cu_addr_off_oe_n,
  output cu_addr_inv,
  output cu_addr_cin,
  output cu_addr_lat_ld_n,
  output cu_addr_pc_ld_n,
  output cu_addr_sp_ld_n,
  output [1:0] cu_addr_lat_oe_n,
  output [1:0] cu_addr_pc_oe_n,
  output [1:0] cu_addr_sp_oe_n,
  output cu_ir_b0_ld_n,
  output cu_ir_b1_ld_n,
  output cu_ir_v1_ld_n,
  output cu_ir_v2_ld_n,
  output cu_mem_re,
  output cu_mem_oe_n,
  output cu_mem_we_n,
  output cu_mem_wbuf_oe_n,
  output cu_mem_rom_oe_n,
  output cu_ie,
  output cu_rw,
  output cu_inr,
  output [7:0] cu_bus_addr_lo
);

  wire cu_a_0, cu_a_1, cu_a_2, cu_a_3, cu_a_4, cu_a_5, cu_a_6, cu_a_7, cu_a_8, cu_a_9, cu_a_10, cu_a_11,
       cu_a_12, cu_a_13, cu_a_14, cu_ab0_n, cu_ab1_n, cu_alat_oe_n_d, cu_blat_oe_n_d, cu_bnd_n, cu_bsel3,
       cu_cond_sel_0, cu_cond_sel_1, cu_const_0_d, cu_cout_q, cu_dbus_n_1, cu_dbus_n_2, cu_dbus_n_3,
       cu_dbus_n_4, cu_dbus_n_5, cu_dbus_n_6, cu_dbus_n_7, cu_force, cu_hw, cu_hw_q, cu_ie_d, cu_jc,
       cu_lat_hi_off, cu_p, cu_p_kept, cu_p_next, cu_p_nor, cu_rom_0, cu_rom_1, cu_rom_2, cu_rom_3, cu_rom_4,
       cu_rom_5, cu_rom_6, cu_rom_7, cu_rom_8, cu_rom_9, cu_rom_10, cu_rom_11, cu_rom_12, cu_rom_13,
       cu_rom_14, cu_rom_15, cu_rom_16, cu_rom_17, cu_rom_18, cu_rom_19, cu_rom_20, cu_rom_21, cu_rom_22,
       cu_rom_23, cu_rom_24, cu_rom_25, cu_rom_26, cu_rom_27, cu_rom_28, cu_rom_29, cu_rom_30, cu_rom_31,
       cu_rom_32, cu_rom_33, cu_rom_34, cu_rom_35, cu_rom_36, cu_rom_37, cu_rom_38, cu_rom_39, cu_rom_40,
       cu_rom_41, cu_rom_42, cu_rom_43, cu_rom_44, cu_rom_45, cu_rom_46, cu_rom_47, cu_rom_48, cu_rom_49,
       cu_rom_50, cu_rom_51, cu_rom_52, cu_rom_53, cu_sw, cu_swi_0, cu_swi_1, cu_swi_2, cu_swi_3, cu_swi_4,
       cu_swi_5, cu_swi_6, cu_swi_7, cu_swi_ld, cu_swi_ld_n, cu_swi_oe_n, cu_swi_oe_n_d, cu_x_n, U3_pin10,
       U3_pin11, U3_pin13, U3_pin14, U4_pin1, U4_pin7, U4_pin12, U5_pin1, U5_pin10, U5_pin11, U5_pin12,
       U5_pin13, U5_pin15, U14_pin4, U14_pin5, U14_pin6, U16_pin9, U16_pin10, U16_pin12, U16_pin13,
       U17_pin13, U18_pin12, U18_pin13, U19_pin11, U28_pin13, U30_pin19;

  // Image #(.height(29), .image("data:image/png;base64,iVBORw0KGgoAAAANSUhEUgAAAI0AAAAdCAYAAACXOO/mAAACO0lEQVR4Xu2YwW7CMAyGK3HYoRLltMfbY+2BBkIT4gzPwROwBDVd8OLfdUnTVPMn+UD+2LO9NDU0jWEYhmEYmdnsdruPruuuzu7b7XYfi/4zXVsDbdu+u3rOa8y9elxTv/xhCUabHNbjtTXgcj6tNffqCY31t437uOF0ul47dmhmRGqspNeKvZ5mRDoUkm7My9PAGdnBPxV0MxpAkTYG70tyGIzGlQ5N/0QfSJwr97qL4Ppxczl8081TeLVPi0MHTmInuj9odN2DtDHkPDQ+dxojsiPdHxD6wf49DTljFad/Gh8FxE8geu+igpGmRYol6f0BPEe3ZbhBWD+hH6yflpyxitP9Xt8HqnGggpGmRYol6RzID/UD+WnJGas4IfnU7MKBCkaaFimWpKeQbgzUD+SnJWes4kxJHvkgTYsUS9A3TjuGPSmjDp6pmpacsYozJXnkgzQtUiykx7MLZ9THM1XTkjNWcaLk0VfQJ1DBSNMixUK6W794rR9mqYb82H4gPy05YxUHNZejlsaOzOMNaH9A/UB+WnLGKk50jV+oxsE1VhoytUixuDxGaGxc1A/kpyVnrCXwA+OjgJSlfqeZOi9okWLFedA8X8gR9gP4qcgZaxE0v8L2oG8mJX9qH/JI7EM5+v03sn8A9cMb3T+FEbX9T6Tmp6ziRg43UFjQ1ldxbfWgbWrNjU3NOtr6aq3NmAl/WPw/PjVYGwa8QZrE13vDYA/NrK+Xz2bv7L6QzVeXMSN2aAzDMAwD8QN7p1WWOXyw8AAAAABJRU5ErkJggg=="), .license("Unspecified"), .width(141)) image_1: pin names not known
  // Image #(.height(29), .image("data:image/png;base64,iVBORw0KGgoAAAANSUhEUgAAAK0AAAAdCAYAAADYZew2AAADUElEQVR4Xu2ZXWoUQRDHN9kHYZfdWVgQ11vkFAEP4Yt4CUW8RU6hID54ALMJQSQvQvZFBI+QB18Uslat3Utb2//qmcqi6Uz9oMhMfXRP1dTMdk8GA8dxHMdxHOcuMZ1OT1mkXsMSY2U8Hj9smuYzCx9Lu9NDqBnWLFKvYYmxQvN8ivPxsbQ7PcTSgJYYK960zg6WBrTEWPHlgbODpQEtMc6/YTibzZ7SzVklP08sS/TEow0K0lsIb55l22uKgLhtbtI/gGoAY2Kucr7b5K/VL9guRG4rvm4yD3P+ZD+nw0NhOiD9GZqnCujiP8qblEh2bRXtbfUWeO7M9XBTfEGNy3q2y5hUZAxTqEE2Jr2e1Pc2zdBmvpzQnJeyJqT/GmzHQn8U9N9TfTWEt8Qm8fSJjesrdANQcZHeQnhTbNd3oiGX0j+1i8aOb9HstRVqkI1hoi3IajQaPZI+XWkzX5LbJi86/xZsf9WE9C+D/xuhfx38T1J9NXCiuYRLoOIi/b7QGinmIho2tatxuRqgGCba0HwW2swn50I14YeIdD9Jfs3n88dR3/zZ7K0nk8mT1L8aUCFK5Iqk6fcFukFMKRdLHIphtDgrbeaTegbZ6IF6y3r6+4LPqZEXdH5D5z8Wi8VI+lcBSrYEikN6A0Ma5zyOlxMZgPQRZEd6xmqzoo1psVFzHrOelxB0ekjHz8P5O+lbDSjZEigO6buSrkGRyBikjyA70jNWmxVtTKONvxRsN2Qk74PvM+lYDUmyO59MNFCRkL4rNMYVjxM2RtKWnaOUiyUOxTCazYo2ptXGS4Ng/8DLAvp7w8sE6VcNjdIcGqhISN+VZJwHik3q1VwscSiG0WxWtDGttmRDtvFpwGfMakh+hq+kTSNXJG2T1BW+Hh6nSyPFXHj9ltscleJyNUAxjGazoo1ptTFxQxbq80raa4M3PPEJ3JFp4TstEunfFcualhjS9V5KPykyaFCoAYgpNooFbUyrjYkbsiBH0l4d3JjyJkVBTavEXJPtQvobUL8e0BzXMoAJb3v5L9xinJKPGoPqY0Ub02oL8JcDrucZHR9Io5OgNUNOCoWvgj7mfK/o4w3sY86O4zjOfjgZnJKs/5P4z5FjwJvWcRzHcRzHqY/fz//eruyibb8AAAAASUVORK5CYII="), .license("Unspecified"), .width(173)) image_2: pin names not known
  ttl74574 U20 (
    .nOE(rst_rc), .D0(cu_rom_0), .D1(cu_rom_1), .D2(cu_rom_2), .D3(cu_rom_3), .D4(cu_rom_4), .D5(cu_rom_5),
    .D6(cu_rom_6), .D7(cu_rom_7), .CP(clk[0]), .Q7(cu_flags_op[3]), .Q6(cu_flags_op[2]), .Q5(cu_flags_op[1]),
    .Q4(cu_flags_op[0]), .Q3(cu_alu_op[3]), .Q2(cu_alu_op[2]), .Q1(cu_alu_op[1]), .Q0(cu_alu_op[0]));  // open: GND, VCC
  _74157 U1 (
    .pin1(cu_ir_b0_ld_n), .pin2(cu_bus_in[2]), .pin3(cu_ir_op[0]), .pin4(cu_a_9), .pin5(cu_bus_in[3]),
    .pin6(cu_ir_op[1]), .pin7(cu_a_10), .pin15(cu_force), .pin14(cu_bus_in[5]), .pin13(cu_ir_op[3]),
    .pin12(cu_a_12), .pin11(cu_bus_in[4]), .pin10(cu_ir_op[2]), .pin9(cu_a_11));
  ttlat28c256 U7 (
    .A14(cu_a_14), .A12(cu_a_12), .A7(cu_a_7), .A6(cu_a_6), .A5(cu_a_5), .A4(cu_a_4), .A3(cu_a_3),
    .A2(cu_a_2), .A1(cu_a_1), .A0(cu_a_0), .I_O0(cu_rom_0), .I_O1(cu_rom_1), .I_O2(cu_rom_2),
    .I_O3(cu_rom_3), .I_O4(cu_rom_4), .I_O5(cu_rom_5), .I_O6(cu_rom_6), .I_O7(cu_rom_7), .nCE(1'b0),
    .A10(cu_a_10), .nOE(1'b0), .A11(cu_a_11), .A9(cu_a_9), .A8(cu_a_8), .A13(cu_a_13), .nWE(1'b1),
    .IMAGE(4'b0010));  // open: GND, VCC
  _74138 U14 (
    .pin1(cu_rom_19), .pin2(cu_rom_20), .pin3(cu_rom_21), .pin4(U14_pin4), .pin5(U14_pin5), .pin6(U14_pin6),
    .pin7(cu_dbus_n_7), .pin14(cu_dbus_n_1), .pin13(cu_dbus_n_2), .pin12(cu_dbus_n_3), .pin11(cu_dbus_n_4),
    .pin10(cu_dbus_n_5), .pin9(cu_dbus_n_6));  // open: pin15
  _74175 U28 (
    .pin1(rst_n), .pin2(cu_hw_q), .pin4(cu_hw), .pin5(cu_addr_cout), .pin7(cu_cout_q), .pin13(U28_pin13),
    .pin12(cu_p_next), .pin10(cu_p), .pin9(clk[1]));  // open: pin3, pin6, pin15, pin14, pin11
  _74157 U2 (
    .pin1(cu_ir_b0_ld_n), .pin2(cu_bus_in[6]), .pin3(cu_ir_op[4]), .pin4(cu_a_13), .pin5(cu_bus_in[7]),
    .pin6(cu_ir_op[5]), .pin7(cu_a_14), .pin15(cu_force), .pin14(cu_bus_in[1]), .pin13(cu_ir_mode[3]),
    .pin12(cu_a_8), .pin11(cu_bus_in[0]), .pin10(cu_ir_mode[2]), .pin9(cu_a_7));
  _7408 U15 (
    .pin1(cu_rom_23), .pin2(cu_ab0_n), .pin3(cu_lat_hi_off), .pin4(cu_ab1_n), .pin5(cu_rom_22),
    .pin6(cu_ie_d), .pin13(cu_p), .pin12(cu_flag_i), .pin11(cu_sw), .pin10(cu_int), .pin9(cu_flag_i),
    .pin8(cu_hw));
  _74377 U29 (
    .pin1(cu_swi_ld_n), .pin2(cu_swi_0), .pin3(cu_bus_in[0]), .pin4(cu_bus_in[1]), .pin5(cu_swi_1),
    .pin6(cu_swi_2), .pin7(cu_bus_in[2]), .pin8(cu_bus_in[3]), .pin9(cu_swi_3), .pin19(cu_swi_7),
    .pin18(cu_bus_in[7]), .pin17(cu_bus_in[6]), .pin16(cu_swi_6), .pin15(cu_swi_5), .pin14(cu_bus_in[5]),
    .pin13(cu_bus_in[4]), .pin12(cu_swi_4), .pin11(clk[1]));
  ttl74574 U21 (
    .nOE(rst_rc), .D0(cu_rom_8), .D1(cu_dbus_n_3), .D2(cu_rom_9), .D3(cu_rom_10), .D4(cu_rom_11),
    .D5(cu_rom_12), .D6(cu_rom_13), .D7(cu_rom_14), .CP(clk[0]), .Q7(cu_regs_cu_bank_n[0]),
    .Q6(cu_regs_cu_idx[1]), .Q5(cu_regs_cu_idx[0]), .Q4(cu_regs_a_sel[1]), .Q3(cu_regs_a_sel[0]),
    .Q2(cu_regs_we_n), .Q1(cu_flags_oe_n), .Q0(cu_flags_bit_val));  // open: GND, VCC
  ttlat28c256 U8 (
    .A14(cu_a_14), .A12(cu_a_12), .A7(cu_a_7), .A6(cu_a_6), .A5(cu_a_5), .A4(cu_a_4), .A3(cu_a_3),
    .A2(cu_a_2), .A1(cu_a_1), .A0(cu_a_0), .I_O0(cu_rom_8), .I_O1(cu_rom_9), .I_O2(cu_rom_10),
    .I_O3(cu_rom_11), .I_O4(cu_rom_12), .I_O5(cu_rom_13), .I_O6(cu_rom_14), .I_O7(cu_rom_15), .nCE(1'b0),
    .A10(cu_a_10), .nOE(1'b0), .A11(cu_a_11), .A9(cu_a_9), .A8(cu_a_8), .A13(cu_a_13), .nWE(1'b1),
    .IMAGE(4'b0011));  // open: GND, VCC
  _74157 U3 (
    .pin1(cu_ir_b1_ld_n), .pin2(cu_bus_in[6]), .pin3(cu_ir_mode[0]), .pin4(cu_a_5), .pin5(cu_bus_in[7]),
    .pin6(cu_ir_mode[1]), .pin7(cu_a_6), .pin15(cu_force), .pin14(U3_pin14), .pin13(U3_pin13),
    .pin11(U3_pin11), .pin10(U3_pin10));  // open: pin12, pin9
  _7408 U16 (
    .pin1(cu_rom_16), .pin2(cu_rom_17), .pin3(cu_bsel3), .pin4(cu_p), .pin5(cu_swi_oe_n), .pin6(cu_p_kept),
    .pin13(U16_pin13), .pin12(U16_pin12), .pin10(U16_pin10), .pin9(U16_pin9));  // open: pin11, pin8
  _74541 U30 (
    .pin1(cu_swi_oe_n), .pin2(cu_swi_0), .pin3(cu_swi_1), .pin4(cu_swi_2), .pin5(cu_swi_3), .pin6(cu_swi_4),
    .pin7(cu_swi_5), .pin8(cu_swi_6), .pin9(cu_swi_7), .pin19(U30_pin19), .pin18(cu_bus_addr_lo[0]),
    .pin17(cu_bus_addr_lo[1]), .pin16(cu_bus_addr_lo[2]), .pin15(cu_bus_addr_lo[3]),
    .pin14(cu_bus_addr_lo[4]), .pin13(cu_bus_addr_lo[5]), .pin12(cu_bus_addr_lo[6]), .pin11(cu_bus_addr_lo[7]));
  ttl74574 U22 (
    .nOE(rst_rc), .D0(cu_rom_15), .D1(cu_rom_16), .D2(cu_rom_17), .D3(cu_alat_oe_n_d), .D4(cu_blat_oe_n_d),
    .D5(cu_rom_18), .D6(cu_const_0_d), .D7(cu_dbus_n_1), .CP(clk[0]), .Q7(cu_regs_a_bus_oe_n),
    .Q6(cu_regs_const_0), .Q5(cu_regs_const_oe_n), .Q4(cu_regs_b_lat_oe_n), .Q3(cu_regs_a_lat_oe_n),
    .Q2(cu_regs_b_sel[1]), .Q1(cu_regs_b_sel[0]), .Q0(cu_regs_cu_bank_n[1]));  // open: GND, VCC
  ttlat28c256 U9 (
    .A14(cu_a_14), .A12(cu_a_12), .A7(cu_a_7), .A6(cu_a_6), .A5(cu_a_5), .A4(cu_a_4), .A3(cu_a_3),
    .A2(cu_a_2), .A1(cu_a_1), .A0(cu_a_0), .I_O0(cu_rom_16), .I_O1(cu_rom_17), .I_O2(cu_rom_18),
    .I_O3(cu_rom_19), .I_O4(cu_rom_20), .I_O5(cu_rom_21), .I_O6(cu_rom_22), .I_O7(cu_rom_23), .nCE(1'b0),
    .A10(cu_a_10), .nOE(1'b0), .A11(cu_a_11), .A9(cu_a_9), .A8(cu_a_8), .A13(cu_a_13), .nWE(1'b1),
    .IMAGE(4'b0100));  // open: GND, VCC
  _74151 U4 (
    .pin1(U4_pin1), .pin2(cu_flag_f), .pin3(cu_flag_z), .pin4(cu_flag_s), .pin5(cu_jc), .pin7(U4_pin7),
    .pin15(cu_flag_c), .pin14(cu_flag_e), .pin13(cu_flag_n), .pin12(U4_pin12), .pin11(cu_ir_op[0]),
    .pin10(cu_ir_op[1]), .pin9(cu_ir_op[2]));  // open: pin6
  _7414 U17 (
    .pin1(cu_rom_3), .pin2(cu_const_0_d), .pin3(cu_rom_22), .pin4(cu_ab0_n), .pin5(cu_rom_23),
    .pin6(cu_ab1_n), .pin13(U17_pin13), .pin11(cu_p_nor), .pin10(cu_p_next), .pin9(cu_swi_ld_n),
    .pin8(cu_swi_ld));  // open: pin12
  ttl74574 U23 (
    .nOE(rst_rc), .D0(cu_dbus_n_2), .D1(cu_rom_24), .D2(cu_rom_25), .D3(cu_rom_26), .D4(cu_rom_27),
    .D5(cu_rom_28), .D6(cu_rom_29), .D7(cu_rom_30), .CP(clk[0]), .Q7(cu_addr_off_oe_n[1]),
    .Q6(cu_addr_off_oe_n[0]), .Q5(cu_addr_off_sel), .Q4(cu_addr_base_oe_n[1]), .Q3(cu_addr_base_oe_n[0]),
    .Q2(cu_addr_base_sel[1]), .Q1(cu_addr_base_sel[0]), .Q0(cu_regs_res_oe_n));  // open: GND, VCC
  ttlat28c256 U10 (
    .A14(cu_a_14), .A12(cu_a_12), .A7(cu_a_7), .A6(cu_a_6), .A5(cu_a_5), .A4(cu_a_4), .A3(cu_a_3),
    .A2(cu_a_2), .A1(cu_a_1), .A0(cu_a_0), .I_O0(cu_rom_24), .I_O1(cu_rom_25), .I_O2(cu_rom_26),
    .I_O3(cu_rom_27), .I_O4(cu_rom_28), .I_O5(cu_rom_29), .I_O6(cu_rom_30), .I_O7(cu_rom_31), .nCE(1'b0),
    .A10(cu_a_10), .nOE(1'b0), .A11(cu_a_11), .A9(cu_a_9), .A8(cu_a_8), .A13(cu_a_13), .nWE(1'b1),
    .IMAGE(4'b0101));  // open: GND, VCC
  _74153 U5 (
    .pin1(U5_pin1), .pin2(cu_cond_sel_1), .pin3(cu_x_n), .pin4(cu_hw_q), .pin5(cu_bnd_n), .pin6(cu_jc),
    .pin7(cu_a_0), .pin15(U5_pin15), .pin14(cu_cond_sel_0), .pin13(U5_pin13), .pin12(U5_pin12),
    .pin11(U5_pin11), .pin10(U5_pin10));  // open: pin9
  _7400 U18 (
    .pin1(cu_rom_22), .pin2(cu_rom_23), .pin3(cu_swi_oe_n_d), .pin4(cu_rom_14), .pin5(cu_rom_15),
    .pin6(cu_alat_oe_n_d), .pin13(U18_pin13), .pin12(U18_pin12), .pin10(cu_rom_18), .pin9(cu_bsel3),
    .pin8(cu_blat_oe_n_d));  // open: pin11
  ttl74574 U24 (
    .nOE(rst_rc), .D0(cu_rom_31), .D1(cu_rom_32), .D2(cu_rom_33), .D3(cu_rom_34), .D4(cu_rom_35),
    .D5(cu_rom_23), .D6(cu_lat_hi_off), .D7(cu_dbus_n_5), .CP(clk[0]), .Q7(cu_addr_pc_oe_n[0]),
    .Q6(cu_addr_lat_oe_n[1]), .Q5(cu_addr_lat_oe_n[0]), .Q4(cu_addr_sp_ld_n), .Q3(cu_addr_pc_ld_n),
    .Q2(cu_addr_lat_ld_n), .Q1(cu_addr_cin), .Q0(cu_addr_inv));  // open: GND, VCC
  _74175 U6 (
    .pin1(rst_n), .pin2(cu_a_1), .pin4(cu_rom_48), .pin5(cu_rom_49), .pin7(cu_a_2), .pin15(cu_a_4),
    .pin13(cu_rom_51), .pin12(cu_rom_50), .pin10(cu_a_3), .pin9(clk[1]));  // open: pin3, pin6, pin14, pin11
  ttlat28c256 U11 (
    .A14(cu_a_14), .A12(cu_a_12), .A7(cu_a_7), .A6(cu_a_6), .A5(cu_a_5), .A4(cu_a_4), .A3(cu_a_3),
    .A2(cu_a_2), .A1(cu_a_1), .A0(cu_a_0), .I_O0(cu_rom_32), .I_O1(cu_rom_33), .I_O2(cu_rom_34),
    .I_O3(cu_rom_35), .I_O4(cu_rom_36), .I_O5(cu_rom_37), .I_O6(cu_rom_38), .I_O7(cu_rom_39), .nCE(1'b0),
    .A10(cu_a_10), .nOE(1'b0), .A11(cu_a_11), .A9(cu_a_9), .A8(cu_a_8), .A13(cu_a_13), .nWE(1'b1),
    .IMAGE(4'b0110));  // open: GND, VCC
  _7427 U19 (
    .pin1(cu_hw), .pin2(cu_sw), .pin3(cu_sw), .pin4(cu_cout_q), .pin5(rst_early), .pin6(cu_x_n),
    .pin13(cu_flag_h), .pin12(cu_bnd_n), .pin11(U19_pin11), .pin10(cu_swi_ld), .pin9(cu_p_kept),
    .pin8(cu_p_nor));
  ttl74574 U25 (
    .nOE(rst_rc), .D0(cu_dbus_n_4), .D1(cu_dbus_n_7), .D2(cu_dbus_n_6), .D3(cu_rom_36), .D4(cu_rom_37),
    .D5(cu_rom_38), .D6(cu_rom_39), .D7(cu_rom_40), .CP(clk[1]), .Q7(cu_mem_re), .Q6(cu_ir_v2_ld_n),
    .Q5(cu_ir_v1_ld_n), .Q4(cu_ir_b1_ld_n), .Q3(cu_ir_b0_ld_n), .Q2(cu_addr_sp_oe_n[1]),
    .Q1(cu_addr_sp_oe_n[0]), .Q0(cu_addr_pc_oe_n[1]));  // open: GND, VCC
  ttlat28c256 U12 (
    .A14(cu_a_14), .A12(cu_a_12), .A7(cu_a_7), .A6(cu_a_6), .A5(cu_a_5), .A4(cu_a_4), .A3(cu_a_3),
    .A2(cu_a_2), .A1(cu_a_1), .A0(cu_a_0), .I_O0(cu_rom_40), .I_O1(cu_rom_41), .I_O2(cu_rom_42),
    .I_O3(cu_rom_43), .I_O4(cu_rom_44), .I_O5(cu_rom_45), .I_O6(cu_rom_46), .I_O7(cu_rom_47), .nCE(1'b0),
    .A10(cu_a_10), .nOE(1'b0), .A11(cu_a_11), .A9(cu_a_9), .A8(cu_a_8), .A13(cu_a_13), .nWE(1'b1),
    .IMAGE(4'b0111));  // open: GND, VCC
  ttl74574 U26 (
    .nOE(rst_rc), .D0(cu_rom_41), .D1(cu_rom_42), .D2(cu_rom_43), .D3(cu_rom_44), .D4(cu_ie_d),
    .D5(cu_dbus_n_1), .D6(cu_rom_45), .D7(cu_rom_46), .CP(clk[1]), .Q7(cu_swi_ld_n), .Q6(cu_inr), .Q5(cu_rw),
    .Q4(cu_ie), .Q3(cu_mem_rom_oe_n), .Q2(cu_mem_wbuf_oe_n), .Q1(cu_mem_we_n), .Q0(cu_mem_oe_n));  // open: GND, VCC
  ttlat28c256 U13 (
    .A14(cu_a_14), .A12(cu_a_12), .A7(cu_a_7), .A6(cu_a_6), .A5(cu_a_5), .A4(cu_a_4), .A3(cu_a_3),
    .A2(cu_a_2), .A1(cu_a_1), .A0(cu_a_0), .I_O0(cu_rom_48), .I_O1(cu_rom_49), .I_O2(cu_rom_50),
    .I_O3(cu_rom_51), .I_O4(cu_rom_52), .I_O5(cu_rom_53), .nCE(1'b0), .A10(cu_a_10), .nOE(1'b0),
    .A11(cu_a_11), .A9(cu_a_9), .A8(cu_a_8), .A13(cu_a_13), .nWE(1'b1), .IMAGE(4'b1000));  // open: GND, I_O6, I_O7, VCC
  ttl74574 U27 (
    .nOE(rst_rc), .D0(cu_swi_oe_n_d), .D1(cu_rom_47), .D2(cu_rom_52), .D3(cu_rom_53), .D4(1'b0), .D5(1'b0),
    .D6(1'b0), .D7(1'b0), .CP(clk[1]), .Q3(cu_cond_sel_1), .Q2(cu_cond_sel_0), .Q1(cu_force), .Q0(cu_swi_oe_n));  // open: GND, Q7, Q6, Q5, Q4, VCC
  Pull_Resistor pull_resistor_1 (.node(cu_alu_op[0]));
  Pull_Resistor pull_resistor_2 (.node(cu_alu_op[1]));
  Pull_Resistor pull_resistor_3 (.node(cu_alu_op[2]));
  Pull_Resistor pull_resistor_4 (.node(cu_alu_op[3]));
  Pull_Resistor pull_resistor_5 (.node(cu_flags_op[0]));
  Pull_Resistor pull_resistor_6 (.node(cu_flags_op[1]));
  Pull_Resistor pull_resistor_7 (.node(cu_flags_op[2]));
  Pull_Resistor pull_resistor_8 (.node(cu_flags_op[3]));
  Pull_Resistor pull_resistor_9 (.node(cu_flags_bit_val));
  Pull_Resistor #(.pull(1)) pull_resistor_10 (.node(cu_flags_oe_n));
  Pull_Resistor #(.pull(1)) pull_resistor_11 (.node(cu_regs_we_n));
  Pull_Resistor #(.pull(1)) pull_resistor_12 (.node(cu_regs_a_sel[0]));
  Pull_Resistor #(.pull(1)) pull_resistor_13 (.node(cu_regs_a_sel[1]));
  Pull_Resistor pull_resistor_14 (.node(cu_regs_cu_idx[0]));
  Pull_Resistor pull_resistor_15 (.node(cu_regs_cu_idx[1]));
  Pull_Resistor #(.pull(1)) pull_resistor_16 (.node(cu_regs_cu_bank_n[0]));
  Pull_Resistor #(.pull(1)) pull_resistor_17 (.node(cu_regs_cu_bank_n[1]));
  Pull_Resistor #(.pull(1)) pull_resistor_18 (.node(cu_regs_b_sel[0]));
  Pull_Resistor #(.pull(1)) pull_resistor_19 (.node(cu_regs_b_sel[1]));
  Pull_Resistor pull_resistor_20 (.node(cu_regs_a_lat_oe_n));
  Pull_Resistor pull_resistor_21 (.node(cu_regs_b_lat_oe_n));
  Pull_Resistor #(.pull(1)) pull_resistor_22 (.node(cu_regs_const_oe_n));
  Pull_Resistor #(.pull(1)) pull_resistor_23 (.node(cu_regs_const_0));
  Pull_Resistor #(.pull(1)) pull_resistor_24 (.node(cu_regs_a_bus_oe_n));
  Pull_Resistor #(.pull(1)) pull_resistor_25 (.node(cu_regs_res_oe_n));
  Pull_Resistor pull_resistor_26 (.node(cu_addr_base_sel[0]));
  Pull_Resistor pull_resistor_27 (.node(cu_addr_base_sel[1]));
  Pull_Resistor #(.pull(1)) pull_resistor_28 (.node(cu_addr_base_oe_n[0]));
  Pull_Resistor #(.pull(1)) pull_resistor_29 (.node(cu_addr_base_oe_n[1]));
  Pull_Resistor pull_resistor_30 (.node(cu_addr_off_sel));
  Pull_Resistor #(.pull(1)) pull_resistor_31 (.node(cu_addr_off_oe_n[0]));
  Pull_Resistor #(.pull(1)) pull_resistor_32 (.node(cu_addr_off_oe_n[1]));
  Pull_Resistor pull_resistor_33 (.node(cu_addr_inv));
  Pull_Resistor pull_resistor_34 (.node(cu_addr_cin));
  Pull_Resistor #(.pull(1)) pull_resistor_35 (.node(cu_addr_lat_ld_n));
  Pull_Resistor #(.pull(1)) pull_resistor_36 (.node(cu_addr_pc_ld_n));
  Pull_Resistor #(.pull(1)) pull_resistor_37 (.node(cu_addr_sp_ld_n));
  Pull_Resistor pull_resistor_38 (.node(cu_addr_lat_oe_n[0]));
  Pull_Resistor pull_resistor_39 (.node(cu_addr_lat_oe_n[1]));
  Pull_Resistor #(.pull(1)) pull_resistor_40 (.node(cu_addr_pc_oe_n[0]));
  Pull_Resistor #(.pull(1)) pull_resistor_41 (.node(cu_addr_pc_oe_n[1]));
  Pull_Resistor #(.pull(1)) pull_resistor_42 (.node(cu_addr_sp_oe_n[0]));
  Pull_Resistor #(.pull(1)) pull_resistor_43 (.node(cu_addr_sp_oe_n[1]));
  Pull_Resistor #(.pull(1)) pull_resistor_44 (.node(cu_ir_b0_ld_n));
  Pull_Resistor #(.pull(1)) pull_resistor_45 (.node(cu_ir_b1_ld_n));
  Pull_Resistor #(.pull(1)) pull_resistor_46 (.node(cu_ir_v1_ld_n));
  Pull_Resistor #(.pull(1)) pull_resistor_47 (.node(cu_ir_v2_ld_n));
  Pull_Resistor pull_resistor_48 (.node(cu_mem_re));
  Pull_Resistor #(.pull(1)) pull_resistor_49 (.node(cu_mem_oe_n));
  Pull_Resistor #(.pull(1)) pull_resistor_50 (.node(cu_mem_we_n));
  Pull_Resistor #(.pull(1)) pull_resistor_51 (.node(cu_mem_wbuf_oe_n));
  Pull_Resistor #(.pull(1)) pull_resistor_52 (.node(cu_mem_rom_oe_n));
  Pull_Resistor pull_resistor_53 (.node(cu_ie));
  Pull_Resistor #(.pull(1)) pull_resistor_54 (.node(cu_rw));
  Pull_Resistor pull_resistor_55 (.node(cu_inr));
  Pull_Resistor #(.pull(1)) pull_resistor_56 (.node(cu_swi_ld_n));
  Pull_Resistor #(.pull(1)) pull_resistor_57 (.node(cu_swi_oe_n));
  Pull_Resistor pull_resistor_58 (.node(cu_force));
  Pull_Resistor #(.pull(1)) pull_resistor_59 (.node(cu_cond_sel_0));
  Pull_Resistor #(.pull(1)) pull_resistor_60 (.node(cu_cond_sel_1));
  // also tied to GND on the sheet: {U14_pin4, U14_pin5, U28_pin13, U3_pin14, U3_pin13, U3_pin11, U3_pin10, U16_pin13, U16_pin12, U16_pin10, U16_pin9, U30_pin19, U4_pin1, U4_pin7, U17_pin13, U5_pin1, U5_pin13, U5_pin12, U5_pin11, U5_pin10, U18_pin13, U18_pin12, U19_pin11}
  // also tied to VCC on the sheet: {U14_pin6, U4_pin12, U5_pin15}

  // Other names for the same wires on the sheet: clk_0 = clk[0]; clk_1 = clk[1];
  //   cu_addr_base_oe_n_0 = cu_addr_base_oe_n[0]; cu_addr_base_oe_n_1 = cu_addr_base_oe_n[1];
  //   cu_addr_base_sel_0 = cu_addr_base_sel[0]; cu_addr_base_sel_1 = cu_addr_base_sel[1];
  //   cu_addr_lat_oe_n_0 = cu_addr_lat_oe_n[0]; cu_addr_lat_oe_n_1 = cu_addr_lat_oe_n[1];
  //   cu_addr_off_oe_n_0 = cu_addr_off_oe_n[0]; cu_addr_off_oe_n_1 = cu_addr_off_oe_n[1];
  //   cu_addr_pc_oe_n_0 = cu_addr_pc_oe_n[0]; cu_addr_pc_oe_n_1 = cu_addr_pc_oe_n[1];
  //   cu_addr_sp_oe_n_0 = cu_addr_sp_oe_n[0]; cu_addr_sp_oe_n_1 = cu_addr_sp_oe_n[1]; cu_alu_op_0 = cu_alu_op[0];
  //   cu_alu_op_1 = cu_alu_op[1]; cu_alu_op_2 = cu_alu_op[2]; cu_alu_op_3 = cu_alu_op[3];
  //   cu_bus_addr_lo_0 = cu_bus_addr_lo[0]; cu_bus_addr_lo_1 = cu_bus_addr_lo[1];
  //   cu_bus_addr_lo_2 = cu_bus_addr_lo[2]; cu_bus_addr_lo_3 = cu_bus_addr_lo[3];
  //   cu_bus_addr_lo_4 = cu_bus_addr_lo[4]; cu_bus_addr_lo_5 = cu_bus_addr_lo[5];
  //   cu_bus_addr_lo_6 = cu_bus_addr_lo[6]; cu_bus_addr_lo_7 = cu_bus_addr_lo[7]; cu_bus_in_0 = cu_bus_in[0];
  //   cu_bus_in_1 = cu_bus_in[1]; cu_bus_in_2 = cu_bus_in[2]; cu_bus_in_3 = cu_bus_in[3]; cu_bus_in_4 = cu_bus_in[4];
  //   cu_bus_in_5 = cu_bus_in[5]; cu_bus_in_6 = cu_bus_in[6]; cu_bus_in_7 = cu_bus_in[7];
  //   cu_flags_op_0 = cu_flags_op[0]; cu_flags_op_1 = cu_flags_op[1]; cu_flags_op_2 = cu_flags_op[2];
  //   cu_flags_op_3 = cu_flags_op[3]; cu_ir_mode_0 = cu_ir_mode[0]; cu_ir_mode_1 = cu_ir_mode[1];
  //   cu_ir_mode_2 = cu_ir_mode[2]; cu_ir_mode_3 = cu_ir_mode[3]; cu_ir_op_0 = cu_ir_op[0]; cu_ir_op_1 = cu_ir_op[1];
  //   cu_ir_op_2 = cu_ir_op[2]; cu_ir_op_3 = cu_ir_op[3]; cu_ir_op_4 = cu_ir_op[4]; cu_ir_op_5 = cu_ir_op[5];
  //   cu_regs_a_sel_0 = cu_regs_a_sel[0]; cu_regs_a_sel_1 = cu_regs_a_sel[1]; cu_regs_b_sel_0 = cu_regs_b_sel[0];
  //   cu_regs_b_sel_1 = cu_regs_b_sel[1]; cu_regs_cu_bank_n_0 = cu_regs_cu_bank_n[0];
  //   cu_regs_cu_bank_n_1 = cu_regs_cu_bank_n[1]; cu_regs_cu_idx_0 = cu_regs_cu_idx[0];
  //   cu_regs_cu_idx_1 = cu_regs_cu_idx[1]

  // Notes on the sheet:
  //   pipeline 1: alu_op_0 .. flags_op_3
  //   opcode bits 3..0 (bypass: bus_data)
  //   microcode bits 7..0 (IMAGE 2)
  //   dbus: the bus_data driver
  //   hw_q, cout_q, P
  //   opcode bits 5..4, mode bits 3..2
  //   abus: latch high off, IE; HW, SW
  //   pending software interrupt port (C13)
  //   pipeline 2: flags_bit_val .. regs_cu_bank_n_0
  //   microcode bits 15..8 (IMAGE 3)
  //   mode bits 1..0 (with byte 1)
  //   b_sel = 11; P kept
  //   pending port -> bus_addr low byte
  //   pipeline 3: regs_cu_bank_n_1 .. regs_a_bus_oe_n
  //   microcode bits 23..16 (IMAGE 4)
  //   jump condition: S Z F 0 C E N 1 by opcode bits 2..0
  //   NOT alu_op3, abus bits; P
  //   pipeline 4: regs_res_oe_n .. addr_off_oe_n_1
  //   microcode bits 31..24 (IMAGE 5)
  //   cond: jc, bnd_n, hw_q, x_n
  //   abus 11, A latch, B latch
  //   pipeline 5: addr_inv .. addr_pc_oe_n_0
  //   step register (cu_next)
  //   microcode bits 39..32 (IMAGE 6)
  //   bnd_n, x_n; P
  //   pipeline 6: addr_pc_oe_n_1 .. mem_re
  //   microcode bits 47..40 (IMAGE 7)
  //   pipeline 7: mem_oe_n .. swi_ld_n
  //   microcode bits 55..48 (IMAGE 8)
  //   pipeline 8: swi_oe_n .. cond_sel_1
  //   pull resistors (C24): the idle level of each pipeline line while rst_rc holds the 574s off
endmodule
