// Logisim project flags.circ as structural Verilog: 1 circuit, main circuit flags
module flags (
  input  [3:0] flags_op,
  input  flags_bit_val,
  input  flags_oe_n,
  input  clk,
  input  rst_n,
  input  flags_alu_c,
  input  flags_alu_z,
  input  flags_alu_n,
  input  flags_alu_s,
  input  flags_alu_e,
  input  flags_alu_f,
  input  [7:0] flags_bus_in,
  output flag_c,
  output flag_e,
  output flag_i,
  output flag_n,
  output flag_s,
  output flag_z,
  output flag_f,
  output flag_h,
  output [7:0] flags_bus_out
);

  wire flags_bit_c_n, flags_bit_e_n, flags_bit_f_n, flags_bit_h_n, flags_bit_i_n, flags_bit_n_n,
       flags_bit_s_n, flags_bit_z_n, flags_c_bit, flags_c_next, flags_ci_sel0, flags_ci_sel1, flags_e_bit,
       flags_e_next, flags_eh_sel0, flags_eh_sel1, flags_f_bit, flags_f_next, flags_h_bit, flags_h_next,
       flags_i_bit, flags_i_next, flags_i_next_n, flags_n_bit, flags_n_next, flags_op_bus_n, flags_op_czn_n,
       flags_op_sef_n, flags_op_zn_n, flags_s_bit, flags_s_next, flags_sf_sel0, flags_sf_sel1, flags_z_bit,
       flags_z_next, flags_zn_ld_n, flags_zn_sel0, flags_zn_sel1, U1_pin5, U1_pin6, U3_pin15, U4_pin1,
       U4_pin15, U6_pin19, U7_pin4, U7_pin5, U9_pin15, U10_pin1, U10_pin15, U12_pin11, U13_pin1, U13_pin15,
       U14_pin2, U14_pin4, U14_pin5, U14_pin9, U14_pin10, U14_pin12, U14_pin13, U15_pin1, U15_pin15;

  _74138 U1 (
    .pin1(flags_op[0]), .pin2(flags_op[1]), .pin3(flags_op[2]), .pin4(flags_op[3]), .pin5(U1_pin5),
    .pin6(U1_pin6), .pin14(flags_op_czn_n), .pin13(flags_op_zn_n), .pin12(flags_op_sef_n),
    .pin11(flags_op_bus_n));  // open: pin7, pin15, pin10, pin9
  _74138 U7 (
    .pin1(flags_op[0]), .pin2(flags_op[1]), .pin3(flags_op[2]), .pin4(U7_pin4), .pin5(U7_pin5),
    .pin6(flags_op[3]), .pin7(flags_bit_h_n), .pin15(flags_bit_c_n), .pin14(flags_bit_e_n),
    .pin13(flags_bit_i_n), .pin12(flags_bit_n_n), .pin11(flags_bit_s_n), .pin10(flags_bit_z_n),
    .pin9(flags_bit_f_n));
  _7411 U2 (
    .pin1(flags_op_bus_n), .pin2(flags_bit_c_n), .pin3(flags_op_czn_n), .pin4(flags_bit_c_n),
    .pin5(flags_bit_i_n), .pin6(flags_ci_sel0), .pin13(flags_bit_i_n), .pin12(flags_ci_sel1),
    .pin11(flags_bit_h_n), .pin10(flags_bit_e_n), .pin9(flags_op_bus_n), .pin8(flags_eh_sel1));
  _7411 U8 (
    .pin1(flags_op_sef_n), .pin2(flags_bit_e_n), .pin3(flags_op_bus_n), .pin4(flags_bit_z_n),
    .pin5(flags_bit_n_n), .pin6(flags_zn_sel1), .pin13(flags_bit_h_n), .pin12(flags_eh_sel0),
    .pin11(flags_bit_n_n), .pin10(flags_bit_z_n), .pin9(flags_zn_ld_n), .pin8(flags_zn_sel0));
  _7411 U12 (
    .pin1(flags_op_bus_n), .pin2(flags_bit_s_n), .pin3(flags_op_sef_n), .pin4(flags_bit_s_n),
    .pin5(flags_bit_f_n), .pin6(flags_sf_sel0), .pin13(flags_bit_f_n), .pin12(flags_sf_sel1),
    .pin11(U12_pin11), .pin10(flags_op_zn_n), .pin9(flags_op_czn_n), .pin8(flags_zn_ld_n));
  _74157 U3 (
    .pin1(flags_op[1]), .pin2(flags_bit_val), .pin3(flag_c), .pin4(flags_c_bit), .pin5(flag_i),
    .pin6(flags_bit_val), .pin7(flags_i_bit), .pin15(U3_pin15), .pin14(flag_h), .pin13(flags_bit_val),
    .pin12(flags_h_bit), .pin11(flags_bit_val), .pin10(flag_e), .pin9(flags_e_bit));
  _74157 U9 (
    .pin1(flags_op[1]), .pin2(flags_bit_val), .pin3(flag_z), .pin4(flags_z_bit), .pin5(flag_n),
    .pin6(flags_bit_val), .pin7(flags_n_bit), .pin15(U9_pin15), .pin14(flag_f), .pin13(flags_bit_val),
    .pin12(flags_f_bit), .pin11(flags_bit_val), .pin10(flag_s), .pin9(flags_s_bit));
  _74153 U4 (
    .pin1(U4_pin1), .pin2(flags_ci_sel1), .pin3(flag_c), .pin4(flags_alu_c), .pin5(flags_bus_in[0]),
    .pin6(flags_c_bit), .pin7(flags_c_next), .pin15(U4_pin15), .pin14(flags_ci_sel0), .pin13(flag_i),
    .pin12(flag_i), .pin11(flags_bus_in[2]), .pin10(flags_i_bit), .pin9(flags_i_next));
  _74153 U10 (
    .pin1(U10_pin1), .pin2(flags_eh_sel1), .pin3(flag_e), .pin4(flags_alu_e), .pin5(flags_bus_in[1]),
    .pin6(flags_e_bit), .pin7(flags_e_next), .pin15(U10_pin15), .pin14(flags_eh_sel0), .pin13(flag_h),
    .pin12(flag_h), .pin11(flags_bus_in[7]), .pin10(flags_h_bit), .pin9(flags_h_next));
  _74153 U13 (
    .pin1(U13_pin1), .pin2(flags_zn_sel1), .pin3(flag_z), .pin4(flags_alu_z), .pin5(flags_bus_in[5]),
    .pin6(flags_z_bit), .pin7(flags_z_next), .pin15(U13_pin15), .pin14(flags_zn_sel0), .pin13(flag_n),
    .pin12(flags_alu_n), .pin11(flags_bus_in[3]), .pin10(flags_n_bit), .pin9(flags_n_next));
  _74153 U15 (
    .pin1(U15_pin1), .pin2(flags_sf_sel1), .pin3(flag_s), .pin4(flags_alu_s), .pin5(flags_bus_in[4]),
    .pin6(flags_s_bit), .pin7(flags_s_next), .pin15(U15_pin15), .pin14(flags_sf_sel0), .pin13(flag_f),
    .pin12(flags_alu_f), .pin11(flags_bus_in[6]), .pin10(flags_f_bit), .pin9(flags_f_next));
  _74175 U5 (
    .pin1(rst_n), .pin2(flag_c), .pin4(flags_c_next), .pin5(flags_e_next), .pin7(flag_e), .pin15(flag_n),
    .pin13(flags_n_next), .pin12(flags_i_next_n), .pin11(flag_i), .pin9(clk));  // open: pin3, pin6, pin14, pin10
  _74175 U11 (
    .pin1(rst_n), .pin2(flag_s), .pin4(flags_s_next), .pin5(flags_z_next), .pin7(flag_z), .pin15(flag_h),
    .pin13(flags_h_next), .pin12(flags_f_next), .pin10(flag_f), .pin9(clk));  // open: pin3, pin6, pin14, pin11
  _7486 U14 (
    .pin1(flags_i_next), .pin2(U14_pin2), .pin3(flags_i_next_n), .pin4(U14_pin4), .pin5(U14_pin5),
    .pin13(U14_pin13), .pin12(U14_pin12), .pin10(U14_pin10), .pin9(U14_pin9));  // open: pin6, pin11, pin8
  _74541 U6 (
    .pin1(flags_oe_n), .pin2(flag_c), .pin3(flag_e), .pin4(flag_i), .pin5(flag_n), .pin6(flag_s),
    .pin7(flag_z), .pin8(flag_f), .pin9(flag_h), .pin19(U6_pin19), .pin18(flags_bus_out[0]),
    .pin17(flags_bus_out[1]), .pin16(flags_bus_out[2]), .pin15(flags_bus_out[3]), .pin14(flags_bus_out[4]),
    .pin13(flags_bus_out[5]), .pin12(flags_bus_out[6]), .pin11(flags_bus_out[7]));
  // also tied to GND on the sheet: {U1_pin5, U7_pin4, U7_pin5, U3_pin15, U9_pin15, U4_pin1, U10_pin1, U13_pin1, U15_pin1, U4_pin15, U10_pin15, U13_pin15, U15_pin15, U14_pin4, U14_pin5, U14_pin13, U14_pin12, U14_pin10, U14_pin9, U6_pin19}
  // also tied to VCC on the sheet: {U1_pin6, U12_pin11, U14_pin2}

  // Other names for the same wires on the sheet: flags_bus_in_0 = flags_bus_in[0]; flags_bus_in_1 = flags_bus_in[1];
  //   flags_bus_in_2 = flags_bus_in[2]; flags_bus_in_3 = flags_bus_in[3]; flags_bus_in_4 = flags_bus_in[4];
  //   flags_bus_in_5 = flags_bus_in[5]; flags_bus_in_6 = flags_bus_in[6]; flags_bus_in_7 = flags_bus_in[7];
  //   flags_bus_out_0 = flags_bus_out[0]; flags_bus_out_1 = flags_bus_out[1]; flags_bus_out_2 = flags_bus_out[2];
  //   flags_bus_out_3 = flags_bus_out[3]; flags_bus_out_4 = flags_bus_out[4]; flags_bus_out_5 = flags_bus_out[5];
  //   flags_bus_out_6 = flags_bus_out[6]; flags_bus_out_7 = flags_bus_out[7]; flags_op_0 = flags_op[0];
  //   flags_op_1 = flags_op[1]; flags_op_2 = flags_op[2]; flags_op_3 = flags_op[3]

  // Notes on the sheet:
  //   flags_op 0xxx
  //   flags_op 1fff
  //   pair selects
  //   bit write lanes
  //   bit write lanes
  //   C I
  //   E H
  //   Z N
  //   S F
  //   C E I N (I inverted)
  //   S Z F H
  //   not I
  //   PSF
endmodule
