// Logisim project iod.circ as structural Verilog: 1 circuit, main circuit iod
module iod (
  input  [7:0] iod_bus_in,
  input  [7:0] iod_addr_in,
  input  iod_ie,
  input  iod_rw,
  input  iod_inr,
  input  clk,
  input  clk_wr_n,
  input  rst_n,
  input  iod_sck,
  input  iod_mosi,
  input  iod_rclk_rx,
  input  iod_rclk_evt,
  input  iod_mbx_sel,
  output [7:0] iod_bus_out,
  output [7:0] iod_addr_out,
  output iod_int,
  output iod_miso,
  output iod_mcu_tx_full,
  output iod_mcu_rx_full,
  output iod_mcu_evt_pend,
  output iod_mcu_rst_n
);

  wire iod_evt_clr_n, iod_evt_link, iod_evt_pend, iod_rx_clr_n, iod_rx_full, iod_tx_free, iod_tx_full,
       iod_tx_q, iod_tx_wr_n, iod_vec, iod_vec_n, iod_y0_n, iod_y2_n, iod_y3_n, U2_pin4, U2_pin5, U2_pin9,
       U2_pin10, U2_pin12, U2_pin13, U3_pin2, U3_pin10, U3_pin12, U4_pin4, U4_pin10, U4_pin12, U5_pin4,
       U5_pin10, U6_pin4, U6_pin10, U6_pin11, U6_pin12, U6_pin13, U7_pin10, U8_pin8, U8_pin11, U8_pin13,
       U8_pin15, U8_pin17, U12_pin4, U12_pin6, U12_pin8, U12_pin19;

  ttl74595 U9 (
    .QB(iod_bus_out[1]), .QC(iod_bus_out[2]), .QD(iod_bus_out[3]), .QE(iod_bus_out[4]), .QF(iod_bus_out[5]),
    .QG(iod_bus_out[6]), .QH(iod_bus_out[7]), .nSRCLR(1'b1), .SRCLK(iod_sck), .RCLK(iod_rclk_rx),
    .nOE(iod_y2_n), .SER(iod_mosi), .QA(iod_bus_out[0]));  // open: GND, QH_prime, VCC
  _74138 U1 (
    .pin1(iod_addr_in[0]), .pin2(iod_rw), .pin3(iod_addr_in[1]), .pin4(iod_addr_in[7]),
    .pin5(iod_addr_in[6]), .pin6(iod_ie), .pin15(iod_y0_n), .pin13(iod_y2_n), .pin12(iod_y3_n));  // open: pin7, pin14, pin11, pin10, pin9
  _7474 U5 (
    .pin1(rst_n), .pin2(iod_vec_n), .pin3(clk), .pin4(U5_pin4), .pin5(iod_evt_clr_n), .pin13(rst_n),
    .pin12(iod_inr), .pin11(clk), .pin10(U5_pin10), .pin9(iod_vec), .pin8(iod_vec_n));  // open: pin6
  ttl74595 U10 (
    .QB(iod_addr_out[1]), .QC(iod_addr_out[2]), .QD(iod_addr_out[3]), .QE(iod_addr_out[4]),
    .QF(iod_addr_out[5]), .QG(iod_addr_out[6]), .QH(iod_addr_out[7]), .QH_prime(iod_evt_link), .nSRCLR(1'b1),
    .SRCLK(iod_sck), .RCLK(iod_rclk_evt), .nOE(iod_vec_n), .SER(iod_mosi), .QA(iod_addr_out[0]));  // open: GND, VCC
  _7432 U2 (
    .pin1(iod_y0_n), .pin2(clk_wr_n), .pin3(iod_tx_wr_n), .pin4(U2_pin4), .pin5(U2_pin5), .pin13(U2_pin13),
    .pin12(U2_pin12), .pin10(U2_pin10), .pin9(U2_pin9));  // open: pin6, pin11, pin8
  _7474 U6 (
    .pin1(iod_vec_n), .pin2(iod_evt_pend), .pin3(clk), .pin4(U6_pin4), .pin5(iod_int), .pin13(U6_pin13),
    .pin12(U6_pin12), .pin11(U6_pin11), .pin10(U6_pin10));  // open: pin6, pin9, pin8
  ttl74595 U11 (
    .QB(iod_bus_out[1]), .QC(iod_bus_out[2]), .QD(iod_bus_out[3]), .QE(iod_bus_out[4]), .QF(iod_bus_out[5]),
    .QG(iod_bus_out[6]), .QH(iod_bus_out[7]), .nSRCLR(1'b1), .SRCLK(iod_sck), .RCLK(iod_rclk_evt),
    .nOE(iod_vec_n), .SER(iod_evt_link), .QA(iod_bus_out[0]));  // open: GND, QH_prime, VCC
  _7474 U3 (
    .pin1(rst_n), .pin2(U3_pin2), .pin3(iod_mbx_sel), .pin4(iod_tx_wr_n), .pin5(iod_tx_full),
    .pin6(iod_tx_free), .pin13(iod_rx_clr_n), .pin12(U3_pin12), .pin11(iod_rclk_rx), .pin10(U3_pin10),
    .pin9(iod_rx_full));  // open: pin8
  _74165 U7 (
    .pin1(iod_tx_wr_n), .pin2(iod_sck), .pin3(iod_bus_in[4]), .pin4(iod_bus_in[5]), .pin5(iod_bus_in[6]),
    .pin6(iod_bus_in[7]), .pin15(iod_mbx_sel), .pin14(iod_bus_in[3]), .pin13(iod_bus_in[2]),
    .pin12(iod_bus_in[1]), .pin11(iod_bus_in[0]), .pin10(U7_pin10), .pin9(iod_tx_q));  // open: pin7
  _7474 U4 (
    .pin1(rst_n), .pin2(iod_y2_n), .pin3(clk), .pin4(U4_pin4), .pin5(iod_rx_clr_n), .pin13(iod_evt_clr_n),
    .pin12(U4_pin12), .pin11(iod_rclk_evt), .pin10(U4_pin10), .pin9(iod_evt_pend));  // open: pin6, pin8
  _74244 U8 (
    .pin1(iod_y3_n), .pin2(iod_rx_full), .pin3(iod_bus_out[7]), .pin4(iod_tx_free), .pin5(iod_bus_out[6]),
    .pin6(iod_evt_pend), .pin7(iod_bus_out[5]), .pin8(U8_pin8), .pin9(iod_bus_out[4]), .pin19(iod_y3_n),
    .pin18(iod_bus_out[0]), .pin17(U8_pin17), .pin16(iod_bus_out[1]), .pin15(U8_pin15),
    .pin14(iod_bus_out[2]), .pin13(U8_pin13), .pin12(iod_bus_out[3]), .pin11(U8_pin11));
  _74244 U12 (
    .pin1(iod_mbx_sel), .pin2(iod_tx_q), .pin3(iod_mcu_rst_n), .pin4(U12_pin4), .pin5(iod_mcu_evt_pend),
    .pin6(U12_pin6), .pin7(iod_mcu_rx_full), .pin8(U12_pin8), .pin9(iod_mcu_tx_full), .pin19(U12_pin19),
    .pin18(iod_miso), .pin17(rst_n), .pin15(iod_evt_pend), .pin13(iod_rx_full), .pin11(iod_tx_full));  // open: pin16, pin14, pin12
  // also tied to GND on the sheet: {U2_pin4, U2_pin5, U2_pin13, U2_pin12, U2_pin10, U2_pin9, U6_pin12, U6_pin11, U3_pin2, U7_pin10, U8_pin8, U12_pin4, U12_pin6, U12_pin8, U8_pin17, U8_pin15, U8_pin13, U8_pin11, U12_pin19}
  // also tied to VCC on the sheet: {U5_pin4, U5_pin10, U6_pin4, U6_pin13, U6_pin10, U3_pin12, U3_pin10, U4_pin4, U4_pin12, U4_pin10}

  // Other names for the same wires on the sheet: iod_addr_in_0 = iod_addr_in[0]; iod_addr_in_1 = iod_addr_in[1];
  //   iod_addr_in_2_nc = iod_addr_in[2]; iod_addr_in_3_nc = iod_addr_in[3]; iod_addr_in_4_nc = iod_addr_in[4];
  //   iod_addr_in_5_nc = iod_addr_in[5]; iod_addr_in_6 = iod_addr_in[6]; iod_addr_in_7 = iod_addr_in[7];
  //   iod_addr_out_0 = iod_addr_out[0]; iod_addr_out_1 = iod_addr_out[1]; iod_addr_out_2 = iod_addr_out[2];
  //   iod_addr_out_3 = iod_addr_out[3]; iod_addr_out_4 = iod_addr_out[4]; iod_addr_out_5 = iod_addr_out[5];
  //   iod_addr_out_6 = iod_addr_out[6]; iod_addr_out_7 = iod_addr_out[7]; iod_bus_in_0 = iod_bus_in[0];
  //   iod_bus_in_1 = iod_bus_in[1]; iod_bus_in_2 = iod_bus_in[2]; iod_bus_in_3 = iod_bus_in[3];
  //   iod_bus_in_4 = iod_bus_in[4]; iod_bus_in_5 = iod_bus_in[5]; iod_bus_in_6 = iod_bus_in[6];
  //   iod_bus_in_7 = iod_bus_in[7]; iod_bus_out_0 = iod_bus_out[0]; iod_bus_out_1 = iod_bus_out[1];
  //   iod_bus_out_2 = iod_bus_out[2]; iod_bus_out_3 = iod_bus_out[3]; iod_bus_out_4 = iod_bus_out[4];
  //   iod_bus_out_5 = iod_bus_out[5]; iod_bus_out_6 = iod_bus_out[6]; iod_bus_out_7 = iod_bus_out[7]

  // Notes on the sheet:
  //   decode: /Y0 OUT TX, /Y2 IN RX, /Y3 IN STATUS
  //   evt_clr (step after the vector step) | VEC (INR delayed one step)
  //   RX: from the MCU -> bus_data (IN RX)
  //   TX strobe: /Y0 OR clk_wr_n
  //   evt_s = INT (on clk, 0 in the vector step) | spare
  //   EVT port -> bus_addr A0-A7 (vector step)
  //   TX full (CPU sets, MCU clears) | RX full (MCU sets, CPU clears)
  //   TX: loaded from bus_data, shifted out to the MCU (bit 7 first)
  //   EVT data -> bus_data (vector step, -> I)
  //   rx_clr (step after IN RX) | EVT pending (MCU sets)
  //   STATUS: RX full, TX free, EVT pending, 0 x 5
  //   74LVC244 at 3.3 V: to the ESP32
endmodule
