// Logisim project test_iod_cpu_reset_tx.circ as structural Verilog: 1 circuit, main circuit test_iod_cpu_reset_tx
module test_iod_cpu_reset_tx (
  output halt,
  output [5:0] clk,
  output clk_wr_n,
  output clk_mem_wr_n,
  output rst_n,
  output rst_early,
  output rst_rc,
  output [7:0] bus_data,
  output [15:0] bus_addr,
  output [7:0] bus_a,
  output [7:0] bus_b,
  output [7:0] mem_d,
  output [7:0] alu_r,
  output [7:0] flag_reg,
  output addr_cout,
  output [3:0] alu_op,
  output [3:0] flags_op,
  output flags_bit_val,
  output flags_oe_n,
  output regs_we_n,
  output [1:0] regs_a_sel,
  output [1:0] regs_cu_idx,
  output [1:0] regs_cu_bank_n,
  output [1:0] regs_b_sel,
  output regs_a_lat_oe_n,
  output regs_b_lat_oe_n,
  output regs_const_oe_n,
  output regs_const_0,
  output regs_a_bus_oe_n,
  output regs_res_oe_n,
  output [1:0] addr_base_sel,
  output [1:0] addr_base_oe_n,
  output addr_off_sel,
  output [1:0] addr_off_oe_n,
  output addr_inv,
  output addr_cin,
  output addr_lat_ld_n,
  output addr_pc_ld_n,
  output addr_sp_ld_n,
  output [1:0] addr_lat_oe_n,
  output [1:0] addr_pc_oe_n,
  output [1:0] addr_sp_oe_n,
  output ir_b0_ld_n,
  output ir_b1_ld_n,
  output ir_v1_ld_n,
  output ir_v2_ld_n,
  output mem_re,
  output mem_oe_n,
  output mem_we_n,
  output mem_wbuf_oe_n,
  output mem_rom_oe_n,
  output ie,
  output rw,
  output inr,
  output [5:0] ir_op,
  output [3:0] ir_mode,
  output [2:0] ir_r1,
  output [2:0] ir_r2,
  output [2:0] ir_r3,
  output ir_r1_2_n,
  output ir_r2_2_n,
  output ir_r3_2_n,
  output [7:0] ir_v1,
  output [7:0] ir_v2,
  output \int ,
  output vec,
  output [6:0] st,
  output fired,
  output m_tx,
  output m_rx,
  output m_evt
);

  wire b_en, in_nc7, mosi, osc, out_shift, rc, rc_tc, rst_req_n, U1_pin3, U1_pin4, U1_pin5, U1_pin6, U1_pin7,
       U1_pin9, U1_pin10, U2_pin2, U2_pin4, U2_pin10, U2_pin13, v_sel_v;
  wire [7:0] b, in_d, inc_b, inc_v, iod_bus_addr_lo, iod_bus_data, low, low_a, v_d;
  wire [12:12] fa;
  wire [14:0] out_lo15;
  wire [15:0] out_d;
  wire [17:0] fq;

  Clock clock_1 (.out(osc));
  _74161 U1 (
    .pin1(rst_req_n), .pin2(osc), .pin3(U1_pin3), .pin4(U1_pin4), .pin5(U1_pin5), .pin6(U1_pin6),
    .pin7(U1_pin7), .pin15(rc_tc), .pin10(U1_pin10), .pin9(U1_pin9));  // open: pin14, pin13, pin12, pin11
  _7474 U2 (
    .pin1(rst_req_n), .pin2(U2_pin2), .pin3(rc_tc), .pin4(U2_pin4), .pin5(rc), .pin13(U2_pin13), .pin12(inr),
    .pin11(clk[5]), .pin10(U2_pin10), .pin9(vec));  // open: pin6, pin8
  ROM #(.addrWidth(8), .dataWidth(8)) rom_1 (.addr(b), .data(inc_b));
  ROM #(.addrWidth(8), .dataWidth(8)) rom_2 (.addr(low_a), .data(inc_v));
  ROM #(.addrWidth(9), .dataWidth(8)) rom_3 (.addr({b[7], low_a}), .data(low));
  Register #(.width(7)) register_1 (.D(fq[6:0]), .en(1'b1), .clk(osc), .Q(st), .clr(1'b0));
  ROM #(.addrWidth(14), .dataWidth(18)) rom_4 (
    .addr({fired, fa[12], b[6], b[7], m_evt, m_rx, m_tx, st}), .data({fq[17:13], b_en, fq[11:0]}));
  Register #(.width(8)) register_2 (.D(in_d), .en(fq[11]), .clk(osc), .Q({in_nc7, in_d[7:1]}), .clr(1'b0));
  Register #(.width(8)) register_3 (.D({in_nc7, in_d[7:1]}), .en(b_en), .clk(osc), .Q(b), .clr(1'b0));
  assign v_d = fq[14] ? inc_b : 8'bz;  // Controlled_Buffer controlled_buffer_1
  not not_1 (v_sel_v, fq[14]);
  assign v_d = v_sel_v ? inc_v : 8'bz;  // Controlled_Buffer controlled_buffer_2
  Register #(.width(8)) register_4 (.D(v_d), .en(fq[13]), .clk(osc), .Q(low_a), .clr(1'b0));
  cpu_main main_1 (
    .osc(osc), .rc(rc), .\int (\int ), .iod_bus_data(iod_bus_data), .iod_bus_addr_lo(iod_bus_addr_lo),
    .clk(clk), .clk_wr_n(clk_wr_n), .clk_mem_wr_n(clk_mem_wr_n), .rst_n(rst_n), .rst_early(rst_early),
    .rst_rc(rst_rc), .bus_data(bus_data), .bus_addr(bus_addr), .bus_a(bus_a), .bus_b(bus_b), .mem_d(mem_d),
    .alu_r(alu_r), .out_18(flag_reg), .addr_cout(addr_cout), .alu_op(alu_op), .flags_op(flags_op),
    .flags_bit_val(flags_bit_val), .flags_oe_n(flags_oe_n), .regs_we_n(regs_we_n), .regs_a_sel(regs_a_sel),
    .regs_cu_idx(regs_cu_idx), .regs_cu_bank_n(regs_cu_bank_n), .regs_b_sel(regs_b_sel),
    .regs_a_lat_oe_n(regs_a_lat_oe_n), .regs_b_lat_oe_n(regs_b_lat_oe_n), .regs_const_oe_n(regs_const_oe_n),
    .regs_const_0(regs_const_0), .regs_a_bus_oe_n(regs_a_bus_oe_n), .regs_res_oe_n(regs_res_oe_n),
    .addr_base_sel(addr_base_sel), .addr_base_oe_n(addr_base_oe_n), .addr_off_sel(addr_off_sel),
    .addr_off_oe_n(addr_off_oe_n), .addr_inv(addr_inv), .addr_cin(addr_cin), .addr_lat_ld_n(addr_lat_ld_n),
    .addr_pc_ld_n(addr_pc_ld_n), .addr_sp_ld_n(addr_sp_ld_n), .addr_lat_oe_n(addr_lat_oe_n),
    .addr_pc_oe_n(addr_pc_oe_n), .addr_sp_oe_n(addr_sp_oe_n), .ir_b0_ld_n(ir_b0_ld_n),
    .ir_b1_ld_n(ir_b1_ld_n), .ir_v1_ld_n(ir_v1_ld_n), .ir_v2_ld_n(ir_v2_ld_n), .mem_re(mem_re),
    .mem_oe_n(mem_oe_n), .mem_we_n(mem_we_n), .mem_wbuf_oe_n(mem_wbuf_oe_n), .mem_rom_oe_n(mem_rom_oe_n),
    .ie(ie), .rw(rw), .inr(inr), .ir_op(ir_op), .ir_mode(ir_mode), .ir_r1(ir_r1), .ir_r2(ir_r2),
    .ir_r3(ir_r3), .ir_r1_2_n(ir_r1_2_n), .ir_r2_2_n(ir_r2_2_n), .ir_r3_2_n(ir_r3_2_n), .ir_v1(ir_v1),
    .ir_v2(ir_v2));
  assign out_d = fq[16] ? {low_a, low} : 16'bz;  // Controlled_Buffer controlled_buffer_3
  not not_2 (out_shift, fq[16]);
  assign out_d = out_shift ? {out_lo15, 1'b0} : 16'bz;  // Controlled_Buffer controlled_buffer_4
  Register #(.width(16)) register_5 (.D(out_d), .en(fq[15]), .clk(osc), .Q({mosi, out_lo15}), .clr(1'b0));
  Register #(.width(1)) register_6 (.D(1'b1), .en(fq[17]), .clk(osc), .Q(fired), .clr(1'b0));
  not not_3 (rst_req_n, fq[17]);
  iod iod_1 (
    .iod_rclk_rx(fq[9]), .iod_rclk_evt(fq[10]), .iod_mbx_sel(fq[8]), .iod_bus_in(bus_data),
    .iod_addr_in(bus_addr[7:0]), .iod_ie(ie), .iod_rw(rw), .iod_inr(inr), .clk(clk[5]), .clk_wr_n(clk_wr_n),
    .rst_n(rst_n), .iod_sck(fq[7]), .iod_mosi(mosi), .iod_bus_out(iod_bus_data),
    .iod_addr_out(iod_bus_addr_lo), .iod_int(\int ), .iod_miso(in_d[0]), .iod_mcu_tx_full(m_tx),
    .iod_mcu_rx_full(m_rx), .iod_mcu_evt_pend(m_evt), .iod_mcu_rst_n(fa[12]));

  assign halt = 1'b0;
  // also tied to GND on the sheet: {U1_pin3, U1_pin4, U1_pin5, U1_pin6}
  // also tied to VCC on the sheet: {U1_pin7, U2_pin2, U2_pin4, U1_pin10, U1_pin9, U2_pin13, U2_pin10}

  // Other names for the same wires on the sheet: b_nc[5:0] = b[5:0]; b_6 = b[6];
  //   fa (some bits) = {fired, b[6], b[7], m_evt, m_rx, m_tx, st}; b_7 = b[7]; low_a[8] = b[7];
  //   lo[7:0] = bus_addr[7:0]; clk_5 = clk[5]; m_rst_n = fa[12]; st_d[6:0] = fq[6:0]; sck = fq[7]; mbx_sel = fq[8];
  //   rclk_rx = fq[9]; rclk_evt = fq[10]; in_en = fq[11]; fq[12] = b_en; v_en = fq[13]; v_sel_b = fq[14];
  //   out_en = fq[15]; out_load = fq[16]; rst_req = fq[17]; miso = in_d[0]; in_lo7[6:0] = in_d[7:1];
  //   inr_q[7:0] = {in_nc7, in_d[7:1]}; out_ld[15:0] = {low_a, low}; v[7:0] = low_a; out_q[15:0] = {mosi, out_lo15};
  //   out_sh[15:1] = out_lo15

  // Notes on the sheet:
  //   reset RC: rc rises after 15 osc periods; vec = INR one step late (observed only)
  //   test MCU: a state machine on osc (follows the 1 us rule)
  //   contents of rom_1 (hex, n*v repeats v):
  //   1 2 3 4 5 6 7 8 9 a b c d e f 10 11 12 13 14 15 16 17 18 19 1a 1b 1c 1d 1e 1f 20 21 22 23 24 25 26
  //   27 28 29 2a 2b 2c 2d 2e 2f 30 31 32 33 34 35 36 37 38 39 3a 3b 3c 3d 3e 3f 40 41 42 43 44 45 46 47
  //   48 49 4a 4b 4c 4d 4e 4f 50 51 52 53 54 55 56 57 58 59 5a 5b 5c 5d 5e 5f 60 61 62 63 64 65 66 67 68
  //   69 6a 6b 6c 6d 6e 6f 70 71 72 73 74 75 76 77 78 79 7a 7b 7c 7d 7e 7f 80 81 82 83 84 85 86 87 88 89
  //   8a 8b 8c 8d 8e 8f 90 91 92 93 94 95 96 97 98 99 9a 9b 9c 9d 9e 9f a0 a1 a2 a3 a4 a5 a6 a7 a8 a9 aa
  //   ab ac ad ae af b0 b1 b2 b3 b4 b5 b6 b7 b8 b9 ba bb bc bd be bf c0 c1 c2 c3 c4 c5 c6 c7 c8 c9 ca cb
  //   cc cd ce cf d0 d1 d2 d3 d4 d5 d6 d7 d8 d9 da db dc dd de df e0 e1 e2 e3 e4 e5 e6 e7 e8 e9 ea eb ec
  //   ed ee ef f0 f1 f2 f3 f4 f5 f6 f7 f8 f9 fa fb fc fd fe ff 0
  //   contents of rom_2 (hex, n*v repeats v):
  //   1 2 3 4 5 6 7 8 9 a b c d e f 10 11 12 13 14 15 16 17 18 19 1a 1b 1c 1d 1e 1f 20 21 22 23 24 25 26
  //   27 28 29 2a 2b 2c 2d 2e 2f 30 31 32 33 34 35 36 37 38 39 3a 3b 3c 3d 3e 3f 40 41 42 43 44 45 46 47
  //   48 49 4a 4b 4c 4d 4e 4f 50 51 52 53 54 55 56 57 58 59 5a 5b 5c 5d 5e 5f 60 61 62 63 64 65 66 67 68
  //   69 6a 6b 6c 6d 6e 6f 70 71 72 73 74 75 76 77 78 79 7a 7b 7c 7d 7e 7f 80 81 82 83 84 85 86 87 88 89
  //   8a 8b 8c 8d 8e 8f 90 91 92 93 94 95 96 97 98 99 9a 9b 9c 9d 9e 9f a0 a1 a2 a3 a4 a5 a6 a7 a8 a9 aa
  //   ab ac ad ae af b0 b1 b2 b3 b4 b5 b6 b7 b8 b9 ba bb bc bd be bf c0 c1 c2 c3 c4 c5 c6 c7 c8 c9 ca cb
  //   cc cd ce cf d0 d1 d2 d3 d4 d5 d6 d7 d8 d9 da db dc dd de df e0 e1 e2 e3 e4 e5 e6 e7 e8 e9 ea eb ec
  //   ed ee ef f0 f1 f2 f3 f4 f5 f6 f7 f8 f9 fa fb fc fd fe ff 0
  //   contents of rom_3 (hex, n*v repeats v):
  //   0 1 2 3 4 5 6 7 8 9 a b c d e f 10 11 12 13 14 15 16 17 18 19 1a 1b 1c 1d 1e 1f 20 21 22 23 24 25 26
  //   27 28 29 2a 2b 2c 2d 2e 2f 30 31 32 33 34 35 36 37 38 39 3a 3b 3c 3d 3e 3f 40 41 42 43 44 45 46 47
  //   48 49 4a 4b 4c 4d 4e 4f 50 51 52 53 54 55 56 57 58 59 5a 5b 5c 5d 5e 5f 60 61 62 63 64 65 66 67 68
  //   69 6a 6b 6c 6d 6e 6f 70 71 72 73 74 75 76 77 78 79 7a 7b 7c 7d 7e 7f 80 81 82 83 84 85 86 87 88 89
  //   8a 8b 8c 8d 8e 8f 90 91 92 93 94 95 96 97 98 99 9a 9b 9c 9d 9e 9f a0 a1 a2 a3 a4 a5 a6 a7 a8 a9 aa
  //   ab ac ad ae af b0 b1 b2 b3 b4 b5 b6 b7 b8 b9 ba bb bc bd be bf c0 c1 c2 c3 c4 c5 c6 c7 c8 c9 ca cb
  //   cc cd ce cf d0 d1 d2 d3 d4 d5 d6 d7 d8 d9 da db dc dd de df e0 e1 e2 e3 e4 e5 e6 e7 e8 e9 ea eb ec
  //   ed ee ef f0 f1 f2 f3 f4 f5 f6 f7 f8 f9 fa fb fc fd fe ff f0 f1 f2 f3 f4 f5 f6 f7 f8 f9 fa fb fc fd
  //   fe ff f0 f1 f2 f3 f4 f5 f6 f7 f8 f9 fa fb fc fd fe ff f0 f1 f2 f3 f4 f5 f6 f7 f8 f9 fa fb fc fd fe
  //   ff f0 f1 f2 f3 f4 f5 f6 f7 f8 f9 fa fb fc fd fe ff f0 f1 f2 f3 f4 f5 f6 f7 f8 f9 fa fb fc fd fe ff
  //   f0 f1 f2 f3 f4 f5 f6 f7 f8 f9 fa fb fc fd fe ff f0 f1 f2 f3 f4 f5 f6 f7 f8 f9 fa fb fc fd fe ff f0
  //   f1 f2 f3 f4 f5 f6 f7 f8 f9 fa fb fc fd fe ff f0 f1 f2 f3 f4 f5 f6 f7 f8 f9 fa fb fc fd fe ff f0 f1
  //   f2 f3 f4 f5 f6 f7 f8 f9 fa fb fc fd fe ff f0 f1 f2 f3 f4 f5 f6 f7 f8 f9 fa fb fc fd fe ff f0 f1 f2
  //   f3 f4 f5 f6 f7 f8 f9 fa fb fc fd fe ff f0 f1 f2 f3 f4 f5 f6 f7 f8 f9 fa fb fc fd fe ff f0 f1 f2 f3
  //   f4 f5 f6 f7 f8 f9 fa fb fc fd fe ff f0 f1 f2 f3 f4 f5 f6 f7 f8 f9 fa fb fc fd fe ff f0 f1 f2 f3 f4
  //   f5 f6 f7 f8 f9 fa fb fc fd fe ff
  //   contents of rom_4 (hex, n*v repeats v):
  //   100 100 100 100 100 100 100 100 100 20100 100 100 100 100 100 100 100 100 100 100 100 100 100 100
  //   100 100 100 100 100 100 100 100 100 100 100 100 100 100 100 100 100 100 100 100 100 100 100 100 100
  //   100 100 100 100 100 100 100 100 100 100 100 100 100 100 100 100 100 100 100 100 100 100 100 100 100
  //   100 100 100 100 100 100 100 100 100 100 100 100 100 100 100 100 100 100 100 100 100 100 100 100 100
  //   100 100 100 100 100 100 100 100 100 100 100 100 100 100 100 100 100 100 100 100 100 100 100 100 100
  //   100 100 100 100 100 100 100 100 100 100 100 100 100 20100 100 100 100 100 100 100 100 100 100 100
  //   100 100 100 100 100 100 100 100 100 100 100 100 100 100 100 100 100 100 100 100 100 100 100 100 100
  //   100 100 100 100 100 100 100 100 100 100 100 100 100 100 100 100 100 100 100 100 100 100 100 100 100
  //   100 100 100 100 100 100 100 100 100 100 100 100 100 100 100 100 100 100 100 100 100 100 100 100 100
  //   100 100 100 100 100 100 100 100 100 100 100 100 100 100 100 100 100 100 100 100 100 100 100 100 100
  //   100 100 100 100 100 100 100 100 100 100 100 100 100 100 100 100 100 20100 100 100 100 100 100 100
  //   100 100 100 100 100 100 100 100 100 100 100 100 100 100 100 100 100 100 100 100 100 100 100 100 100
  //   100 100 100 100 100 100 100 100 100 100 100 100 100 100 100 100 100 100 100 100 100 100 100 100 100
  //   100 100 100 100 100 100 100 100 100 100 100 100 100 100 100 100 100 100 100 100 100 100 100 100 100
  //   100 100 100 100 100 100 100 100 100 100 100 100 100 100 100 100 100 100 100 100 100 100 100 100 100
  //   100 100 100 100 100 100 100 100 100 100 100 100 100 100 100 100 100 100 100 100 100 20100 100 100
  //   100 100 100 100 100 100 100 100 100 100 100 100 100 100 100 100 100 100 100 100 100 100 100 100 100
  //   100 100 100 100 100 100 100 100 100 100 100 100 100 100 100 100 100 100 100 100 100 100 100 100 100
  //   100 100 100 100 100 100 100 100 100 100 100 100 100 100 100 100 100 100 100 100 100 100 100 100 100
  //   100 100 100 100 100 100 100 100 100 100 100 100 100 100 100 100 100 100 100 100 100 100 100 100 100
  //   100 100 100 100 100 100 100 100 100 100 100 100 100 100 100 100 100 100 100 100 100 100 100 100 100
  //   20100 100 100 100 100 100 100 100 100 100 100 100 100 100 100 100 100 100 100 100 100 100 100 100
  //   100 100 100 100 100 100 100 100 100 100 100 100 100 100 100 100 100 100 100 100 100 100 100 100 100
  //   100 100 100 100 100 100 100 100 100 100 100 100 100 100 100 100 100 100 100 100 100 100 100 100 100
  //   100 100 100 100 100 100 100 100 100 100 100 100 100 100 100 100 100 100 100 100 100 100 100 100 100
  //   100 100 100 100 100 100 100 100 100 100 100 100 100 100 100 100 100 100 100 100 100 100 100 100 100
  //   100 100 100 100 20100 100 100 100 100 100 100 100 100 100 100 100 100 100 100 100 100 100 100 100
  //   100 100 100 100 100 100 100 100 100 100 100 100 100 100 100 100 100 100 100 100 100 100 100 100 100
  //   100 100 100 100 100 100 100 100 100 100 100 100 100 100 100 100 100 100 100 100 100 100 100 100 100
  //   100 100 100 100 100 100 100 100 100 100 100 100 100 100 100 100 100 100 100 100 100 100 100 100 100
  //   100 100 100 100 100 100 100 100 100 100 100 100 100 100 100 100 100 100 100 100 100 100 100 100 100
  //   100 100 100 100 100 100 100 100 20100 100 100 100 100 100 100 100 100 100 100 100 100 100 100 100
  //   100 100 100 100 100 100 100 100 100 100 100 100 100 100 100 100 100 100 100 100 100 100 100 100 100
  //   100 100 100 100 100 100 100 100 100 100 100 100 100 100 100 100 100 100 100 100 100 100 100 100 100
  //   100 100 100 100 100 100 100 100 100 100 100 100 100 100 100 100 100 100 100 100 100 100 100 100 100
  //   100 100 100 100 100 100 100 100 100 100 100 100 100 100 100 100 100 100 100 100 100 100 100 100 100
  //   100 100 100 100 100 100 100 100 100 100 100 100 20100 100 100 100 100 100 100 100 100 100 100 100
  //   100 100 100 100 100 100 100 100 100 100 100 100 100 100 100 100 100 100 100 100 100 100 100 100 100
  //   100 100 100 100 100 100 100 100 100 100 100 100 100 100 100 100 100 100 100 100 100 100 100 100 100
  //   100 100 100 100 100 100 100 100 100 100 100 100 100 100 100 100 100 100 100 100 100 100 100 100 100
  //   100 100 100 100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
  //   reset once: rst_req in state H3 clears the reset RC; fired keeps it from coming back
endmodule
