// Logisim project ir.circ as structural Verilog: 1 circuit, main circuit ir
module ir (
  input  clk,
  input  ir_b0_ld_n,
  input  ir_b1_ld_n,
  input  ir_v1_ld_n,
  input  ir_v2_ld_n,
  input  [7:0] ir_bus_in,
  output [5:0] ir_op,
  output [3:0] ir_mode,
  output [2:0] ir_r1,
  output [2:0] ir_r2,
  output [2:0] ir_r3,
  output ir_r1_2_n,
  output ir_r2_2_n,
  output ir_r3_2_n,
  output [7:0] ir_v1,
  output [7:0] ir_v2
);

  wire ir_bus_2_n, ir_bus_5_n, U3_pin7, U3_pin8, U3_pin13, U3_pin14, U3_pin17, U3_pin18, U6_pin4, U6_pin7,
       U6_pin8, U6_pin13, U6_pin14, U6_pin17, U6_pin18, U7_pin5, U7_pin9, U7_pin11, U7_pin13;

  _74377 U1 (
    .pin1(ir_b0_ld_n), .pin2(ir_mode[2]), .pin3(ir_bus_in[0]), .pin4(ir_bus_in[1]), .pin5(ir_mode[3]),
    .pin6(ir_op[0]), .pin7(ir_bus_in[2]), .pin8(ir_bus_in[3]), .pin9(ir_op[1]), .pin19(ir_op[5]),
    .pin18(ir_bus_in[7]), .pin17(ir_bus_in[6]), .pin16(ir_op[4]), .pin15(ir_op[3]), .pin14(ir_bus_in[5]),
    .pin13(ir_bus_in[4]), .pin12(ir_op[2]), .pin11(clk));
  _74377 U4 (
    .pin1(ir_b1_ld_n), .pin2(ir_r2[0]), .pin3(ir_bus_in[0]), .pin4(ir_bus_in[1]), .pin5(ir_r2[1]),
    .pin6(ir_r2[2]), .pin7(ir_bus_in[2]), .pin8(ir_bus_in[3]), .pin9(ir_r1[0]), .pin19(ir_mode[1]),
    .pin18(ir_bus_in[7]), .pin17(ir_bus_in[6]), .pin16(ir_mode[0]), .pin15(ir_r1[2]), .pin14(ir_bus_in[5]),
    .pin13(ir_bus_in[4]), .pin12(ir_r1[1]), .pin11(clk));
  _7414 U7 (
    .pin1(ir_bus_in[5]), .pin2(ir_bus_5_n), .pin3(ir_bus_in[2]), .pin4(ir_bus_2_n), .pin5(U7_pin5),
    .pin13(U7_pin13), .pin11(U7_pin11), .pin9(U7_pin9));  // open: pin6, pin12, pin10, pin8
  _74377 U2 (
    .pin1(ir_v1_ld_n), .pin2(ir_r3[0]), .pin3(ir_bus_in[0]), .pin4(ir_bus_in[1]), .pin5(ir_r3[1]),
    .pin6(ir_r3[2]), .pin7(ir_bus_in[2]), .pin8(ir_bus_in[3]), .pin9(ir_v1[3]), .pin19(ir_v1[7]),
    .pin18(ir_bus_in[7]), .pin17(ir_bus_in[6]), .pin16(ir_v1[6]), .pin15(ir_v1[5]), .pin14(ir_bus_in[5]),
    .pin13(ir_bus_in[4]), .pin12(ir_v1[4]), .pin11(clk));
  _74377 U5 (
    .pin1(ir_v2_ld_n), .pin2(ir_v2[0]), .pin3(ir_bus_in[0]), .pin4(ir_bus_in[1]), .pin5(ir_v2[1]),
    .pin6(ir_v2[2]), .pin7(ir_bus_in[2]), .pin8(ir_bus_in[3]), .pin9(ir_v2[3]), .pin19(ir_v2[7]),
    .pin18(ir_bus_in[7]), .pin17(ir_bus_in[6]), .pin16(ir_v2[6]), .pin15(ir_v2[5]), .pin14(ir_bus_in[5]),
    .pin13(ir_bus_in[4]), .pin12(ir_v2[4]), .pin11(clk));
  _74377 U3 (
    .pin1(ir_b1_ld_n), .pin2(ir_r1_2_n), .pin3(ir_bus_5_n), .pin4(ir_bus_2_n), .pin5(ir_r2_2_n),
    .pin7(U3_pin7), .pin8(U3_pin8), .pin18(U3_pin18), .pin17(U3_pin17), .pin14(U3_pin14), .pin13(U3_pin13),
    .pin11(clk));  // open: pin6, pin9, pin19, pin16, pin15, pin12
  _74377 U6 (
    .pin1(ir_v1_ld_n), .pin2(ir_r3_2_n), .pin3(ir_bus_2_n), .pin4(U6_pin4), .pin7(U6_pin7), .pin8(U6_pin8),
    .pin18(U6_pin18), .pin17(U6_pin17), .pin14(U6_pin14), .pin13(U6_pin13), .pin11(clk));  // open: pin5, pin6, pin9, pin19, pin16, pin15, pin12

  assign ir_v1[2:0] = ir_r3;
  // also tied to GND on the sheet: {U7_pin5, U7_pin13, U7_pin11, U7_pin9, U3_pin7, U3_pin8, U6_pin4, U6_pin7, U6_pin8, U3_pin18, U3_pin17, U3_pin14, U3_pin13, U6_pin18, U6_pin17, U6_pin14, U6_pin13}

  // Other names for the same wires on the sheet: ir_bus_in_0 = ir_bus_in[0]; ir_bus_in_1 = ir_bus_in[1];
  //   ir_bus_in_2 = ir_bus_in[2]; ir_bus_in_3 = ir_bus_in[3]; ir_bus_in_4 = ir_bus_in[4]; ir_bus_in_5 = ir_bus_in[5];
  //   ir_bus_in_6 = ir_bus_in[6]; ir_bus_in_7 = ir_bus_in[7]; ir_mode_0 = ir_mode[0]; ir_mode_1 = ir_mode[1];
  //   ir_mode_2 = ir_mode[2]; ir_mode_3 = ir_mode[3]; ir_op_0 = ir_op[0]; ir_op_1 = ir_op[1]; ir_op_2 = ir_op[2];
  //   ir_op_3 = ir_op[3]; ir_op_4 = ir_op[4]; ir_op_5 = ir_op[5]; ir_r1_0 = ir_r1[0]; ir_r1_1 = ir_r1[1];
  //   ir_r1_2 = ir_r1[2]; ir_r2_0 = ir_r2[0]; ir_r2_1 = ir_r2[1]; ir_r2_2 = ir_r2[2]; ir_v1_0 = ir_r3[0];
  //   ir_v1_1 = ir_r3[1]; ir_v1_2 = ir_r3[2]; ir_v1_3 = ir_v1[3]; ir_v1_4 = ir_v1[4]; ir_v1_5 = ir_v1[5];
  //   ir_v1_6 = ir_v1[6]; ir_v1_7 = ir_v1[7]; ir_v2_0 = ir_v2[0]; ir_v2_1 = ir_v2[1]; ir_v2_2 = ir_v2[2];
  //   ir_v2_3 = ir_v2[3]; ir_v2_4 = ir_v2[4]; ir_v2_5 = ir_v2[5]; ir_v2_6 = ir_v2[6]; ir_v2_7 = ir_v2[7]

  // Notes on the sheet:
  //   byte 0: opcode, mode 3..2
  //   byte 1: mode 1..0, R1, R2
  //   NOT bus bits 5, 2 (for X1, X2)
  //   V1 (R3 = bits 2..0)
  //   V2
  //   X1: not R1 bit 2, not R2 bit 2 (with byte 1)
  //   X2: not R3 bit 2 (with V1)
endmodule
