// Logisim project mem.circ as structural Verilog: 1 circuit, main circuit mem
module mem (
  input  clk_mem_wr_n,
  input  mem_re,
  input  mem_oe_n,
  input  mem_we_n,
  input  mem_wbuf_oe_n,
  input  mem_rom_oe_n,
  input  [15:0] mem_addr,
  input  [7:0] mem_bus_in,
  output [7:0] mem_bus_out,
  output [7:0] mem_d
);

  wire mem_a15_n, mem_ram_we_n, mem_rom_d_0, mem_rom_d_1, mem_rom_d_2, mem_rom_d_3, mem_rom_d_4, mem_rom_d_5,
       mem_rom_d_6, mem_rom_d_7, U4_pin19, U5_pin19, U6_pin19, U7_pin4, U7_pin5, U7_pin9, U7_pin10, U7_pin12,
       U7_pin13, U8_pin3, U8_pin5, U8_pin9, U8_pin11, U8_pin13;

  ttlas6c1008 U1 (
    .A16(1'b0), .A14(mem_addr[14]), .A12(mem_addr[12]), .A7(mem_addr[7]), .A6(mem_addr[6]), .A5(mem_addr[5]),
    .A4(mem_addr[4]), .A3(mem_addr[3]), .A2(mem_addr[2]), .A1(mem_addr[1]), .A0(mem_addr[0]), .DQ0(mem_d[0]),
    .DQ1(mem_d[1]), .DQ2(mem_d[2]), .DQ3(mem_d[3]), .DQ4(mem_d[4]), .DQ5(mem_d[5]), .DQ6(mem_d[6]),
    .DQ7(mem_d[7]), .nCE(1'b0), .A10(mem_addr[10]), .nOE(mem_oe_n), .A11(mem_addr[11]), .A9(mem_addr[9]),
    .A8(mem_addr[8]), .A13(mem_addr[13]), .nWE(mem_ram_we_n), .CE2(mem_re), .A15(mem_addr[15]),
    .DQ0_in(mem_d[0]), .DQ1_in(mem_d[1]), .DQ2_in(mem_d[2]), .DQ3_in(mem_d[3]), .DQ4_in(mem_d[4]),
    .DQ5_in(mem_d[5]), .DQ6_in(mem_d[6]), .DQ7_in(mem_d[7]));  // open: NC, GND, VCC
  ttlat28c256 U2 (
    .A14(mem_addr[14]), .A12(mem_addr[12]), .A7(mem_addr[7]), .A6(mem_addr[6]), .A5(mem_addr[5]),
    .A4(mem_addr[4]), .A3(mem_addr[3]), .A2(mem_addr[2]), .A1(mem_addr[1]), .A0(mem_addr[0]),
    .I_O0(mem_rom_d_0), .I_O1(mem_rom_d_1), .I_O2(mem_rom_d_2), .I_O3(mem_rom_d_3), .I_O4(mem_rom_d_4),
    .I_O5(mem_rom_d_5), .I_O6(mem_rom_d_6), .I_O7(mem_rom_d_7), .nCE(mem_addr[15]), .A10(mem_addr[10]),
    .nOE(mem_rom_oe_n), .A11(mem_addr[11]), .A9(mem_addr[9]), .A8(mem_addr[8]), .A13(mem_addr[13]),
    .nWE(1'b1), .IMAGE(4'b0000));  // open: GND, VCC
  _74541 U4 (
    .pin1(mem_rom_oe_n), .pin2(mem_rom_d_0), .pin3(mem_rom_d_1), .pin4(mem_rom_d_2), .pin5(mem_rom_d_3),
    .pin6(mem_rom_d_4), .pin7(mem_rom_d_5), .pin8(mem_rom_d_6), .pin9(mem_rom_d_7), .pin19(U4_pin19),
    .pin18(mem_d[0]), .pin17(mem_d[1]), .pin16(mem_d[2]), .pin15(mem_d[3]), .pin14(mem_d[4]),
    .pin13(mem_d[5]), .pin12(mem_d[6]), .pin11(mem_d[7]));
  _74541 U5 (
    .pin1(mem_wbuf_oe_n), .pin2(mem_bus_in[0]), .pin3(mem_bus_in[1]), .pin4(mem_bus_in[2]),
    .pin5(mem_bus_in[3]), .pin6(mem_bus_in[4]), .pin7(mem_bus_in[5]), .pin8(mem_bus_in[6]),
    .pin9(mem_bus_in[7]), .pin19(U5_pin19), .pin18(mem_d[0]), .pin17(mem_d[1]), .pin16(mem_d[2]),
    .pin15(mem_d[3]), .pin14(mem_d[4]), .pin13(mem_d[5]), .pin12(mem_d[6]), .pin11(mem_d[7]));
  ttlat28c256 U3 (
    .A14(mem_addr[14]), .A12(mem_addr[12]), .A7(mem_addr[7]), .A6(mem_addr[6]), .A5(mem_addr[5]),
    .A4(mem_addr[4]), .A3(mem_addr[3]), .A2(mem_addr[2]), .A1(mem_addr[1]), .A0(mem_addr[0]),
    .I_O0(mem_rom_d_0), .I_O1(mem_rom_d_1), .I_O2(mem_rom_d_2), .I_O3(mem_rom_d_3), .I_O4(mem_rom_d_4),
    .I_O5(mem_rom_d_5), .I_O6(mem_rom_d_6), .I_O7(mem_rom_d_7), .nCE(mem_a15_n), .A10(mem_addr[10]),
    .nOE(mem_rom_oe_n), .A11(mem_addr[11]), .A9(mem_addr[9]), .A8(mem_addr[8]), .A13(mem_addr[13]),
    .nWE(1'b1), .IMAGE(4'b0001));  // open: GND, VCC
  _74541 U6 (
    .pin1(mem_oe_n), .pin2(mem_d[0]), .pin3(mem_d[1]), .pin4(mem_d[2]), .pin5(mem_d[3]), .pin6(mem_d[4]),
    .pin7(mem_d[5]), .pin8(mem_d[6]), .pin9(mem_d[7]), .pin19(U6_pin19), .pin18(mem_bus_out[0]),
    .pin17(mem_bus_out[1]), .pin16(mem_bus_out[2]), .pin15(mem_bus_out[3]), .pin14(mem_bus_out[4]),
    .pin13(mem_bus_out[5]), .pin12(mem_bus_out[6]), .pin11(mem_bus_out[7]));
  _7432 U7 (
    .pin1(clk_mem_wr_n), .pin2(mem_we_n), .pin3(mem_ram_we_n), .pin4(U7_pin4), .pin5(U7_pin5),
    .pin13(U7_pin13), .pin12(U7_pin12), .pin10(U7_pin10), .pin9(U7_pin9));  // open: pin6, pin11, pin8
  _7414 U8 (
    .pin1(mem_addr[15]), .pin2(mem_a15_n), .pin3(U8_pin3), .pin5(U8_pin5), .pin13(U8_pin13),
    .pin11(U8_pin11), .pin9(U8_pin9));  // open: pin4, pin6, pin12, pin10, pin8
  // also tied to GND on the sheet: {U4_pin19, U5_pin19, U6_pin19, U7_pin4, U7_pin5, U7_pin13, U7_pin12, U7_pin10, U7_pin9, U8_pin3, U8_pin5, U8_pin13, U8_pin11, U8_pin9}

  // Other names for the same wires on the sheet: mem_addr_0 = mem_addr[0]; mem_addr_1 = mem_addr[1];
  //   mem_addr_2 = mem_addr[2]; mem_addr_3 = mem_addr[3]; mem_addr_4 = mem_addr[4]; mem_addr_5 = mem_addr[5];
  //   mem_addr_6 = mem_addr[6]; mem_addr_7 = mem_addr[7]; mem_addr_8 = mem_addr[8]; mem_addr_9 = mem_addr[9];
  //   mem_addr_10 = mem_addr[10]; mem_addr_11 = mem_addr[11]; mem_addr_12 = mem_addr[12]; mem_addr_13 = mem_addr[13];
  //   mem_addr_14 = mem_addr[14]; mem_addr_15 = mem_addr[15]; mem_bus_in_0 = mem_bus_in[0];
  //   mem_bus_in_1 = mem_bus_in[1]; mem_bus_in_2 = mem_bus_in[2]; mem_bus_in_3 = mem_bus_in[3];
  //   mem_bus_in_4 = mem_bus_in[4]; mem_bus_in_5 = mem_bus_in[5]; mem_bus_in_6 = mem_bus_in[6];
  //   mem_bus_in_7 = mem_bus_in[7]; mem_bus_out_0 = mem_bus_out[0]; mem_bus_out_1 = mem_bus_out[1];
  //   mem_bus_out_2 = mem_bus_out[2]; mem_bus_out_3 = mem_bus_out[3]; mem_bus_out_4 = mem_bus_out[4];
  //   mem_bus_out_5 = mem_bus_out[5]; mem_bus_out_6 = mem_bus_out[6]; mem_bus_out_7 = mem_bus_out[7];
  //   mem_d_0 = mem_d[0]; mem_d_1 = mem_d[1]; mem_d_2 = mem_d[2]; mem_d_3 = mem_d[3]; mem_d_4 = mem_d[4];
  //   mem_d_5 = mem_d[5]; mem_d_6 = mem_d[6]; mem_d_7 = mem_d[7]

  // Notes on the sheet:
  //   ROM → local bus (boot copy; HCT levels, M4)
  //   RAM 0000-FFFF (A16 = 0); DQ_in: the same pins, read side (M2)
  //   boot ROM 0000-7FFF (IMAGE = 0: its half of the boot image, M3)
  //   write: data bus → local bus
  //   boot ROM 8000-FFFF (IMAGE = 1: its half of the boot image, M3)
  //   read: local bus → data bus
  //   RAM WE# = clk_mem_wr_n OR mem_we_n (M1)
  //   NOT A15: the high ROM's /CE
endmodule
