// Logisim project test_mem_cpu.circ as structural Verilog: 1 circuit, main circuit test_mem_cpu
module test_mem_cpu (
  input  clk,
  input  rst_n,
  input  clk_mem_wr_n,
  input  [1:0] addr_base_sel,
  input  [1:0] addr_base_oe_n,
  input  addr_off_sel,
  input  [1:0] addr_off_oe_n,
  input  addr_inv,
  input  addr_cin,
  input  addr_lat_ld_n,
  input  addr_pc_ld_n,
  input  addr_sp_ld_n,
  input  [1:0] addr_lat_oe_n,
  input  [1:0] addr_pc_oe_n,
  input  [1:0] addr_sp_oe_n,
  input  [7:0] addr_bus_a,
  input  [7:0] addr_bus_b,
  input  ir_b0_ld_n,
  input  ir_b1_ld_n,
  input  ir_v1_ld_n,
  input  ir_v2_ld_n,
  input  mem_re,
  input  mem_oe_n,
  input  mem_we_n,
  input  mem_wbuf_oe_n,
  input  mem_rom_oe_n,
  input  [7:0] iod_port,
  input  iod_port_oe_n,
  input  [7:0] iod_data,
  input  iod_data_oe_n,
  input  [7:0] cpu_data,
  input  cpu_data_oe_n,
  output [7:0] bus_data,
  output [7:0] bus_addr_hi,
  output [7:0] bus_addr_lo,
  output [7:0] mem_d,
  output addr_cout,
  output [5:0] ir_op,
  output [3:0] ir_mode,
  output [7:0] ir_v1,
  output [7:0] ir_v2
);

  wire ir_r1_2_n, ir_r2_2_n, ir_r3_2_n, not_1_out, not_2_out, not_3_out;
  wire [2:0] ir_r1, ir_r2, ir_r3;

  assign bus_addr_lo = not_1_out ? iod_port : 8'bz;  // Controlled_Buffer controlled_buffer_1
  not not_1 (not_1_out, iod_port_oe_n);
  assign bus_data = not_2_out ? iod_data : 8'bz;  // Controlled_Buffer controlled_buffer_2
  not not_2 (not_2_out, iod_data_oe_n);
  assign bus_data = not_3_out ? cpu_data : 8'bz;  // Controlled_Buffer controlled_buffer_3
  not not_3 (not_3_out, cpu_data_oe_n);
  addr addr_1 (
    .clk(clk), .rst_n(rst_n), .addr_base_sel(addr_base_sel), .addr_base_oe_n(addr_base_oe_n),
    .addr_off_sel(addr_off_sel), .addr_off_oe_n(addr_off_oe_n), .addr_inv(addr_inv), .addr_cin(addr_cin),
    .addr_lat_ld_n(addr_lat_ld_n), .addr_pc_ld_n(addr_pc_ld_n), .addr_sp_ld_n(addr_sp_ld_n),
    .addr_lat_oe_n(addr_lat_oe_n), .addr_pc_oe_n(addr_pc_oe_n), .addr_sp_oe_n(addr_sp_oe_n),
    .addr_cout(addr_cout), .addr_bus_a(addr_bus_a), .addr_bus_b(addr_bus_b), .addr_v1(ir_v1),
    .addr_v2(ir_v2), .addr_bus_addr_lo_in(bus_addr_lo), .addr_bus_addr_hi(bus_addr_hi),
    .addr_bus_addr_lo(bus_addr_lo), .addr_bus_out(bus_data));
  ir ir_1 (
    .clk(clk), .ir_b0_ld_n(ir_b0_ld_n), .ir_b1_ld_n(ir_b1_ld_n), .ir_v1_ld_n(ir_v1_ld_n),
    .ir_v2_ld_n(ir_v2_ld_n), .ir_bus_in(bus_data), .ir_v1(ir_v1), .ir_v2(ir_v2), .ir_op(ir_op),
    .ir_mode(ir_mode), .ir_r1(ir_r1), .ir_r2(ir_r2), .ir_r3(ir_r3), .ir_r1_2_n(ir_r1_2_n),
    .ir_r2_2_n(ir_r2_2_n), .ir_r3_2_n(ir_r3_2_n));
  mem mem_1 (
    .clk_mem_wr_n(clk_mem_wr_n), .mem_re(mem_re), .mem_oe_n(mem_oe_n), .mem_we_n(mem_we_n),
    .mem_wbuf_oe_n(mem_wbuf_oe_n), .mem_rom_oe_n(mem_rom_oe_n), .mem_addr({bus_addr_hi, bus_addr_lo}),
    .mem_bus_in(bus_data), .mem_bus_out(bus_data), .mem_d(mem_d));

  // Other names for the same wires on the sheet: bus_addr[15:0] = {bus_addr_hi, bus_addr_lo}
endmodule
