// Logisim project regs.circ as structural Verilog: 1 circuit, main circuit regs
module regs (
  input  clk,
  input  clk_wr_n,
  input  regs_we_n,
  input  [1:0] regs_a_sel,
  input  [1:0] regs_cu_idx,
  input  [1:0] regs_cu_bank_n,
  input  [1:0] regs_b_sel,
  input  regs_a_lat_oe_n,
  input  regs_b_lat_oe_n,
  input  regs_const_oe_n,
  input  regs_const_0,
  input  regs_a_bus_oe_n,
  input  regs_res_oe_n,
  input  [2:0] regs_r1,
  input  [2:0] regs_r2,
  input  [2:0] regs_r3,
  input  [7:0] regs_alu_r,
  input  [7:0] regs_bus_in,
  output [7:0] regs_a,
  output [7:0] regs_b,
  output [7:0] regs_bus_out
);

  wire regs_a_idx_0, regs_a_idx_1, regs_a_re_hi_n, regs_a_re_lo_n, regs_b_idx_0, regs_b_idx_1,
       regs_b_re_hi_n, regs_b_re_lo_n, regs_r1_2_n, regs_r2_2_n, regs_r3_2_n, regs_we_hi_n, regs_we_lo_n,
       regs_wr_n, U1_pin1, U1_pin8, U1_pin11, U1_pin13, U1_pin15, U1_pin17, U1_pin19, U4_pin12, U4_pin13,
       U6_pin1, U6_pin15, U9_pin3, U9_pin4, U9_pin5, U9_pin6, U9_pin7, U9_pin8, U9_pin9, U9_pin19, U11_pin1,
       U11_pin15, U14_pin19, U15_pin1, U15_pin3, U15_pin13, U15_pin15, U19_pin1, U19_pin3, U19_pin13,
       U19_pin15;

  _74240 U1 (
    .pin1(U1_pin1), .pin2(regs_r1[2]), .pin4(regs_r2[2]), .pin6(regs_r3[2]), .pin8(U1_pin8),
    .pin19(U1_pin19), .pin18(regs_r1_2_n), .pin17(U1_pin17), .pin16(regs_r2_2_n), .pin15(U1_pin15),
    .pin14(regs_r3_2_n), .pin13(U1_pin13), .pin11(U1_pin11));  // open: pin3, pin5, pin7, pin9, pin12
  _74153 U6 (
    .pin1(U6_pin1), .pin2(regs_a_sel[1]), .pin3(regs_cu_idx[0]), .pin4(regs_r3[0]), .pin5(regs_r2[0]),
    .pin6(regs_r1[0]), .pin7(regs_a_idx_0), .pin15(U6_pin15), .pin14(regs_a_sel[0]), .pin13(regs_cu_idx[1]),
    .pin12(regs_r3[1]), .pin11(regs_r2[1]), .pin10(regs_r1[1]), .pin9(regs_a_idx_1));
  _74153 U11 (
    .pin1(U11_pin1), .pin2(regs_a_sel[1]), .pin3(regs_cu_bank_n[0]), .pin4(regs_r3[2]), .pin5(regs_r2[2]),
    .pin6(regs_r1[2]), .pin7(regs_a_re_lo_n), .pin15(U11_pin15), .pin14(regs_a_sel[0]),
    .pin13(regs_cu_bank_n[1]), .pin12(regs_r3_2_n), .pin11(regs_r2_2_n), .pin10(regs_r1_2_n),
    .pin9(regs_a_re_hi_n));
  _74153 U15 (
    .pin1(U15_pin1), .pin2(regs_b_sel[1]), .pin3(U15_pin3), .pin4(regs_r3[0]), .pin5(regs_r1[0]),
    .pin6(regs_r2[0]), .pin7(regs_b_idx_0), .pin15(U15_pin15), .pin14(regs_b_sel[0]), .pin13(U15_pin13),
    .pin12(regs_r3[1]), .pin11(regs_r1[1]), .pin10(regs_r2[1]), .pin9(regs_b_idx_1));
  _74153 U19 (
    .pin1(U19_pin1), .pin2(regs_b_sel[1]), .pin3(U19_pin3), .pin4(regs_r3[2]), .pin5(regs_r1[2]),
    .pin6(regs_r2[2]), .pin7(regs_b_re_lo_n), .pin15(U19_pin15), .pin14(regs_b_sel[0]), .pin13(U19_pin13),
    .pin12(regs_r3_2_n), .pin11(regs_r1_2_n), .pin10(regs_r2_2_n), .pin9(regs_b_re_hi_n));
  _74670 U2 (
    .pin1(regs_bus_in[1]), .pin2(regs_bus_in[2]), .pin3(regs_bus_in[3]), .pin4(regs_a_idx_1),
    .pin5(regs_a_idx_0), .pin6(regs_a[3]), .pin7(regs_a[2]), .pin15(regs_bus_in[0]), .pin14(regs_a_idx_0),
    .pin13(regs_a_idx_1), .pin12(regs_we_lo_n), .pin11(regs_a_re_lo_n), .pin10(regs_a[0]), .pin9(regs_a[1]));
  _74670 U7 (
    .pin1(regs_bus_in[5]), .pin2(regs_bus_in[6]), .pin3(regs_bus_in[7]), .pin4(regs_a_idx_1),
    .pin5(regs_a_idx_0), .pin6(regs_a[7]), .pin7(regs_a[6]), .pin15(regs_bus_in[4]), .pin14(regs_a_idx_0),
    .pin13(regs_a_idx_1), .pin12(regs_we_lo_n), .pin11(regs_a_re_lo_n), .pin10(regs_a[4]), .pin9(regs_a[5]));
  _74670 U12 (
    .pin1(regs_bus_in[1]), .pin2(regs_bus_in[2]), .pin3(regs_bus_in[3]), .pin4(regs_a_idx_1),
    .pin5(regs_a_idx_0), .pin6(regs_a[3]), .pin7(regs_a[2]), .pin15(regs_bus_in[0]), .pin14(regs_a_idx_0),
    .pin13(regs_a_idx_1), .pin12(regs_we_hi_n), .pin11(regs_a_re_hi_n), .pin10(regs_a[0]), .pin9(regs_a[1]));
  _74670 U16 (
    .pin1(regs_bus_in[5]), .pin2(regs_bus_in[6]), .pin3(regs_bus_in[7]), .pin4(regs_a_idx_1),
    .pin5(regs_a_idx_0), .pin6(regs_a[7]), .pin7(regs_a[6]), .pin15(regs_bus_in[4]), .pin14(regs_a_idx_0),
    .pin13(regs_a_idx_1), .pin12(regs_we_hi_n), .pin11(regs_a_re_hi_n), .pin10(regs_a[4]), .pin9(regs_a[5]));
  _74670 U3 (
    .pin1(regs_bus_in[1]), .pin2(regs_bus_in[2]), .pin3(regs_bus_in[3]), .pin4(regs_b_idx_1),
    .pin5(regs_b_idx_0), .pin6(regs_b[3]), .pin7(regs_b[2]), .pin15(regs_bus_in[0]), .pin14(regs_a_idx_0),
    .pin13(regs_a_idx_1), .pin12(regs_we_lo_n), .pin11(regs_b_re_lo_n), .pin10(regs_b[0]), .pin9(regs_b[1]));
  _74670 U8 (
    .pin1(regs_bus_in[5]), .pin2(regs_bus_in[6]), .pin3(regs_bus_in[7]), .pin4(regs_b_idx_1),
    .pin5(regs_b_idx_0), .pin6(regs_b[7]), .pin7(regs_b[6]), .pin15(regs_bus_in[4]), .pin14(regs_a_idx_0),
    .pin13(regs_a_idx_1), .pin12(regs_we_lo_n), .pin11(regs_b_re_lo_n), .pin10(regs_b[4]), .pin9(regs_b[5]));
  _74670 U13 (
    .pin1(regs_bus_in[1]), .pin2(regs_bus_in[2]), .pin3(regs_bus_in[3]), .pin4(regs_b_idx_1),
    .pin5(regs_b_idx_0), .pin6(regs_b[3]), .pin7(regs_b[2]), .pin15(regs_bus_in[0]), .pin14(regs_a_idx_0),
    .pin13(regs_a_idx_1), .pin12(regs_we_hi_n), .pin11(regs_b_re_hi_n), .pin10(regs_b[0]), .pin9(regs_b[1]));
  _74670 U17 (
    .pin1(regs_bus_in[5]), .pin2(regs_bus_in[6]), .pin3(regs_bus_in[7]), .pin4(regs_b_idx_1),
    .pin5(regs_b_idx_0), .pin6(regs_b[7]), .pin7(regs_b[6]), .pin15(regs_bus_in[4]), .pin14(regs_a_idx_0),
    .pin13(regs_a_idx_1), .pin12(regs_we_hi_n), .pin11(regs_b_re_hi_n), .pin10(regs_b[4]), .pin9(regs_b[5]));
  _7432 U4 (
    .pin1(clk_wr_n), .pin2(regs_we_n), .pin3(regs_wr_n), .pin4(regs_wr_n), .pin5(regs_a_re_lo_n),
    .pin6(regs_we_lo_n), .pin13(U4_pin13), .pin12(U4_pin12), .pin10(regs_a_re_hi_n), .pin9(regs_wr_n),
    .pin8(regs_we_hi_n));  // open: pin11
  _74541 U9 (
    .pin1(regs_const_oe_n), .pin2(regs_const_0), .pin3(U9_pin3), .pin4(U9_pin4), .pin5(U9_pin5),
    .pin6(U9_pin6), .pin7(U9_pin7), .pin8(U9_pin8), .pin9(U9_pin9), .pin19(U9_pin19), .pin18(regs_b[0]),
    .pin17(regs_b[1]), .pin16(regs_b[2]), .pin15(regs_b[3]), .pin14(regs_b[4]), .pin13(regs_b[5]),
    .pin12(regs_b[6]), .pin11(regs_b[7]));
  _74541 U14 (
    .pin1(regs_a_bus_oe_n), .pin2(regs_a[0]), .pin3(regs_a[1]), .pin4(regs_a[2]), .pin5(regs_a[3]),
    .pin6(regs_a[4]), .pin7(regs_a[5]), .pin8(regs_a[6]), .pin9(regs_a[7]), .pin19(U14_pin19),
    .pin18(regs_bus_out[0]), .pin17(regs_bus_out[1]), .pin16(regs_bus_out[2]), .pin15(regs_bus_out[3]),
    .pin14(regs_bus_out[4]), .pin13(regs_bus_out[5]), .pin12(regs_bus_out[6]), .pin11(regs_bus_out[7]));
  ttl74574 U5 (
    .nOE(regs_res_oe_n), .D0(regs_alu_r[0]), .D1(regs_alu_r[1]), .D2(regs_alu_r[2]), .D3(regs_alu_r[3]),
    .D4(regs_alu_r[4]), .D5(regs_alu_r[5]), .D6(regs_alu_r[6]), .D7(regs_alu_r[7]), .CP(clk),
    .Q7(regs_bus_out[7]), .Q6(regs_bus_out[6]), .Q5(regs_bus_out[5]), .Q4(regs_bus_out[4]),
    .Q3(regs_bus_out[3]), .Q2(regs_bus_out[2]), .Q1(regs_bus_out[1]), .Q0(regs_bus_out[0]));  // open: GND, VCC
  ttl74574 U10 (
    .nOE(regs_a_lat_oe_n), .D0(regs_bus_in[0]), .D1(regs_bus_in[1]), .D2(regs_bus_in[2]),
    .D3(regs_bus_in[3]), .D4(regs_bus_in[4]), .D5(regs_bus_in[5]), .D6(regs_bus_in[6]), .D7(regs_bus_in[7]),
    .CP(clk), .Q7(regs_a[7]), .Q6(regs_a[6]), .Q5(regs_a[5]), .Q4(regs_a[4]), .Q3(regs_a[3]), .Q2(regs_a[2]),
    .Q1(regs_a[1]), .Q0(regs_a[0]));  // open: GND, VCC
  ttl74574 U18 (
    .nOE(regs_b_lat_oe_n), .D0(regs_bus_in[0]), .D1(regs_bus_in[1]), .D2(regs_bus_in[2]),
    .D3(regs_bus_in[3]), .D4(regs_bus_in[4]), .D5(regs_bus_in[5]), .D6(regs_bus_in[6]), .D7(regs_bus_in[7]),
    .CP(clk), .Q7(regs_b[7]), .Q6(regs_b[6]), .Q5(regs_b[5]), .Q4(regs_b[4]), .Q3(regs_b[3]), .Q2(regs_b[2]),
    .Q1(regs_b[1]), .Q0(regs_b[0]));  // open: GND, VCC
  // also tied to GND on the sheet: {U6_pin1, U11_pin1, U15_pin1, U15_pin3, U19_pin1, U1_pin1, U1_pin8, U1_pin17, U1_pin15, U1_pin13, U1_pin11, U6_pin15, U11_pin15, U15_pin15, U15_pin13, U19_pin15, U9_pin3, U9_pin4, U9_pin5, U9_pin6, U9_pin7, U9_pin8, U9_pin9, U4_pin13, U4_pin12, U9_pin19, U14_pin19}
  // also tied to VCC on the sheet: {U19_pin3, U1_pin19, U19_pin13}

  // Other names for the same wires on the sheet: regs_a_0 = regs_a[0]; regs_a_1 = regs_a[1]; regs_a_2 = regs_a[2];
  //   regs_a_3 = regs_a[3]; regs_a_4 = regs_a[4]; regs_a_5 = regs_a[5]; regs_a_6 = regs_a[6]; regs_a_7 = regs_a[7];
  //   regs_a_sel_0 = regs_a_sel[0]; regs_a_sel_1 = regs_a_sel[1]; regs_alu_r_0 = regs_alu_r[0];
  //   regs_alu_r_1 = regs_alu_r[1]; regs_alu_r_2 = regs_alu_r[2]; regs_alu_r_3 = regs_alu_r[3];
  //   regs_alu_r_4 = regs_alu_r[4]; regs_alu_r_5 = regs_alu_r[5]; regs_alu_r_6 = regs_alu_r[6];
  //   regs_alu_r_7 = regs_alu_r[7]; regs_b_0 = regs_b[0]; regs_b_1 = regs_b[1]; regs_b_2 = regs_b[2];
  //   regs_b_3 = regs_b[3]; regs_b_4 = regs_b[4]; regs_b_5 = regs_b[5]; regs_b_6 = regs_b[6]; regs_b_7 = regs_b[7];
  //   regs_b_sel_0 = regs_b_sel[0]; regs_b_sel_1 = regs_b_sel[1]; regs_bus_in_0 = regs_bus_in[0];
  //   regs_bus_in_1 = regs_bus_in[1]; regs_bus_in_2 = regs_bus_in[2]; regs_bus_in_3 = regs_bus_in[3];
  //   regs_bus_in_4 = regs_bus_in[4]; regs_bus_in_5 = regs_bus_in[5]; regs_bus_in_6 = regs_bus_in[6];
  //   regs_bus_in_7 = regs_bus_in[7]; regs_bus_out_0 = regs_bus_out[0]; regs_bus_out_1 = regs_bus_out[1];
  //   regs_bus_out_2 = regs_bus_out[2]; regs_bus_out_3 = regs_bus_out[3]; regs_bus_out_4 = regs_bus_out[4];
  //   regs_bus_out_5 = regs_bus_out[5]; regs_bus_out_6 = regs_bus_out[6]; regs_bus_out_7 = regs_bus_out[7];
  //   regs_cu_bank_n_0 = regs_cu_bank_n[0]; regs_cu_bank_n_1 = regs_cu_bank_n[1]; regs_cu_idx_0 = regs_cu_idx[0];
  //   regs_cu_idx_1 = regs_cu_idx[1]; regs_r1_0 = regs_r1[0]; regs_r1_1 = regs_r1[1]; regs_r1_2 = regs_r1[2];
  //   regs_r2_0 = regs_r2[0]; regs_r2_1 = regs_r2[1]; regs_r2_2 = regs_r2[2]; regs_r3_0 = regs_r3[0];
  //   regs_r3_1 = regs_r3[1]; regs_r3_2 = regs_r3[2]

  // Notes on the sheet:
  //   not bit 2
  //   port A / write index
  //   port A banks
  //   port B index
  //   port B banks (11 = off)
  //   port A, words 0-3, bits 3..0
  //   port A, words 0-3, bits 7..4
  //   port A, words 4-7, bits 3..0
  //   port A, words 4-7, bits 7..4
  //   port B, words 0-3, bits 3..0
  //   port B, words 0-3, bits 7..4
  //   port B, words 4-7, bits 3..0
  //   port B, words 4-7, bits 7..4
  //   /WE per bank
  //   constant 0000000c → B
  //   bus A → data bus
  //   result latch → data bus
  //   operand latch → bus A
  //   operand latch → bus B
endmodule
