// Logisim project cpu.circ as structural Verilog: 1 circuit, main circuit main
module main (
  input  osc,
  input  rc,
  input  \int ,
  input  [7:0] iod_bus_data,
  input  [7:0] iod_bus_addr_lo,
  output [5:0] clk,
  output clk_wr_n,
  output clk_mem_wr_n,
  output rst_n,
  output rst_early,
  output rst_rc,
  output [7:0] bus_data,
  output [15:0] bus_addr,
  output [7:0] bus_a,
  output [7:0] bus_b,
  output [7:0] mem_d,
  output [7:0] alu_r,
  output [7:0] flag_reg,
  output addr_cout,
  output [3:0] alu_op,
  output [3:0] flags_op,
  output flags_bit_val,
  output flags_oe_n,
  output regs_we_n,
  output [1:0] regs_a_sel,
  output [1:0] regs_cu_idx,
  output [1:0] regs_cu_bank_n,
  output [1:0] regs_b_sel,
  output regs_a_lat_oe_n,
  output regs_b_lat_oe_n,
  output regs_const_oe_n,
  output regs_const_0,
  output regs_a_bus_oe_n,
  output regs_res_oe_n,
  output [1:0] addr_base_sel,
  output [1:0] addr_base_oe_n,
  output addr_off_sel,
  output [1:0] addr_off_oe_n,
  output addr_inv,
  output addr_cin,
  output addr_lat_ld_n,
  output addr_pc_ld_n,
  output addr_sp_ld_n,
  output [1:0] addr_lat_oe_n,
  output [1:0] addr_pc_oe_n,
  output [1:0] addr_sp_oe_n,
  output ir_b0_ld_n,
  output ir_b1_ld_n,
  output ir_v1_ld_n,
  output ir_v2_ld_n,
  output mem_re,
  output mem_oe_n,
  output mem_we_n,
  output mem_wbuf_oe_n,
  output mem_rom_oe_n,
  output ie,
  output rw,
  output inr,
  output [5:0] ir_op,
  output [3:0] ir_mode,
  output [2:0] ir_r1,
  output [2:0] ir_r2,
  output [2:0] ir_r3,
  output ir_r1_2_n,
  output ir_r2_2_n,
  output ir_r3_2_n,
  output [7:0] ir_v1,
  output [7:0] ir_v2
);

  wire alu_c, alu_e, alu_f, alu_n, alu_s, alu_z;

  clkgen clkgen_1 (
    .clkgen_osc(osc), .clkgen_rc(rc), .clk(clk), .clk_wr_n(clk_wr_n), .clk_mem_wr_n(clk_mem_wr_n),
    .rst_n(rst_n), .rst_early(rst_early), .rst_rc(rst_rc));
  alu alu_1 (
    .alu_op(alu_op), .alu_cin(flag_reg[0]), .alu_c(alu_c), .alu_z(alu_z), .alu_n(alu_n), .alu_s(alu_s),
    .alu_e(alu_e), .alu_f(alu_f), .alu_a(bus_a), .alu_b(bus_b), .alu_r(alu_r));
  flags flags_1 (
    .flags_op(flags_op), .flags_bit_val(flags_bit_val), .flags_oe_n(flags_oe_n), .clk(clk[4]), .rst_n(rst_n),
    .flags_alu_c(alu_c), .flags_alu_z(alu_z), .flags_alu_n(alu_n), .flags_alu_s(alu_s), .flags_alu_e(alu_e),
    .flags_alu_f(alu_f), .flags_bus_in(iod_bus_data), .flag_c(flag_reg[0]), .flag_e(flag_reg[1]),
    .flag_i(flag_reg[2]), .flag_n(flag_reg[3]), .flag_s(flag_reg[4]), .flag_z(flag_reg[5]),
    .flag_f(flag_reg[6]), .flag_h(flag_reg[7]), .flags_bus_out(iod_bus_data));
  ir ir_1 (
    .clk(clk[0]), .ir_b0_ld_n(ir_b0_ld_n), .ir_b1_ld_n(ir_b1_ld_n), .ir_v1_ld_n(ir_v1_ld_n),
    .ir_v2_ld_n(ir_v2_ld_n), .ir_bus_in(iod_bus_data), .ir_op(ir_op), .ir_mode(ir_mode), .ir_r1(ir_r1),
    .ir_r2(ir_r2), .ir_r3(ir_r3), .ir_r1_2_n(ir_r1_2_n), .ir_r2_2_n(ir_r2_2_n), .ir_r3_2_n(ir_r3_2_n),
    .ir_v1(ir_v1), .ir_v2(ir_v2));
  mem mem_1 (
    .clk_mem_wr_n(clk_mem_wr_n), .mem_re(mem_re), .mem_oe_n(mem_oe_n), .mem_we_n(mem_we_n),
    .mem_wbuf_oe_n(mem_wbuf_oe_n), .mem_rom_oe_n(mem_rom_oe_n), .mem_addr({bus_addr[15:8], iod_bus_addr_lo}),
    .mem_bus_in(iod_bus_data), .mem_bus_out(iod_bus_data), .mem_d(mem_d));
  cu cu_1 (
    .cu_flag_n(flag_reg[3]), .cu_flag_s(flag_reg[4]), .cu_flag_z(flag_reg[5]), .clk(clk[3:2]),
    .cu_flag_f(flag_reg[6]), .cu_flag_h(flag_reg[7]), .cu_int(\int ), .cu_addr_cout(addr_cout),
    .rst_n(rst_n), .rst_early(rst_early), .rst_rc(rst_rc), .cu_bus_in(iod_bus_data), .cu_ir_op(ir_op),
    .cu_ir_mode(ir_mode), .cu_flag_c(flag_reg[0]), .cu_flag_e(flag_reg[1]), .cu_flag_i(flag_reg[2]),
    .cu_regs_b_lat_oe_n(regs_b_lat_oe_n), .cu_regs_const_oe_n(regs_const_oe_n),
    .cu_regs_const_0(regs_const_0), .cu_alu_op(alu_op), .cu_regs_a_bus_oe_n(regs_a_bus_oe_n),
    .cu_regs_res_oe_n(regs_res_oe_n), .cu_addr_base_sel(addr_base_sel), .cu_addr_base_oe_n(addr_base_oe_n),
    .cu_addr_off_sel(addr_off_sel), .cu_addr_off_oe_n(addr_off_oe_n), .cu_addr_inv(addr_inv),
    .cu_addr_cin(addr_cin), .cu_addr_lat_ld_n(addr_lat_ld_n), .cu_addr_pc_ld_n(addr_pc_ld_n),
    .cu_addr_sp_ld_n(addr_sp_ld_n), .cu_addr_lat_oe_n(addr_lat_oe_n), .cu_addr_pc_oe_n(addr_pc_oe_n),
    .cu_addr_sp_oe_n(addr_sp_oe_n), .cu_ir_b0_ld_n(ir_b0_ld_n), .cu_ir_b1_ld_n(ir_b1_ld_n),
    .cu_ir_v1_ld_n(ir_v1_ld_n), .cu_ir_v2_ld_n(ir_v2_ld_n), .cu_mem_re(mem_re), .cu_flags_op(flags_op),
    .cu_mem_oe_n(mem_oe_n), .cu_mem_we_n(mem_we_n), .cu_mem_wbuf_oe_n(mem_wbuf_oe_n),
    .cu_mem_rom_oe_n(mem_rom_oe_n), .cu_ie(ie), .cu_rw(rw), .cu_inr(inr), .cu_bus_addr_lo(iod_bus_addr_lo),
    .cu_flags_bit_val(flags_bit_val), .cu_flags_oe_n(flags_oe_n), .cu_regs_we_n(regs_we_n),
    .cu_regs_a_sel(regs_a_sel), .cu_regs_cu_idx(regs_cu_idx), .cu_regs_cu_bank_n(regs_cu_bank_n),
    .cu_regs_b_sel(regs_b_sel), .cu_regs_a_lat_oe_n(regs_a_lat_oe_n));
  regs regs_1 (
    .clk(clk[4]), .clk_wr_n(clk_wr_n), .regs_we_n(regs_we_n), .regs_a_sel(regs_a_sel),
    .regs_cu_idx(regs_cu_idx), .regs_cu_bank_n(regs_cu_bank_n), .regs_b_sel(regs_b_sel),
    .regs_a_lat_oe_n(regs_a_lat_oe_n), .regs_b_lat_oe_n(regs_b_lat_oe_n), .regs_const_oe_n(regs_const_oe_n),
    .regs_const_0(regs_const_0), .regs_a_bus_oe_n(regs_a_bus_oe_n), .regs_res_oe_n(regs_res_oe_n),
    .regs_r1(ir_r1), .regs_r2(ir_r2), .regs_r3(ir_r3), .regs_r1_2_n(ir_r1_2_n), .regs_r2_2_n(ir_r2_2_n),
    .regs_r3_2_n(ir_r3_2_n), .regs_alu_r(alu_r), .regs_bus_in(iod_bus_data), .regs_a(bus_a), .regs_b(bus_b),
    .regs_bus_out(iod_bus_data));
  addr addr_1 (
    .addr_sp_oe_n(addr_sp_oe_n), .addr_bus_a(bus_a), .clk(clk[1]), .addr_bus_b(bus_b), .addr_v1(ir_v1),
    .addr_v2(ir_v2), .rst_n(rst_n), .addr_bus_addr_lo_in(iod_bus_addr_lo), .addr_base_sel(addr_base_sel),
    .addr_base_oe_n(addr_base_oe_n), .addr_off_sel(addr_off_sel), .addr_off_oe_n(addr_off_oe_n),
    .addr_inv(addr_inv), .addr_cin(addr_cin), .addr_lat_ld_n(addr_lat_ld_n), .addr_pc_ld_n(addr_pc_ld_n),
    .addr_sp_ld_n(addr_sp_ld_n), .addr_lat_oe_n(addr_lat_oe_n), .addr_pc_oe_n(addr_pc_oe_n),
    .addr_cout(addr_cout), .addr_bus_addr_hi(bus_addr[15:8]), .addr_bus_addr_lo(iod_bus_addr_lo),
    .addr_bus_out(iod_bus_data));

  assign bus_addr[7:0] = iod_bus_addr_lo;
  assign bus_data = iod_bus_data;

  // Other names for the same wires on the sheet: clk_2 = clk[2]; clk_3 = clk[3]; bus_addr_lo[7:0] = iod_bus_addr_lo;
  //   bus_addr_hi[7:0] = bus_addr[15:8]; clk_0 = clk[0]; clk_1 = clk[1]; clk_4 = clk[4]; clk_5 = clk[5];
  //   flag_c = flag_reg[0]; flag_e = flag_reg[1]; flag_i = flag_reg[2]; flag_n = flag_reg[3]; flag_s = flag_reg[4];
  //   flag_z = flag_reg[5]; flag_f = flag_reg[6]; flag_h = flag_reg[7]

  // Notes on the sheet:
  //   test points for the trace bench (circuits/cpu/test_cpu.circ), U14
endmodule
